// Logisim project CRC校验.circ as structural Verilog: 2 circuits, main circuit 四位模二除法器
module \四位模二除法器  (
  input  [3:0] in_1,
  input  [3:0] in_2,
  output out_3,
  output [2:0] out_4
);

  wire [3:0] xor_1_out;
  wire [3:3] multiplexer_1_out;

  assign xor_1_out = in_1 ^ in_2;  // XOR_Gate xor_1, 4 bits wide
  Multiplexer #(.width(4), .enable("false")) multiplexer_1 (
    .in0(in_1), .in1(xor_1_out), .out({multiplexer_1_out[3], out_4}), .sel(in_1[3]));

  assign out_3 = in_1[3];

  // Other names for the same wires on the sheet: C[2:0] = out_4; A[3:0] = in_1; D = in_1[3]; B[3:0] = in_2
endmodule

module CRC (
  input  [7:0] in_1,
  input  [3:0] in_2,
  output [10:0] out_3
);

  wire [2:0] \四位模二除法器_1_out_4 , \四位模二除法器_2_out_4 , \四位模二除法器_3_out_4 , \四位模二除法器_4_out_4 , \四位模二除法器_5_out_4 ,
       \四位模二除法器_6_out_4 , \四位模二除法器_7_out_4 ;

  \四位模二除法器  \u_四位模二除法器_1  (.in_1(in_1[7:4]), .in_2(in_2), .out_4(\四位模二除法器_1_out_4 ));  // open: out_3
  \四位模二除法器  \u_四位模二除法器_2  (.in_1({\四位模二除法器_1_out_4 , in_1[3]}), .in_2(in_2), .out_4(\四位模二除法器_2_out_4 ));  // open: out_3
  \四位模二除法器  \u_四位模二除法器_3  (.in_1({\四位模二除法器_2_out_4 , in_1[2]}), .in_2(in_2), .out_4(\四位模二除法器_3_out_4 ));  // open: out_3
  \四位模二除法器  \u_四位模二除法器_4  (.in_1({\四位模二除法器_3_out_4 , in_1[1]}), .in_2(in_2), .out_4(\四位模二除法器_4_out_4 ));  // open: out_3
  \四位模二除法器  \u_四位模二除法器_5  (.in_1({\四位模二除法器_4_out_4 , in_1[0]}), .in_2(in_2), .out_4(\四位模二除法器_5_out_4 ));  // open: out_3
  \四位模二除法器  \u_四位模二除法器_6  (.in_1({\四位模二除法器_5_out_4 , 1'b0}), .in_2(in_2), .out_4(\四位模二除法器_6_out_4 ));  // open: out_3
  \四位模二除法器  \u_四位模二除法器_7  (.in_1({\四位模二除法器_6_out_4 , 1'b0}), .in_2(in_2), .out_4(\四位模二除法器_7_out_4 ));  // open: out_3
  \四位模二除法器  \u_四位模二除法器_8  (.in_1({\四位模二除法器_7_out_4 , 1'b0}), .in_2(in_2), .out_4(out_3[2:0]));  // open: out_3

  assign out_3[10:3] = in_1;

  // Other names for the same wires on the sheet: A[7:0] = in_1; C[10:0] = {in_1, out_3[2:0]}; B[3:0] = in_2;
  //   remain[2:0] = out_3[2:0]
endmodule
