// Logisim project fsm.circ as structural Verilog: 3 circuits, main circuit fsm
module fsm (
  input  [1:0] in_1,
  input  in_2,
  output out_3
);

  wire CLK;
  wire [2:0] multiplexer_1_out, register_1_q, \状态转移_1_o0 ;

  Clock clock_1 (.out(CLK));
  \状态转移  \u_状态转移_1  (
    .s2(register_1_q[2]), .s1(register_1_q[1]), .s0(register_1_q[0]), .i1(in_1[1]), .i0(in_1[0]),
    .o2(\状态转移_1_o0 [2]), .o1(\状态转移_1_o0 [1]), .o0(\状态转移_1_o0 [0]));
  Multiplexer #(.width(3), .enable("false")) multiplexer_1 (
    .in0(\状态转移_1_o0 ), .in1(3'b000), .out(multiplexer_1_out), .sel(in_2));
  Register #(.width(3)) register_1 (.D(multiplexer_1_out), .Q(register_1_q), .clk(CLK));  // open: en, clr
  \输出逻辑  \u_输出逻辑_1  (
    .s2(register_1_q[2]), .s1(register_1_q[1]), .s0(register_1_q[0]), .i1(in_1[1]), .i0(in_1[0]), .out(out_3));

  // Other names for the same wires on the sheet: CLR = in_2; In[1:0] = in_1; Z = out_3
endmodule

module \状态转移  (
  input  s2,
  input  s1,
  input  s0,
  input  i1,
  input  i0,
  output o2,
  output o1,
  output o0
);

  wire and_2_out, and_3_out, and_4_out, and_5_out, and_6_out, and_7_out, and_8_out, not_1_out, not_2_out,
       not_3_out, not_4_out, not_5_out, not_6_out, not_7_out, not_8_out, not_9_out, not_10_out, not_11_out,
       not_12_out, not_13_out, not_14_out, not_15_out, not_16_out, not_17_out, not_18_out, not_19_out,
       not_20_out, not_21_out, not_22_out;

  not not_1 (not_1_out, s2);
  not not_2 (not_2_out, i0);
  not not_3 (not_3_out, s2);
  not not_4 (not_4_out, s1);
  not not_5 (not_5_out, i1);
  not not_6 (not_6_out, s2);
  not not_7 (not_7_out, s1);
  not not_8 (not_8_out, i0);
  not not_9 (not_9_out, s2);
  not not_10 (not_10_out, s0);
  not not_11 (not_11_out, i0);
  not not_12 (not_12_out, s1);
  not not_13 (not_13_out, s0);
  not not_14 (not_14_out, i1);
  not not_15 (not_15_out, s2);
  not not_16 (not_16_out, s1);
  not not_17 (not_17_out, i0);
  not not_18 (not_18_out, s2);
  not not_19 (not_19_out, s0);
  not not_20 (not_20_out, i0);
  not not_21 (not_21_out, s2);
  not not_22 (not_22_out, i1);
  and and_1 (o2, not_1_out, s1, s0, not_2_out);
  and and_2 (and_2_out, not_3_out, not_4_out, s0, not_5_out);
  and and_3 (and_3_out, not_6_out, not_7_out, s0, not_8_out);
  and and_4 (and_4_out, not_9_out, s1, not_10_out, not_11_out);
  and and_5 (and_5_out, not_12_out, not_13_out, not_14_out, i0);
  and and_6 (and_6_out, not_15_out, not_16_out, s0, not_17_out);
  and and_7 (and_7_out, not_18_out, s1, not_19_out, not_20_out);
  and and_8 (and_8_out, not_21_out, s1, not_22_out, i0);
  or or_1 (o1, and_2_out, and_3_out, and_4_out);
  or or_2 (o0, and_5_out, and_6_out, and_7_out, and_8_out);
endmodule

module \输出逻辑  (
  input  s2,
  input  s1,
  input  s0,
  input  i1,
  input  i0,
  output out
);

  wire not_1_out, not_2_out;

  not not_1 (not_1_out, s2);
  not not_2 (not_2_out, i0);
  and and_1 (out, not_1_out, s1, s0, not_2_out);
endmodule
