// Logisim project grf.circ as structural Verilog: 1 circuit, main circuit grf
module grf (
  input  in_1,
  input  in_2,
  input  in_3,
  input  [4:0] in_4,
  input  [31:0] in_5,
  input  [4:0] in_6,
  input  [4:0] in_7,
  output [31:0] out_8,
  output [31:0] out_9
);

  wire demultiplexer_1_out0, demultiplexer_1_out1, demultiplexer_1_out2, demultiplexer_1_out3,
       demultiplexer_1_out4, demultiplexer_1_out5, demultiplexer_1_out6, demultiplexer_1_out7,
       demultiplexer_2_out0, demultiplexer_2_out1, demultiplexer_2_out2, demultiplexer_2_out3,
       demultiplexer_2_out4, demultiplexer_2_out5, demultiplexer_2_out6, demultiplexer_2_out7,
       demultiplexer_4_out0, demultiplexer_4_out1, demultiplexer_4_out2, demultiplexer_4_out3,
       demultiplexer_4_out4, demultiplexer_4_out5, demultiplexer_4_out6, demultiplexer_4_out7,
       demultiplexer_5_out0, demultiplexer_5_out1, demultiplexer_5_out2, demultiplexer_5_out3,
       demultiplexer_5_out4, demultiplexer_5_out5, demultiplexer_5_out6, demultiplexer_5_out7, E1, E2, E3, E4;
  wire [31:0] R11, R12, R21, R22, R31, R32, R41, R42, register_1_q, register_2_q, register_3_q, register_4_q,
       register_5_q, register_6_q, register_7_q, register_8_q, register_9_q, register_10_q, register_11_q,
       register_12_q, register_13_q, register_14_q, register_15_q, register_16_q, register_17_q,
       register_18_q, register_19_q, register_20_q, register_21_q, register_22_q, register_23_q,
       register_24_q, register_25_q, register_26_q, register_27_q, register_28_q, register_29_q,
       register_30_q, register_31_q, register_32_q;

  Demultiplexer #(.select(3), .enable("false")) demultiplexer_1 (
    .out0(demultiplexer_1_out0), .out1(demultiplexer_1_out1), .out2(demultiplexer_1_out2),
    .out3(demultiplexer_1_out3), .out4(demultiplexer_1_out4), .out5(demultiplexer_1_out5),
    .out6(demultiplexer_1_out6), .out7(demultiplexer_1_out7), .in(E1), .sel(in_7[2:0]));
  Register #(.width(32)) register_1 (.D(in_5), .en(1'b0), .Q(register_1_q), .clk(in_1), .clr(in_2));
  Register #(.width(32)) register_2 (.D(in_5), .en(demultiplexer_1_out1), .Q(register_2_q), .clk(in_1), .clr(in_2));
  Register #(.width(32)) register_3 (.D(in_5), .en(demultiplexer_1_out2), .Q(register_3_q), .clk(in_1), .clr(in_2));
  Register #(.width(32)) register_4 (.D(in_5), .en(demultiplexer_1_out3), .Q(register_4_q), .clk(in_1), .clr(in_2));
  Register #(.width(32)) register_5 (.D(in_5), .en(demultiplexer_1_out4), .Q(register_5_q), .clk(in_1), .clr(in_2));
  Register #(.width(32)) register_6 (.D(in_5), .en(demultiplexer_1_out5), .Q(register_6_q), .clk(in_1), .clr(in_2));
  Register #(.width(32)) register_7 (.D(in_5), .en(demultiplexer_1_out6), .Q(register_7_q), .clk(in_1), .clr(in_2));
  Register #(.width(32)) register_8 (.D(in_5), .en(demultiplexer_1_out7), .Q(register_8_q), .clk(in_1), .clr(in_2));
  Multiplexer #(.select(3), .width(32), .enable("false")) multiplexer_1 (
    .in0(register_1_q), .in1(register_2_q), .in2(register_3_q), .in3(register_4_q), .in4(register_5_q),
    .in5(register_6_q), .in6(register_7_q), .in7(register_8_q), .out(R11), .sel(in_6[2:0]));
  Multiplexer #(.select(2), .width(32), .enable("false")) multiplexer_2 (
    .in0(R11), .in1(R21), .in2(R31), .in3(R41), .out(out_8), .sel(in_6[4:3]));
  Multiplexer #(.select(2), .width(32), .enable("false")) multiplexer_3 (
    .in0(R12), .in1(R22), .in2(R32), .in3(R42), .out(out_9), .sel(in_4[4:3]));
  Multiplexer #(.select(3), .width(32), .enable("false")) multiplexer_4 (
    .in0(register_1_q), .in1(register_2_q), .in2(register_3_q), .in3(register_4_q), .in4(register_5_q),
    .in5(register_6_q), .in6(register_7_q), .in7(register_8_q), .out(R12), .sel(in_4[2:0]));
  Demultiplexer #(.select(3), .enable("false")) demultiplexer_2 (
    .out0(demultiplexer_2_out0), .out1(demultiplexer_2_out1), .out2(demultiplexer_2_out2),
    .out3(demultiplexer_2_out3), .out4(demultiplexer_2_out4), .out5(demultiplexer_2_out5),
    .out6(demultiplexer_2_out6), .out7(demultiplexer_2_out7), .in(E2), .sel(in_7[2:0]));
  Demultiplexer #(.select(2), .enable("false")) demultiplexer_3 (
    .out0(E1), .out1(E2), .out2(E3), .out3(E4), .in(in_3), .sel(in_7[4:3]));
  Register #(.width(32)) register_9 (.D(in_5), .en(demultiplexer_2_out0), .Q(register_9_q), .clk(in_1), .clr(in_2));
  Register #(.width(32)) register_10 (.D(in_5), .en(demultiplexer_2_out1), .Q(register_10_q), .clk(in_1), .clr(in_2));
  Register #(.width(32)) register_11 (.D(in_5), .en(demultiplexer_2_out2), .Q(register_11_q), .clk(in_1), .clr(in_2));
  Register #(.width(32)) register_12 (.D(in_5), .en(demultiplexer_2_out3), .Q(register_12_q), .clk(in_1), .clr(in_2));
  Register #(.width(32)) register_13 (.D(in_5), .en(demultiplexer_2_out4), .Q(register_13_q), .clk(in_1), .clr(in_2));
  Register #(.width(32)) register_14 (.D(in_5), .en(demultiplexer_2_out5), .Q(register_14_q), .clk(in_1), .clr(in_2));
  Register #(.width(32)) register_15 (.D(in_5), .en(demultiplexer_2_out6), .Q(register_15_q), .clk(in_1), .clr(in_2));
  Register #(.width(32)) register_16 (.D(in_5), .en(demultiplexer_2_out7), .Q(register_16_q), .clk(in_1), .clr(in_2));
  Multiplexer #(.select(3), .width(32), .enable("false")) multiplexer_5 (
    .in0(register_9_q), .in1(register_10_q), .in2(register_11_q), .in3(register_12_q), .in4(register_13_q),
    .in5(register_14_q), .in6(register_15_q), .in7(register_16_q), .out(R21), .sel(in_6[2:0]));
  Multiplexer #(.select(3), .width(32), .enable("false")) multiplexer_6 (
    .in0(register_9_q), .in1(register_10_q), .in2(register_11_q), .in3(register_12_q), .in4(register_13_q),
    .in5(register_14_q), .in6(register_15_q), .in7(register_16_q), .out(R22), .sel(in_4[2:0]));
  Demultiplexer #(.select(3), .enable("false")) demultiplexer_4 (
    .out0(demultiplexer_4_out0), .out1(demultiplexer_4_out1), .out2(demultiplexer_4_out2),
    .out3(demultiplexer_4_out3), .out4(demultiplexer_4_out4), .out5(demultiplexer_4_out5),
    .out6(demultiplexer_4_out6), .out7(demultiplexer_4_out7), .in(E3), .sel(in_7[2:0]));
  Register #(.width(32)) register_17 (.D(in_5), .en(demultiplexer_4_out0), .Q(register_17_q), .clk(in_1), .clr(in_2));
  Register #(.width(32)) register_18 (.D(in_5), .en(demultiplexer_4_out1), .Q(register_18_q), .clk(in_1), .clr(in_2));
  Register #(.width(32)) register_19 (.D(in_5), .en(demultiplexer_4_out2), .Q(register_19_q), .clk(in_1), .clr(in_2));
  Register #(.width(32)) register_20 (.D(in_5), .en(demultiplexer_4_out3), .Q(register_20_q), .clk(in_1), .clr(in_2));
  Register #(.width(32)) register_21 (.D(in_5), .en(demultiplexer_4_out4), .Q(register_21_q), .clk(in_1), .clr(in_2));
  Register #(.width(32)) register_22 (.D(in_5), .en(demultiplexer_4_out5), .Q(register_22_q), .clk(in_1), .clr(in_2));
  Register #(.width(32)) register_23 (.D(in_5), .en(demultiplexer_4_out6), .Q(register_23_q), .clk(in_1), .clr(in_2));
  Register #(.width(32)) register_24 (.D(in_5), .en(demultiplexer_4_out7), .Q(register_24_q), .clk(in_1), .clr(in_2));
  Multiplexer #(.select(3), .width(32), .enable("false")) multiplexer_7 (
    .in0(register_17_q), .in1(register_18_q), .in2(register_19_q), .in3(register_20_q), .in4(register_21_q),
    .in5(register_22_q), .in6(register_23_q), .in7(register_24_q), .out(R31), .sel(in_6[2:0]));
  Multiplexer #(.select(3), .width(32), .enable("false")) multiplexer_8 (
    .in0(register_17_q), .in1(register_18_q), .in2(register_19_q), .in3(register_20_q), .in4(register_21_q),
    .in5(register_22_q), .in6(register_23_q), .in7(register_24_q), .out(R32), .sel(in_4[2:0]));
  Demultiplexer #(.select(3), .enable("false")) demultiplexer_5 (
    .out0(demultiplexer_5_out0), .out1(demultiplexer_5_out1), .out2(demultiplexer_5_out2),
    .out3(demultiplexer_5_out3), .out4(demultiplexer_5_out4), .out5(demultiplexer_5_out5),
    .out6(demultiplexer_5_out6), .out7(demultiplexer_5_out7), .in(E4), .sel(in_7[2:0]));
  Register #(.width(32)) register_25 (.D(in_5), .en(demultiplexer_5_out0), .Q(register_25_q), .clk(in_1), .clr(in_2));
  Register #(.width(32)) register_26 (.D(in_5), .en(demultiplexer_5_out1), .Q(register_26_q), .clk(in_1), .clr(in_2));
  Register #(.width(32)) register_27 (.D(in_5), .en(demultiplexer_5_out2), .Q(register_27_q), .clk(in_1), .clr(in_2));
  Register #(.width(32)) register_28 (.D(in_5), .en(demultiplexer_5_out3), .Q(register_28_q), .clk(in_1), .clr(in_2));
  Register #(.width(32)) register_29 (.D(in_5), .en(demultiplexer_5_out4), .Q(register_29_q), .clk(in_1), .clr(in_2));
  Register #(.width(32)) register_30 (.D(in_5), .en(demultiplexer_5_out5), .Q(register_30_q), .clk(in_1), .clr(in_2));
  Register #(.width(32)) register_31 (.D(in_5), .en(demultiplexer_5_out6), .Q(register_31_q), .clk(in_1), .clr(in_2));
  Register #(.width(32)) register_32 (.D(in_5), .en(demultiplexer_5_out7), .Q(register_32_q), .clk(in_1), .clr(in_2));
  Multiplexer #(.select(3), .width(32), .enable("false")) multiplexer_9 (
    .in0(register_25_q), .in1(register_26_q), .in2(register_27_q), .in3(register_28_q), .in4(register_29_q),
    .in5(register_30_q), .in6(register_31_q), .in7(register_32_q), .out(R42), .sel(in_4[2:0]));
  Multiplexer #(.select(3), .width(32), .enable("false")) multiplexer_10 (
    .in0(register_25_q), .in1(register_26_q), .in2(register_27_q), .in3(register_28_q), .in4(register_29_q),
    .in5(register_30_q), .in6(register_31_q), .in7(register_32_q), .out(R41), .sel(in_6[2:0]));

  // Other names for the same wires on the sheet: A1[4:0] = in_6; A2[4:0] = in_4; A3[4:0] = in_7; clk = in_1;
  //   RD1[31:0] = out_8; RD2[31:0] = out_9; reset = in_2; WD[31:0] = in_5; WE = in_3
endmodule
