// Logisim project cpu.circ as structural Verilog: 12 circuits, main circuit main
module main (
  input  Reset,
  output [31:0] out_2,
  output out_3,
  output [4:0] out_4,
  output [31:0] out_5,
  output out_6,
  output [4:0] out_7,
  output [31:0] out_8
);

  wire ALUSrcBSel, clk, EXTOp, Zero;
  wire [1:0] A3Sel, WDSel;
  wire [2:0] DataType, NPCSel;
  wire [3:0] ALUControl;
  wire [4:0] Shamt, SPLT_rd_15_11, SPLT_rs_25_21, SPLT_rt_20_16;
  wire [5:0] Func, Opcode;
  wire [15:0] SPLT_addr_imm_15_0;
  wire [25:0] Imm26;
  wire [31:0] adder_1_out, ALUout, EXT_ext32, MR_out, multiplexer_2_out, NPC, OldData, PC4, PC_do, RD1, RD2,
       subtractor_1_out;

  Clock clock_1 (.out(clk));
  Subtractor #(.width(32)) subtractor_1 (.a(NPC), .b(32'h3000), .out(subtractor_1_out));  // open: bin, bout
  PC PC (.clk(clk), .reset(Reset), .DI(subtractor_1_out), .DO(PC_do));
  // Probe on adder_1_out
  Adder #(.width(32)) adder_1 (.a(PC_do), .b(32'h3000), .out(adder_1_out));  // open: cin, cout
  NPC u_NPC (.PC(adder_1_out), .Imm26(Imm26), .NPC(NPC), .NPCSel(NPCSel), .PC4(PC4), .RA(RD1));
  IM IM (.Address(adder_1_out), .Data(out_2));
  SPLT SPLT (
    .Instruction(out_2), .Op_31_26(Opcode), .Addr_Imm_15_0(SPLT_addr_imm_15_0), .Rs_25_21(SPLT_rs_25_21),
    .Rt_20_16(SPLT_rt_20_16), .Imm_25_0(Imm26), .Rd_15_11(SPLT_rd_15_11), .Shamt_6_10(Shamt), .Func_5_0(Func));
  Multiplexer #(.select(2), .width(5), .enable("false")) multiplexer_1 (
    .in0(SPLT_rd_15_11), .in1(SPLT_rt_20_16), .in2({5{1'b1}}), .out(out_4), .sel(A3Sel));  // open: in3
  EXT EXT (.Imm16(SPLT_addr_imm_15_0), .Signed(EXTOp), .Ext32(EXT_ext32));
  GRF GRF (
    .A1(SPLT_rs_25_21), .A2(SPLT_rt_20_16), .A3(out_4), .WD(out_5), .RD1(RD1), .RD2(RD2), .we(out_3),
    .rst(Reset));
  CU CU (
    .Zero(Zero), .Opcode(Opcode), .Func(Func), .NPCSel(NPCSel), .EXTOp(EXTOp), .ALUControl(ALUControl),
    .DMWr(out_6), .ALUSrcSel(ALUSrcBSel), .RFWr(out_3), .WDSel(WDSel), .A3Sel(A3Sel), .Data_Type(DataType));
  Multiplexer #(.width(32), .enable("false")) multiplexer_2 (
    .in0(RD2), .in1(EXT_ext32), .out(multiplexer_2_out), .sel(ALUSrcBSel));
  ALU ALU (
    .SrcA(RD1), .SrcB(multiplexer_2_out), .ALUControl(ALUControl),
    .ALUResult({ALUout[31:7], out_7, ALUout[1:0]}), .Zero(Zero), .Shamt(Shamt));
  MW MW (.Data(RD2), .Addr({ALUout[31:7], out_7, ALUout[1:0]}), .Old_Data(OldData), .Data_Type(DataType), .Out(out_8));
  DM DM (.WD(out_8), .Address({ALUout[31:7], out_7, ALUout[1:0]}), .RD(OldData), .Wr(out_6), .clk(clk), .reset(Reset));
  MR MR (.Data(OldData), .Addr({ALUout[31:7], out_7, ALUout[1:0]}), .Data_Type(DataType), .Out(MR_out));
  Multiplexer #(.select(2), .width(32), .enable("false")) multiplexer_3 (
    .in0({ALUout[31:7], out_7, ALUout[1:0]}), .in1(MR_out), .in2(PC4), .out(out_5), .sel(WDSel));  // open: in3

  // Other names for the same wires on the sheet: _Instr[31:0] = out_2; _MemData[31:0] = out_8; _RegWrite[4:0] = out_4;
  //   ALUout[6:2] = out_7; DMWr = out_6; DMreset = Reset; GRFreset = Reset; PCreset = Reset; RFData[31:0] = out_5;
  //   RFWr = out_3
endmodule

module GRF (
  input  we,
  input  [4:0] A1,
  input  [4:0] A2,
  input  [4:0] A3,
  input  [31:0] WD,
  input  rst,
  output [31:0] RD1,
  output [31:0] RD2
);

  wire clk;
  wire [31:0] i0, i1, i2, i3, i4, i5, i6, i7, i8, i9, i10, i11, i12, i13, i14, i15, i16, i17, i18, i19, i20,
       i21, i22, i23, i24, i25, i26, i27, i28, i29, i30, i31, o0, o1, o2, o3, o4, o5, o6, o7, o8, o9, o10,
       o11, o12, o13, o14, o15, o16, o17, o18, o19, o20, o21, o22, o23, o24, o25, o26, o27, o28, o29, o30,
       o31;

  Clock clock_1 (.out(clk));
  Register #(.width(32)) r0 (.D({32{1'b0}}), .en(we), .Q(o0), .clk(clk), .clr(rst));
  Register #(.width(32)) r1 (.D(i1), .en(we), .Q(o1), .clk(clk), .clr(rst));
  Register #(.width(32)) r2 (.D(i2), .en(we), .Q(o2), .clk(clk), .clr(rst));
  Register #(.width(32)) r3 (.D(i3), .en(we), .Q(o3), .clk(clk), .clr(rst));
  Register #(.width(32)) r4 (.D(i4), .en(we), .Q(o4), .clk(clk), .clr(rst));
  Register #(.width(32)) r5 (.D(i5), .en(we), .Q(o5), .clk(clk), .clr(rst));
  Register #(.width(32)) r6 (.D(i6), .en(we), .Q(o6), .clk(clk), .clr(rst));
  Register #(.width(32)) r7 (.D(i7), .en(we), .Q(o7), .clk(clk), .clr(rst));
  Register #(.width(32)) r8 (.D(i8), .en(we), .Q(o8), .clk(clk), .clr(rst));
  Register #(.width(32)) r9 (.D(i9), .en(we), .Q(o9), .clk(clk), .clr(rst));
  Register #(.width(32)) r10 (.D(i10), .en(we), .Q(o10), .clk(clk), .clr(rst));
  Register #(.width(32)) r11 (.D(i11), .en(we), .Q(o11), .clk(clk), .clr(rst));
  Register #(.width(32)) r12 (.D(i12), .en(we), .Q(o12), .clk(clk), .clr(rst));
  Register #(.width(32)) r13 (.D(i13), .en(we), .Q(o13), .clk(clk), .clr(rst));
  Register #(.width(32)) r14 (.D(i14), .en(we), .Q(o14), .clk(clk), .clr(rst));
  Register #(.width(32)) r15 (.D(i15), .en(we), .Q(o15), .clk(clk), .clr(rst));
  Register #(.width(32)) r16 (.D(i16), .en(we), .Q(o16), .clk(clk), .clr(rst));
  Register #(.width(32)) r17 (.D(i17), .en(we), .Q(o17), .clk(clk), .clr(rst));
  Register #(.width(32)) r18 (.D(i18), .en(we), .Q(o18), .clk(clk), .clr(rst));
  Register #(.width(32)) r19 (.D(i19), .en(we), .Q(o19), .clk(clk), .clr(rst));
  Register #(.width(32)) r20 (.D(i20), .en(we), .Q(o20), .clk(clk), .clr(rst));
  Register #(.width(32)) r21 (.D(i21), .en(we), .Q(o21), .clk(clk), .clr(rst));
  Register #(.width(32)) r22 (.D(i22), .en(we), .Q(o22), .clk(clk), .clr(rst));
  Register #(.width(32)) r23 (.D(i23), .en(we), .Q(o23), .clk(clk), .clr(rst));
  Register #(.width(32)) r24 (.D(i24), .en(we), .Q(o24), .clk(clk), .clr(rst));
  Register #(.width(32)) r25 (.D(i25), .en(we), .Q(o25), .clk(clk), .clr(rst));
  Register #(.width(32)) r26 (.D(i26), .en(we), .Q(o26), .clk(clk), .clr(rst));
  Register #(.width(32)) r27 (.D(i27), .en(we), .Q(o27), .clk(clk), .clr(rst));
  Register #(.width(32)) r28 (.D(i28), .en(we), .Q(o28), .clk(clk), .clr(rst));
  Register #(.width(32)) r29 (.D(i29), .en(we), .Q(o29), .clk(clk), .clr(rst));
  Register #(.width(32)) r30 (.D(i30), .en(we), .Q(o30), .clk(clk), .clr(rst));
  Register #(.width(32)) r31 (.D(i31), .en(we), .Q(o31), .clk(clk), .clr(rst));
  Multiplexer #(.select(5), .width(32), .enable("false")) multiplexer_1 (
    .in0(o0), .in1(o1), .in2(o2), .in3(o3), .in4(o4), .in5(o5), .in6(o6), .in7(o7), .in8(o8), .in9(o9),
    .in10(o10), .in11(o11), .in12(o12), .in13(o13), .in14(o14), .in15(o15), .in16(o16), .in17(o17),
    .in18(o18), .in19(o19), .in20(o20), .in21(o21), .in22(o22), .in23(o23), .in24(o24), .in25(o25),
    .in26(o26), .in27(o27), .in28(o28), .in29(o29), .in30(o30), .in31(o31), .out(RD1), .sel(A1));
  Multiplexer #(.select(5), .width(32), .enable("false")) multiplexer_2 (
    .in0(o0), .in1(o1), .in2(o2), .in3(o3), .in4(o4), .in5(o5), .in6(o6), .in7(o7), .in8(o8), .in9(o9),
    .in10(o10), .in11(o11), .in12(o12), .in13(o13), .in14(o14), .in15(o15), .in16(o16), .in17(o17),
    .in18(o18), .in19(o19), .in20(o20), .in21(o21), .in22(o22), .in23(o23), .in24(o24), .in25(o25),
    .in26(o26), .in27(o27), .in28(o28), .in29(o29), .in30(o30), .in31(o31), .out(RD2), .sel(A2));
  Demultiplexer #(.select(5), .width(32), .tristate("true"), .enable("false")) demultiplexer_1 (
    .out0(i0), .out1(i1), .out2(i2), .out3(i3), .out4(i4), .out5(i5), .out6(i6), .out7(i7), .out8(i8),
    .out9(i9), .out10(i10), .out11(i11), .out12(i12), .out13(i13), .out14(i14), .out15(i15), .out16(i16),
    .out17(i17), .out18(i18), .out19(i19), .out20(i20), .out21(i21), .out22(i22), .out23(i23), .out24(i24),
    .out25(i25), .out26(i26), .out27(i27), .out28(i28), .out29(i29), .out30(i30), .out31(i31), .in(WD),
    .sel(A3));
endmodule

module PC (
  input  clk,
  input  reset,
  input  [31:0] DI,
  output [31:0] DO
);

  Register #(.width(32)) register_1 (.D(DI), .Q(DO), .clk(clk), .clr(reset));  // open: en
endmodule

module NPC (
  input  [31:0] PC,
  input  [25:0] Imm26,
  input  [2:0] NPCSel,
  input  [31:0] RA,
  output [31:0] NPC,
  output [31:0] PC4
);

  wire [31:0] adder_2_out, bit_extender_1_out, shifter_1_out;

  assign bit_extender_1_out = {{16{Imm26[15]}}, Imm26[15:0]};  // Bit_Extender bit_extender_1
  Adder #(.width(32)) adder_1 (.a(PC), .b(32'h4), .out(PC4));  // open: cin, cout
  Shifter #(.width(32)) shifter_1 (.in(bit_extender_1_out), .\dist (5'b00010), .out(shifter_1_out));
  Adder #(.width(32)) adder_2 (.a(PC4), .b(shifter_1_out), .out(adder_2_out));  // open: cin, cout
  Multiplexer #(.select(3), .width(32), .enable("false")) multiplexer_1 (
    .in0(PC4), .in1(adder_2_out), .in2({PC[31:28], Imm26, 2'b00}), .in3(RA), .out(NPC), .sel(NPCSel));  // open: in4, in5, in6, in7
endmodule

module IM (
  input  [31:0] Address,
  output [31:0] Data
);

  ROM #(.addrWidth(5), .dataWidth(32)) rom_1 (.addr(Address[6:2]), .data(Data));  // open: sel

  // Notes on the sheet:
  //   contents of rom_1 (hex, n*v repeats v):
  //   34010001
endmodule

module DM (
  input  Wr,
  input  clk,
  input  reset,
  input  [31:0] WD,
  input  [31:0] Address,
  output [31:0] RD
);

  RAM #(.addrWidth(5), .dataWidth(32), .bus("separate")) ram_1 (
    .addr(Address[6:2]), .din(WD), .data(RD), .str(Wr), .clk(clk), .clr(reset));  // open: sel, ld
endmodule

module ALU (
  input  [31:0] SrcA,
  input  [31:0] SrcB,
  input  [3:0] ALUControl,
  input  [4:0] Shamt,
  output [31:0] ALUResult,
  output Zero
);

  wire [31:0] adder_1_out, and_1_out, or_1_out, shifter_1_out, shifter_2_out, shifter_3_out, subtractor_1_out;

  Adder #(.width(32)) adder_1 (.a(SrcA), .b(SrcB), .out(adder_1_out));  // open: cin, cout
  Subtractor #(.width(32)) subtractor_1 (.a(SrcA), .b(SrcB), .out(subtractor_1_out));  // open: bin, bout
  assign or_1_out = SrcA | SrcB;  // OR_Gate or_1, 32 bits wide
  assign and_1_out = SrcA & SrcB;  // AND_Gate and_1, 32 bits wide
  Shifter #(.width(32)) shifter_1 (.in(SrcB), .\dist (5'b10000), .out(shifter_1_out));
  Shifter #(.width(32)) shifter_2 (.in(SrcB), .\dist (Shamt), .out(shifter_2_out));
  Shifter #(.width(32)) shifter_3 (.in(SrcA), .\dist (SrcB[4:0]), .out(shifter_3_out));
  Multiplexer #(.select(4), .width(32), .enable("false")) multiplexer_1 (
    .in0(adder_1_out), .in1(subtractor_1_out), .in2(or_1_out), .in3(and_1_out), .in4(shifter_1_out),
    .in5(shifter_2_out), .in6(shifter_3_out), .out(ALUResult), .sel(ALUControl));  // open: in7, in8, in9, in10, in11, in12, in13, in14, in15
  Comparator #(.width(32)) comparator_1 (.a({32{1'b0}}), .b(ALUResult), .eq(Zero));  // open: gt, lt
endmodule

module SPLT (
  input  [31:0] Instruction,
  output [5:0] Op_31_26,
  output [15:0] Addr_Imm_15_0,
  output [4:0] Rs_25_21,
  output [4:0] Rt_20_16,
  output [25:0] Imm_25_0,
  output [4:0] Rd_15_11,
  output [4:0] Shamt_6_10,
  output [5:0] Func_5_0
);


  assign Addr_Imm_15_0 = Instruction[15:0];
  assign Func_5_0 = Instruction[5:0];
  assign Imm_25_0 = Instruction[25:0];
  assign Op_31_26 = Instruction[31:26];
  assign Rd_15_11 = Instruction[15:11];
  assign Rs_25_21 = Instruction[25:21];
  assign Rt_20_16 = Instruction[20:16];
  assign Shamt_6_10 = Instruction[10:6];
endmodule

module CU (
  input  Zero,
  input  [5:0] Opcode,
  input  [5:0] Func,
  output [2:0] NPCSel,
  output EXTOp,
  output [3:0] ALUControl,
  output DMWr,
  output ALUSrcSel,
  output RFWr,
  output [1:0] WDSel,
  output [1:0] A3Sel,
  output [2:0] Data_Type
);

  wire _Load, _Save, add, addu, \and , and_1_out, beq, comparator_2_eq, comparator_3_eq, comparator_4_eq,
       comparator_5_eq, comparator_6_eq, comparator_7_eq, comparator_8_eq, comparator_9_eq, comparator_10_eq,
       jal, jr, lb, lbu, lh, lhu, lui, lw, \or , or_1_out, or_2_out, or_3_out, or_4_out, or_5_out, or_6_out,
       or_9_out, or_10_out, or_11_out, or_12_out, or_13_out, or_14_out, or_15_out, or_16_out, or_17_out, ori,
       R, sb, sh, sll, sllv, sub, subu, sw;

  and and_1 (and_1_out, Zero, beq);
  Comparator #(.width(6)) comparator_1 (.a(Opcode), .b({6{1'b0}}), .eq(R));  // open: gt, lt
  Comparator #(.width(6)) comparator_2 (.a(Func), .b(6'b100001), .eq(comparator_2_eq));  // open: gt, lt
  Comparator #(.width(6)) comparator_3 (.a(Func), .b(6'b100011), .eq(comparator_3_eq));  // open: gt, lt
  Comparator #(.width(6)) comparator_4 (.a(Func), .b(6'b100100), .eq(comparator_4_eq));  // open: gt, lt
  Comparator #(.width(6)) comparator_5 (.a(Func), .b(6'b100101), .eq(comparator_5_eq));  // open: gt, lt
  Comparator #(.width(6)) comparator_6 (.a(Func), .b(6'b001000), .eq(comparator_6_eq));  // open: gt, lt
  Comparator #(.width(6)) comparator_7 (.a(Func), .b(6'b100000), .eq(comparator_7_eq));  // open: gt, lt
  Comparator #(.width(6)) comparator_8 (.a(Func), .b(6'b100010), .eq(comparator_8_eq));  // open: gt, lt
  buf or_1 (or_1_out, and_1_out);  // OR_Gate
  buf or_2 (or_2_out, jal);  // OR_Gate
  buf or_3 (or_3_out, jr);  // OR_Gate
  or or_4 (or_4_out, ori, _Load, lui);
  buf or_5 (or_5_out, jal);  // OR_Gate
  and and_2 (addu, R, comparator_2_eq);
  and and_3 (subu, R, comparator_3_eq);
  and and_4 (\and , R, comparator_4_eq);
  and and_5 (\or , R, comparator_5_eq);
  and and_6 (jr, R, comparator_6_eq);
  and and_7 (add, R, comparator_7_eq);
  and and_8 (sub, R, comparator_8_eq);
  or or_6 (or_6_out, _Load, _Save);
  Priority_Encoder priority_encoder_1 (
    .in1(or_1_out), .in2(or_2_out), .in3(or_3_out), .out(NPCSel));  // open: in0, in4, in5, in6, in7, en_in, gs, en_out
  Pull_Resistor pull_resistor_1 (.node(NPCSel));
  Priority_Encoder #(.select(2)) priority_encoder_2 (
    .in1(or_4_out), .in2(or_5_out), .out(A3Sel));  // open: in0, in3, gs, en_out, en_in
  Pull_Resistor pull_resistor_2 (.node(A3Sel));
  buf or_7 (EXTOp, or_6_out);  // OR_Gate
  buf or_8 (DMWr, _Save);  // OR_Gate
  nor nor_1 (RFWr, beq, _Save, jr);
  Comparator #(.width(6)) comparator_9 (.a(Func), .b({6{1'b0}}), .eq(comparator_9_eq));  // open: gt, lt
  Comparator #(.width(6)) comparator_10 (.a(Func), .b(6'b000100), .eq(comparator_10_eq));  // open: gt, lt
  and and_9 (sll, R, comparator_9_eq);
  and and_10 (sllv, R, comparator_10_eq);
  or or_9 (or_9_out, subu, beq, sub);
  or or_10 (or_10_out, ori, \or );
  buf or_11 (or_11_out, \and );  // OR_Gate
  buf or_12 (or_12_out, lui);  // OR_Gate
  buf or_13 (or_13_out, _Load);  // OR_Gate
  buf or_14 (or_14_out, jal);  // OR_Gate
  or or_15 (or_15_out, sh, lh);
  or or_16 (or_16_out, lhu, sb);
  buf or_17 (or_17_out, lb);  // OR_Gate
  Priority_Encoder #(.select(2)) priority_encoder_3 (
    .in1(or_13_out), .in2(or_14_out), .out(WDSel));  // open: in0, in3, gs, en_out, en_in
  Priority_Encoder #(.select(4)) priority_encoder_4 (
    .in1(or_9_out), .in2(or_10_out), .in3(or_11_out), .in4(or_12_out), .in5(sll), .in6(sllv), .out(ALUControl));  // open: in0, in7, in8, in9, in10, in11, in12, in13, in14, in15, gs, en_out, en_in
  Priority_Encoder priority_encoder_5 (
    .in1(or_15_out), .in2(or_16_out), .in3(or_17_out), .in4(lbu), .out(Data_Type));  // open: in0, in5, in6, in7, en_in, gs, en_out
  or or_18 (ALUSrcSel, ori, _Save, _Load, lui);
  Pull_Resistor pull_resistor_3 (.node(WDSel));
  Pull_Resistor pull_resistor_4 (.node(ALUControl));
  Pull_Resistor pull_resistor_5 (.node(Data_Type));
  Comparator #(.width(6)) comparator_11 (.a(Opcode), .b(6'b000100), .eq(beq));  // open: gt, lt
  Comparator #(.width(6)) comparator_12 (.a(Opcode), .b(6'b001101), .eq(ori));  // open: gt, lt
  Comparator #(.width(6)) comparator_13 (.a(Opcode), .b(6'b000011), .eq(jal));  // open: gt, lt
  Comparator #(.width(6)) comparator_14 (.a(Opcode), .b(6'b101011), .eq(sw));  // open: gt, lt
  Comparator #(.width(6)) comparator_15 (.a(Opcode), .b(6'b100011), .eq(lw));  // open: gt, lt
  Comparator #(.width(6)) comparator_16 (.a(Opcode), .b(6'b001111), .eq(lui));  // open: gt, lt
  Comparator #(.width(6)) comparator_17 (.a(Opcode), .b(6'b100001), .eq(lh));  // open: gt, lt
  Comparator #(.width(6)) comparator_18 (.a(Opcode), .b(6'b100101), .eq(lhu));  // open: gt, lt
  Comparator #(.width(6)) comparator_19 (.a(Opcode), .b(6'b100000), .eq(lb));  // open: gt, lt
  Comparator #(.width(6)) comparator_20 (.a(Opcode), .b(6'b100100), .eq(lbu));  // open: gt, lt
  Comparator #(.width(6)) comparator_21 (.a(Opcode), .b(6'b101001), .eq(sh));  // open: gt, lt
  Comparator #(.width(6)) comparator_22 (.a(Opcode), .b(6'b101000), .eq(sb));  // open: gt, lt
  or or_19 (_Save, sw, sh, sb);
  or or_20 (_Load, lhu, lb, lbu, lh, lw);

  // Other names for the same wires on the sheet: ALUSrcBSel = ALUSrcSel

  // Notes on the sheet:
  //   无溢出检测
  //   不用写入寄存器的指令！！！
endmodule

module EXT (
  input  [15:0] Imm16,
  input  Signed,
  output [31:0] Ext32
);

  wire [31:0] bit_extender_1_out, bit_extender_2_out;

  assign bit_extender_1_out = {{16{1'b0}}, Imm16};  // Bit_Extender bit_extender_1
  assign bit_extender_2_out = {{16{Imm16[15]}}, Imm16};  // Bit_Extender bit_extender_2
  Multiplexer #(.width(32), .enable("false")) multiplexer_1 (
    .in0(bit_extender_1_out), .in1(bit_extender_2_out), .out(Ext32), .sel(Signed));
endmodule

module MR (
  input  [31:0] Data,
  input  [31:0] Addr,
  input  [2:0] Data_Type,
  output [31:0] Out
);

  wire [7:0] multiplexer_2_out;
  wire [15:0] multiplexer_1_out;
  wire [31:0] lb, lbu, lh, lhu;

  Multiplexer #(.width(16), .enable("false")) multiplexer_1 (
    .in0(Data[15:0]), .in1(Data[31:16]), .out(multiplexer_1_out), .sel(Addr[1]));
  Multiplexer #(.select(2), .width(8), .enable("false")) multiplexer_2 (
    .in0(Data[7:0]), .in1(Data[15:8]), .in2(Data[23:16]), .in3(Data[31:24]), .out(multiplexer_2_out),
    .sel(Addr[1:0]));
  assign lh = {{16{multiplexer_1_out[15]}}, multiplexer_1_out};  // Bit_Extender bit_extender_1
  assign lhu = {{16{1'b0}}, multiplexer_1_out};  // Bit_Extender bit_extender_2
  assign lb = {{24{multiplexer_2_out[7]}}, multiplexer_2_out};  // Bit_Extender bit_extender_3
  assign lbu = {{24{1'b0}}, multiplexer_2_out};  // Bit_Extender bit_extender_4
  Multiplexer #(.select(3), .width(32), .enable("false")) multiplexer_3 (
    .in0(Data), .in1(lh), .in2(lhu), .in3(lb), .in4(lbu), .out(Out), .sel(Data_Type));  // open: in5, in6, in7
  Pull_Resistor pull_resistor_1 (.node(Out));

  // Other names for the same wires on the sheet: lw[31:0] = Data
endmodule

module MW (
  input  [31:0] Data,
  input  [31:0] Addr,
  input  [31:0] Old_Data,
  input  [2:0] Data_Type,
  output [31:0] Out
);

  wire [31:0] and_1_out, and_2_out, not_1_out, sb, sh, shifter_1_out, shifter_2_out;

  Multiplexer #(.width(32), .enable("false")) multiplexer_1 (
    .in0({Old_Data[31:16], Data[15:0]}), .in1({Data[15:0], Old_Data[15:0]}), .out(sh), .sel(Addr[1]));
  Shifter #(.width(32), .shift("rl")) shifter_1 (.in(32'hffffff00), .\dist ({Addr[1:0], 3'b000}), .out(shifter_1_out));
  Shifter #(.width(32)) shifter_2 (.in(Data), .\dist ({Addr[1:0], 3'b000}), .out(shifter_2_out));
  assign and_1_out = Old_Data & shifter_1_out;  // AND_Gate and_1, 32 bits wide
  assign not_1_out = ~shifter_1_out;  // NOT_Gate not_1, 32 bits wide
  assign and_2_out = not_1_out & shifter_2_out;  // AND_Gate and_2, 32 bits wide
  Multiplexer #(.select(3), .width(32), .enable("false")) multiplexer_2 (
    .in0(Data), .in1(sh), .in2(sb), .out(Out), .sel(Data_Type));  // open: in3, in4, in5, in6, in7
  assign sb = and_1_out | and_2_out;  // OR_Gate or_1, 32 bits wide
  Pull_Resistor pull_resistor_1 (.node(Out));

  // Other names for the same wires on the sheet: sw[31:0] = Data
endmodule
