// Logisim project cpu_错误版.circ as structural Verilog: 10 circuits, main circuit main
module main (
  input  DMreset,
  input  PCreset,
  input  ResetType
);

  wire ALUSrcBSel, clk, DMWr, EXTOp, multiplexer_1_out, multiplexer_2_out, register_1_q, RFWr, Zero;
  wire [1:0] A3Sel, WDSel;
  wire [2:0] NPCSel;
  wire [3:0] ALUControl;
  wire [4:0] multiplexer_3_out, SPLT_rd_15_11, SPLT_rs_25_21, SPLT_rt_20_16;
  wire [5:0] Func, Opcode;
  wire [15:0] SPLT_addr_imm_15_0;
  wire [25:0] Imm26;
  wire [31:0] adder_1_out, ALU_aluresult, DM_rd, EXT_ext32, GRF_rd2, IM_data, multiplexer_4_out,
       multiplexer_5_out, NPC, PC4, PC_do, RD1;

  Multiplexer #(.enable("false")) multiplexer_1 (.in0(1'b0), .in1(1'b1), .out(multiplexer_1_out), .sel(PCreset));
  Clock clock_1 (.out(clk));
  Register #(.width(1)) register_1 (.D(multiplexer_1_out), .Q(register_1_q), .clk(clk));  // open: en, clr
  Multiplexer #(.enable("false")) multiplexer_2 (
    .in0(register_1_q), .in1(PCreset), .out(multiplexer_2_out), .sel(ResetType));
  PC PC (.clk(clk), .reset(multiplexer_2_out), .DI(NPC), .DO(PC_do));
  // Probe on adder_1_out
  Adder #(.width(32)) adder_1 (.a(PC_do), .b({32{1'b0}}), .out(adder_1_out));  // open: cin, cout
  IM IM (.Address(adder_1_out), .Data(IM_data));
  NPC u_NPC (.PC(PC_do), .Imm26(Imm26), .NPC(NPC), .NPCSel(NPCSel), .PC4(PC4), .RA(RD1));
  SPLT SPLT (
    .Instruction(IM_data), .Op_31_26(Opcode), .Addr_Imm_15_0(SPLT_addr_imm_15_0), .Rs_25_21(SPLT_rs_25_21),
    .Rt_20_16(SPLT_rt_20_16), .Imm_25_0(Imm26), .Rd_15_11(SPLT_rd_15_11), .Func_5_0(Func));  // open: Shamt_6_10
  CU CU (
    .Zero(Zero), .Opcode(Opcode), .Func(Func), .NPCSel(NPCSel), .EXTOp(EXTOp), .ALUControl(ALUControl),
    .DMWr(DMWr), .ALUSrcSel(ALUSrcBSel), .RFWr(RFWr), .WDSel(WDSel), .A3Sel(A3Sel));
  Multiplexer #(.select(2), .width(5), .enable("false")) multiplexer_3 (
    .in0(SPLT_rd_15_11), .in1(SPLT_rt_20_16), .in2({5{1'b1}}), .out(multiplexer_3_out), .sel(A3Sel));  // open: in3
  GRF GRF (
    .A1(SPLT_rs_25_21), .A2(SPLT_rt_20_16), .A3(multiplexer_3_out), .WD(multiplexer_5_out), .RD1(RD1),
    .RD2(GRF_rd2), .we(RFWr));  // open: rst
  EXT EXT (.Imm16(SPLT_addr_imm_15_0), .Signed(EXTOp), .Ext32(EXT_ext32));
  ALU ALU (.SrcA(RD1), .SrcB(multiplexer_4_out), .ALUControl(ALUControl), .ALUResult(ALU_aluresult), .Zero(Zero));
  Multiplexer #(.width(32), .enable("false")) multiplexer_4 (
    .in0(GRF_rd2), .in1(EXT_ext32), .out(multiplexer_4_out), .sel(ALUSrcBSel));
  DM DM (.WD(GRF_rd2), .Address(ALU_aluresult), .RD(DM_rd), .Wr(DMWr), .clk(clk), .reset(DMreset));
  Multiplexer #(.select(2), .width(32), .enable("false")) multiplexer_5 (
    .in0(ALU_aluresult), .in1(DM_rd), .in2(PC4), .out(multiplexer_5_out), .sel(WDSel));  // open: in3
endmodule

module GRF (
  input  we,
  input  [4:0] A1,
  input  [4:0] A2,
  input  [4:0] A3,
  input  [31:0] WD,
  input  rst,
  output [31:0] RD1,
  output [31:0] RD2
);

  wire clk;
  wire [31:0] i0, i1, i2, i3, i4, i5, i6, i7, i8, i9, i10, i11, i12, i13, i14, i15, i16, i17, i18, i19, i20,
       i21, i22, i23, i24, i25, i26, i27, i28, i29, i30, i31, o0, o1, o2, o3, o4, o5, o6, o7, o8, o9, o10,
       o11, o12, o13, o14, o15, o16, o17, o18, o19, o20, o21, o22, o23, o24, o25, o26, o27, o28, o29, o30,
       o31;

  Clock clock_1 (.out(clk));
  Register #(.width(32)) r0 (.D({32{1'b0}}), .en(we), .Q(o0), .clk(clk), .clr(rst));
  Register #(.width(32)) r1 (.D(i1), .en(we), .Q(o1), .clk(clk), .clr(rst));
  Register #(.width(32)) r2 (.D(i2), .en(we), .Q(o2), .clk(clk), .clr(rst));
  Register #(.width(32)) r3 (.D(i3), .en(we), .Q(o3), .clk(clk), .clr(rst));
  Register #(.width(32)) r4 (.D(i4), .en(we), .Q(o4), .clk(clk), .clr(rst));
  Register #(.width(32)) r5 (.D(i5), .en(we), .Q(o5), .clk(clk), .clr(rst));
  Register #(.width(32)) r6 (.D(i6), .en(we), .Q(o6), .clk(clk), .clr(rst));
  Register #(.width(32)) r7 (.D(i7), .en(we), .Q(o7), .clk(clk), .clr(rst));
  Register #(.width(32)) r8 (.D(i8), .en(we), .Q(o8), .clk(clk), .clr(rst));
  Register #(.width(32)) r9 (.D(i9), .en(we), .Q(o9), .clk(clk), .clr(rst));
  Register #(.width(32)) r10 (.D(i10), .en(we), .Q(o10), .clk(clk), .clr(rst));
  Register #(.width(32)) r11 (.D(i11), .en(we), .Q(o11), .clk(clk), .clr(rst));
  Register #(.width(32)) r12 (.D(i12), .en(we), .Q(o12), .clk(clk), .clr(rst));
  Register #(.width(32)) r13 (.D(i13), .en(we), .Q(o13), .clk(clk), .clr(rst));
  Register #(.width(32)) r14 (.D(i14), .en(we), .Q(o14), .clk(clk), .clr(rst));
  Register #(.width(32)) r15 (.D(i15), .en(we), .Q(o15), .clk(clk), .clr(rst));
  Register #(.width(32)) r16 (.D(i16), .en(we), .Q(o16), .clk(clk), .clr(rst));
  Register #(.width(32)) r17 (.D(i17), .en(we), .Q(o17), .clk(clk), .clr(rst));
  Register #(.width(32)) r18 (.D(i18), .en(we), .Q(o18), .clk(clk), .clr(rst));
  Register #(.width(32)) r19 (.D(i19), .en(we), .Q(o19), .clk(clk), .clr(rst));
  Register #(.width(32)) r20 (.D(i20), .en(we), .Q(o20), .clk(clk), .clr(rst));
  Register #(.width(32)) r21 (.D(i21), .en(we), .Q(o21), .clk(clk), .clr(rst));
  Register #(.width(32)) r22 (.D(i22), .en(we), .Q(o22), .clk(clk), .clr(rst));
  Register #(.width(32)) r23 (.D(i23), .en(we), .Q(o23), .clk(clk), .clr(rst));
  Register #(.width(32)) r24 (.D(i24), .en(we), .Q(o24), .clk(clk), .clr(rst));
  Register #(.width(32)) r25 (.D(i25), .en(we), .Q(o25), .clk(clk), .clr(rst));
  Register #(.width(32)) r26 (.D(i26), .en(we), .Q(o26), .clk(clk), .clr(rst));
  Register #(.width(32)) r27 (.D(i27), .en(we), .Q(o27), .clk(clk), .clr(rst));
  Register #(.width(32)) r28 (.D(i28), .en(we), .Q(o28), .clk(clk), .clr(rst));
  Register #(.width(32)) r29 (.D(i29), .en(we), .Q(o29), .clk(clk), .clr(rst));
  Register #(.width(32)) r30 (.D(i30), .en(we), .Q(o30), .clk(clk), .clr(rst));
  Register #(.width(32)) r31 (.D(i31), .en(we), .Q(o31), .clk(clk), .clr(rst));
  Multiplexer #(.select(5), .width(32), .enable("false")) multiplexer_1 (
    .in0(o0), .in1(o1), .in2(o2), .in3(o3), .in4(o4), .in5(o5), .in6(o6), .in7(o7), .in8(o8), .in9(o9),
    .in10(o10), .in11(o11), .in12(o12), .in13(o13), .in14(o14), .in15(o15), .in16(o16), .in17(o17),
    .in18(o18), .in19(o19), .in20(o20), .in21(o21), .in22(o22), .in23(o23), .in24(o24), .in25(o25),
    .in26(o26), .in27(o27), .in28(o28), .in29(o29), .in30(o30), .in31(o31), .out(RD1), .sel(A1));
  Multiplexer #(.select(5), .width(32), .enable("false")) multiplexer_2 (
    .in0(o0), .in1(o1), .in2(o2), .in3(o3), .in4(o4), .in5(o5), .in6(o6), .in7(o7), .in8(o8), .in9(o9),
    .in10(o10), .in11(o11), .in12(o12), .in13(o13), .in14(o14), .in15(o15), .in16(o16), .in17(o17),
    .in18(o18), .in19(o19), .in20(o20), .in21(o21), .in22(o22), .in23(o23), .in24(o24), .in25(o25),
    .in26(o26), .in27(o27), .in28(o28), .in29(o29), .in30(o30), .in31(o31), .out(RD2), .sel(A2));
  Demultiplexer #(.select(5), .width(32), .tristate("true"), .enable("false")) demultiplexer_1 (
    .out0(i0), .out1(i1), .out2(i2), .out3(i3), .out4(i4), .out5(i5), .out6(i6), .out7(i7), .out8(i8),
    .out9(i9), .out10(i10), .out11(i11), .out12(i12), .out13(i13), .out14(i14), .out15(i15), .out16(i16),
    .out17(i17), .out18(i18), .out19(i19), .out20(i20), .out21(i21), .out22(i22), .out23(i23), .out24(i24),
    .out25(i25), .out26(i26), .out27(i27), .out28(i28), .out29(i29), .out30(i30), .out31(i31), .in(WD),
    .sel(A3));
endmodule

module PC (
  input  clk,
  input  reset,
  input  [31:0] DI,
  output [31:0] DO
);

  Register #(.width(32)) register_1 (.D(DI), .Q(DO), .clk(clk), .clr(reset));  // open: en
endmodule

module NPC (
  input  [31:0] PC,
  input  [25:0] Imm26,
  input  [2:0] NPCSel,
  input  [31:0] RA,
  output [31:0] NPC,
  output [31:0] PC4
);

  wire [31:0] adder_1_out, adder_2_out, bit_extender_1_out, shifter_1_out;

  assign bit_extender_1_out = {{16{1'b0}}, Imm26[15:0]};  // Bit_Extender bit_extender_1
  Adder #(.width(32)) adder_1 (.a(PC), .b(32'h4), .out(adder_1_out));  // open: cin, cout
  Shifter #(.width(32)) shifter_1 (.in(bit_extender_1_out), .\dist (5'b00010), .out(shifter_1_out));
  Adder #(.width(32)) adder_2 (.a(adder_1_out), .b(shifter_1_out), .out(adder_2_out));  // open: cin, cout
  Multiplexer #(.select(3), .width(32), .enable("false")) multiplexer_1 (
    .in0(adder_1_out), .in1(adder_2_out), .in2({PC[31:28], Imm26, 2'b00}), .in3(RA), .out(NPC), .sel(NPCSel));  // open: in4, in5, in6, in7
endmodule

module IM (
  input  [31:0] Address,
  output [31:0] Data
);

  ROM #(.addrWidth(5), .dataWidth(32)) rom_1 (.addr(Address[6:2]), .data(Data));  // open: sel

  // Notes on the sheet:
  //   contents of rom_1 (hex, n*v repeats v):
  //   34100007 34110007 c000c05 3411000f 8000c09 12110001 3412000f 34140001 3e00008 2329821
endmodule

module DM (
  input  Wr,
  input  clk,
  input  reset,
  input  [31:0] WD,
  input  [31:0] Address,
  output [31:0] RD
);

  RAM #(.addrWidth(5), .dataWidth(32), .bus("separate")) ram_1 (
    .addr(Address[6:2]), .din(WD), .data(RD), .str(Wr), .clk(clk), .clr(reset));  // open: sel, ld
endmodule

module ALU (
  input  [31:0] SrcA,
  input  [31:0] SrcB,
  input  [3:0] ALUControl,
  output [31:0] ALUResult,
  output Zero
);

  wire [31:0] adder_1_out, and_1_out, or_1_out, subtractor_1_out;

  Adder #(.width(32)) adder_1 (.a(SrcA), .b(SrcB), .out(adder_1_out));  // open: cin, cout
  Subtractor #(.width(32)) subtractor_1 (.a(SrcA), .b(SrcB), .out(subtractor_1_out));  // open: bin, bout
  assign or_1_out = SrcA | SrcB;  // OR_Gate or_1, 32 bits wide
  assign and_1_out = SrcA & SrcB;  // AND_Gate and_1, 32 bits wide
  Multiplexer #(.select(4), .width(32), .enable("false")) multiplexer_1 (
    .in0(adder_1_out), .in1(subtractor_1_out), .in2(or_1_out), .in3(and_1_out), .out(ALUResult),
    .sel(ALUControl));  // open: in4, in5, in6, in7, in8, in9, in10, in11, in12, in13, in14, in15
  Comparator #(.width(32)) comparator_1 (.a({32{1'b0}}), .b(ALUResult), .eq(Zero));  // open: gt, lt
endmodule

module SPLT (
  input  [31:0] Instruction,
  output [5:0] Op_31_26,
  output [15:0] Addr_Imm_15_0,
  output [4:0] Rs_25_21,
  output [4:0] Rt_20_16,
  output [25:0] Imm_25_0,
  output [4:0] Rd_15_11,
  output [4:0] Shamt_6_10,
  output [5:0] Func_5_0
);


  assign Addr_Imm_15_0 = Instruction[15:0];
  assign Func_5_0 = Instruction[5:0];
  assign Imm_25_0 = Instruction[25:0];
  assign Op_31_26 = Instruction[31:26];
  assign Rd_15_11 = Instruction[15:11];
  assign Rs_25_21 = Instruction[25:21];
  assign Rt_20_16 = Instruction[20:16];
  assign Shamt_6_10 = Instruction[10:6];
endmodule

module CU (
  input  Zero,
  input  [5:0] Opcode,
  input  [5:0] Func,
  output [2:0] NPCSel,
  output EXTOp,
  output [3:0] ALUControl,
  output DMWr,
  output ALUSrcSel,
  output RFWr,
  output [1:0] WDSel,
  output [1:0] A3Sel
);

  wire addu, \and , and_1_out, beq, comparator_2_eq, comparator_3_eq, comparator_4_eq, comparator_5_eq,
       comparator_6_eq, jal, jr, lw, \or , or_1_out, or_2_out, or_3_out, or_4_out, or_5_out, or_8_out,
       or_9_out, or_10_out, or_11_out, ori, R, subu, sw;

  and and_1 (and_1_out, Zero, beq);
  Comparator #(.width(6)) comparator_1 (.a(Opcode), .b({6{1'b0}}), .eq(R));  // open: gt, lt
  Comparator #(.width(6)) comparator_2 (.a(Func), .b(6'b100001), .eq(comparator_2_eq));  // open: gt, lt
  Comparator #(.width(6)) comparator_3 (.a(Func), .b(6'b100011), .eq(comparator_3_eq));  // open: gt, lt
  Comparator #(.width(6)) comparator_4 (.a(Func), .b(6'b100100), .eq(comparator_4_eq));  // open: gt, lt
  Comparator #(.width(6)) comparator_5 (.a(Func), .b(6'b100111), .eq(comparator_5_eq));  // open: gt, lt
  Comparator #(.width(6)) comparator_6 (.a(Func), .b(6'b001000), .eq(comparator_6_eq));  // open: gt, lt
  buf or_1 (or_1_out, and_1_out);  // OR_Gate
  buf or_2 (or_2_out, jal);  // OR_Gate
  buf or_3 (or_3_out, jr);  // OR_Gate
  or or_4 (or_4_out, ori, sw, lw);
  buf or_5 (or_5_out, jal);  // OR_Gate
  and and_2 (addu, R, comparator_2_eq);
  and and_3 (subu, R, comparator_3_eq);
  and and_4 (\and , R, comparator_4_eq);
  and and_5 (\or , R, comparator_5_eq);
  and and_6 (jr, R, comparator_6_eq);
  Priority_Encoder priority_encoder_1 (
    .in1(or_1_out), .in2(or_2_out), .in3(or_3_out), .out(NPCSel));  // open: in0, in4, in5, in6, in7, en_in, gs, en_out
  Pull_Resistor pull_resistor_1 (.node(NPCSel));
  Pull_Resistor pull_resistor_2 (.node(A3Sel));
  Priority_Encoder #(.select(2)) priority_encoder_2 (
    .in1(or_4_out), .in2(or_5_out), .out(A3Sel));  // open: in0, in3, gs, en_out, en_in
  or or_6 (EXTOp, lw, sw);
  buf or_7 (DMWr, sw);  // OR_Gate
  nor nor_1 (RFWr, beq, sw, jr);
  Comparator #(.width(6)) comparator_7 (.a(Opcode), .b(6'b000100), .eq(beq));  // open: gt, lt
  Comparator #(.width(6)) comparator_8 (.a(Opcode), .b(6'b001101), .eq(ori));  // open: gt, lt
  Comparator #(.width(6)) comparator_9 (.a(Opcode), .b(6'b000011), .eq(jal));  // open: gt, lt
  Comparator #(.width(6)) comparator_10 (.a(Opcode), .b(6'b101011), .eq(sw));  // open: gt, lt
  Comparator #(.width(6)) comparator_11 (.a(Opcode), .b(6'b100011), .eq(lw));  // open: gt, lt
  or or_8 (or_8_out, subu, beq);
  buf or_9 (or_9_out, ori);  // OR_Gate
  buf or_10 (or_10_out, sw);  // OR_Gate
  buf or_11 (or_11_out, jal);  // OR_Gate
  Priority_Encoder #(.select(2)) priority_encoder_3 (
    .in1(or_10_out), .in2(or_11_out), .out(WDSel));  // open: in0, in3, gs, en_out, en_in
  Priority_Encoder #(.select(4)) priority_encoder_4 (
    .in1(or_8_out), .in2(or_9_out), .out(ALUControl));  // open: in0, in3, in4, in5, in6, in7, in8, in9, in10, in11, in12, in13, in14, in15, gs, en_out, en_in
  buf or_12 (ALUSrcSel, ori);  // OR_Gate
  Pull_Resistor pull_resistor_3 (.node(WDSel));
  Pull_Resistor pull_resistor_4 (.node(ALUControl));

  // Other names for the same wires on the sheet: ALUSrcBSel = ALUSrcSel
endmodule

module EXT (
  input  [15:0] Imm16,
  input  Signed,
  output [31:0] Ext32
);

  wire [31:0] bit_extender_1_out, bit_extender_2_out;

  assign bit_extender_1_out = {{16{1'b0}}, Imm16};  // Bit_Extender bit_extender_1
  assign bit_extender_2_out = {{16{Imm16[15]}}, Imm16};  // Bit_Extender bit_extender_2
  Multiplexer #(.width(32), .enable("false")) multiplexer_1 (
    .in0(bit_extender_1_out), .in1(bit_extender_2_out), .out(Ext32), .sel(Signed));
endmodule
