// Logisim project cpu_pipeline-转发阻塞.circ as structural Verilog: 23 circuits, main circuit main
module main (
  input  RESET,
  output [31:0] _pc_w,
  output [31:0] _pc_m,
  output out_4,
  output [4:0] out_5,
  output [31:0] out_6,
  output out_7,
  output [31:0] out_8,
  output [31:0] out_9
);

  wire alu_1_zero, and_1_out, and_2_out, CLK, e_m_reg_1_zero_o, ExtOpD, F_Rt_Sel_M, Flush_E, not_1_out,
       not_2_out, PCSelD, Stall_D, Stall_F, ZeroD;
  wire [1:0] ALUSrcBSel, counter_2_q, F_Rs_Sel_D, F_Rs_Sel_E, F_Rt_Sel_D, F_Rt_Sel_E, RegAddrSel, RegDataSel,
       Tnew_E, Tnew_M, Tnew_W, Tuse1_D, Tuse2_D;
  wire [2:0] counter_1_q, NPCSelD;
  wire [3:0] ALUControlE;
  wire [4:0] d_e_reg_1_rd_o, d_e_reg_1_rs_o, d_e_reg_1_rt_o, e_m_reg_1_rd_o, e_m_reg_1_rs_o, e_m_reg_1_rt_o,
       Out_E, Out_M, Out_W, RdD, RdW_t, RsD, RtD, RtW, S1_D, S1_E, S2_D, S2_E, S2_M, ShamtD, ShamtE;
  wire [15:0] splt_1_addr_imm_15_0;
  wire [25:0] splt_1_imm_25_0;
  wire [31:0] adder_2_out, alu_1_aluresult, ALUResW, d_e_reg_1_pc_o, dm_1_rd, e_m_reg_1_ext32_o,
       e_m_reg_1_rd1_o, EtoD, Ext32, Ext32E, f_d_reg_1_pc4_o, Fwd_ALU_A_E, Fwd_ALU_B_E, Fwd_RD1_D, Fwd_RD2_D,
       Fwd_WD_M, im_1_data, InstD, InstE, InstM, InstW, MtoD, multiplexer_1_out, multiplexer_4_out, NPCD,
       PC4D, PC4E, PC4F, PC4M, PC4W, pc_1_do, PCM, PCW, RD1D, RD1E, RD2D, RD2E, RDW, WtoD;

  Clock clock_1 (.out(CLK));
  Multiplexer #(.width(32), .enable("false")) multiplexer_1 (
    .in0(PC4F), .in1(NPCD), .out(multiplexer_1_out), .sel(PCSelD));
  not not_1 (not_1_out, counter_1_q[0]);
  not not_2 (not_2_out, counter_1_q[1]);
  Counter #(.width(3), .max('h4), .ongoal("stay")) counter_1 (
    .D(3'b100), .Q(counter_1_q), .clk(CLK), .clr(RESET));  // open: load, count, carry
  and and_1 (and_1_out, not_1_out, not_2_out, counter_1_q[2]);
  Counter #(.width(2), .max('h3), .ongoal("stay")) counter_2 (
    .D(2'b11), .Q(counter_2_q), .clk(CLK), .clr(RESET));  // open: load, count, carry
  PC pc_1 (.clk(CLK), .reset(RESET), .DI(multiplexer_1_out), .DO(pc_1_do), .Stall(Stall_F));
  and and_2 (and_2_out, counter_2_q[0], counter_2_q[1]);
  // Probe on pc_1_do
  Adder #(.width(32)) adder_1 (.a(pc_1_do), .b(32'h4), .out(PC4F));  // open: cin, cout
  Multiplexer #(.width(32)) multiplexer_2 (.in0(32'h3000), .in1(PCW), .out(_pc_w), .sel(and_1_out));  // open: en
  Multiplexer #(.width(32)) multiplexer_3 (.in0(32'h3000), .in1(PCM), .out(_pc_m), .sel(and_2_out));  // open: en
  IM im_1 (.Address(pc_1_do), .Data(im_1_data));
  F_D_Reg f_d_reg_1 (
    .CLK(CLK), .Inst_I(im_1_data), .F_D_Stall(Stall_D), .PC4_I(pc_1_do), .Clear(RESET), .Inst_O(InstD),
    .PC4_O(f_d_reg_1_pc4_o));
  D d_1 (.Inst(InstD), .S1_D(S1_D), .S2_D(S2_D), .tuse1_D(Tuse1_D), .tuse2_D(Tuse2_D));
  SPLT splt_1 (
    .Instruction(InstD), .Addr_Imm_15_0(splt_1_addr_imm_15_0), .Rs_25_21(RsD), .Rt_20_16(RtD),
    .Imm_25_0(splt_1_imm_25_0), .Rd_15_11(RdD), .Shamt_6_10(ShamtD));  // open: Op_31_26, Func_5_0
  CU cu_1 (
    .Zero(ZeroD), .Inst(InstD), .NPCSel(NPCSelD), .EXTOp(ExtOpD), .PCSel(PCSelD));  // open: ALUControl, DMWr, ALUSrcBSel, RFWr, WDSel, A3Sel, Data_Type
  GRF grf_1 (.A1(RsD), .A2(RtD), .A3(out_5), .WD(out_6), .RD1(RD1D), .RD2(RD2D), .we(out_4), .rst(RESET));
  Comparator #(.width(32), .mode("unsigned")) comparator_1 (.a(Fwd_RD1_D), .b(Fwd_RD2_D), .eq(ZeroD));  // open: gt, lt
  EXT ext_1 (.Imm16(splt_1_addr_imm_15_0), .Signed(ExtOpD), .Ext32(Ext32));
  NPC npc_1 (.PC(f_d_reg_1_pc4_o), .Imm26(splt_1_imm_25_0), .NPC(NPCD), .NPCSel(NPCSelD), .PC4(PC4D), .RA(Fwd_RD1_D));
  D_E_Reg d_e_reg_1 (
    .Inst_O(InstE), .CLK(CLK), .Inst_I(InstD), .F_D_Stall(1'b0), .PC4_O(PC4E), .PC4_I(PC4D), .Clear(RESET),
    .RD1_I(Fwd_RD1_D), .RD2_I(Fwd_RD2_D), .Ext32_I(Ext32), .Rs_I(RsD), .Rt_I(RtD), .Rd_I(RdD), .RD1_O(RD1E),
    .RD2_O(RD2E), .Rs_O(d_e_reg_1_rs_o), .Rt_O(d_e_reg_1_rt_o), .Rd_O(d_e_reg_1_rd_o), .Ext32_O(Ext32E),
    .Shamt_I(ShamtD), .Shamt_O(ShamtE), .PC_I(f_d_reg_1_pc4_o), .PC_O(d_e_reg_1_pc_o), .Flush(Flush_E));
  Multiplexer #(.select(2), .width(32), .enable("false")) multiplexer_4 (
    .in0(Fwd_ALU_B_E), .in1(Ext32E), .out(multiplexer_4_out), .sel(ALUSrcBSel));  // open: in2, in3
  CU cu_2 (
    .Inst(InstE), .ALUControl(ALUControlE), .ALUSrcBSel(ALUSrcBSel));  // open: Zero, NPCSel, EXTOp, DMWr, RFWr, WDSel, A3Sel, Data_Type, PCSel
  ALU alu_1 (
    .SrcA(Fwd_ALU_A_E), .SrcB(multiplexer_4_out), .ALUControl(ALUControlE), .ALUResult(alu_1_aluresult),
    .Zero(alu_1_zero), .Shamt(ShamtE));
  E e_1 (
    .Instr(InstE), .pc_4(PC4E), .imm32(Ext32E), .S1_E(S1_E), .S2_E(S2_E), .Out_E(Out_E), .tnew_E(Tnew_E),
    .EtoD(EtoD));
  E_M_Reg e_m_reg_1 (
    .CLK(CLK), .Inst_I(InstE), .F_D_Stall(1'b0), .PC4_I(PC4E), .Clear(RESET), .RD1_I(Fwd_ALU_A_E),
    .RD2_I(Fwd_ALU_B_E), .Ext32_I(Ext32E), .Rs_I(d_e_reg_1_rs_o), .Rt_I(d_e_reg_1_rt_o),
    .Rd_I(d_e_reg_1_rd_o), .Inst_O(InstM), .PC4_O(PC4M), .RD1_O(e_m_reg_1_rd1_o), .RD2_O(out_9),
    .Ext32_O(e_m_reg_1_ext32_o), .Rs_O(e_m_reg_1_rs_o), .Rt_O(e_m_reg_1_rt_o), .Rd_O(e_m_reg_1_rd_o),
    .ALURes_I(alu_1_aluresult), .ALURes_O(out_8), .Zero_I(alu_1_zero), .Zero_O(e_m_reg_1_zero_o),
    .PC_I(d_e_reg_1_pc_o), .PC_O(PCM));  // open: Flush
  SU su_1 (
    .S1_D(S1_D), .S2_D(S2_D), .Tuse1_D(Tuse1_D), .Tuse2_D(Tuse2_D), .Out_E(Out_E), .Tnew_E(Tnew_E),
    .Tnew_M(Tnew_M), .Out_M(Out_M), .Stall_F(Stall_F), .Stall_D(Stall_D), .flush_E(Flush_E));
  CU cu_3 (
    .Inst(InstM), .DMWr(out_7));  // open: Zero, NPCSel, EXTOp, ALUControl, ALUSrcBSel, RFWr, WDSel, A3Sel, Data_Type, PCSel
  DM dm_1 (.WD(Fwd_WD_M), .Address(out_8), .RD(dm_1_rd), .Wr(out_7), .clk(CLK), .reset(RESET));
  M m_1 (.Instr(InstM), .pc_4(PC4M), .ALUresult(out_8), .S2_M(S2_M), .Out_M(Out_M), .tnew_M(Tnew_M), .MtoD(MtoD));
  FU fu_1 (
    .des_M(Out_M), .des_W(Out_W), .tNew_M(Tnew_M), .tNew_W(Tnew_W), .s1_D(S1_D), .s2_D(S2_D), .s1_E(S1_E),
    .s2_E(S2_E), .des_E(Out_E), .tNew_E(Tnew_E), .s2_M(S2_M), .fRtMsel(F_Rt_Sel_M), .fRsDsel(F_Rs_Sel_D),
    .fRtDsel(F_Rt_Sel_D), .fRsEsel(F_Rs_Sel_E), .fRtEsel(F_Rt_Sel_E));
  M_W_Reg m_w_reg_1 (
    .CLK(CLK), .Inst_I(InstM), .F_D_Stall(1'b0), .PC4_I(PC4M), .Clear(RESET), .RD1_I(e_m_reg_1_rd1_o),
    .RD2_I(Fwd_WD_M), .Ext32_I(e_m_reg_1_ext32_o), .Rs_I(e_m_reg_1_rs_o), .Rt_I(e_m_reg_1_rt_o),
    .Rd_I(e_m_reg_1_rd_o), .ALURes_I(out_8), .Zero_I(e_m_reg_1_zero_o), .Inst_O(InstW), .PC4_O(PC4W),
    .Rt_O(RtW), .Rd_O(RdW_t), .ALURes_O(ALUResW), .RD_I_2(dm_1_rd), .RD_O_2(RDW), .PC_I(PCM), .PC_O(PCW));  // open: RD1_O, RD2_O, Ext32_O, Rs_O, Zero_O
  // Probe on PCW
  Multiplexer #(.select(2), .width(32), .enable("false")) multiplexer_5 (
    .in0(RD1D), .in1(EtoD), .in2(MtoD), .in3({32{1'b0}}), .out(Fwd_RD1_D), .sel(F_Rs_Sel_D));
  Multiplexer #(.select(2), .width(32), .enable("false")) multiplexer_6 (
    .in0(RD2D), .in1(EtoD), .in2(MtoD), .in3({32{1'b0}}), .out(Fwd_RD2_D), .sel(F_Rt_Sel_D));
  Adder #(.width(32)) adder_2 (.a(PC4W), .b(32'h4), .out(adder_2_out));  // open: cin, cout
  Multiplexer #(.width(32), .enable("false")) multiplexer_7 (.in0(out_9), .in1(WtoD), .out(Fwd_WD_M), .sel(F_Rt_Sel_M));
  CU cu_4 (
    .Inst(InstW), .RFWr(out_4), .WDSel(RegDataSel), .A3Sel(RegAddrSel));  // open: Zero, NPCSel, EXTOp, ALUControl, DMWr, ALUSrcBSel, Data_Type, PCSel
  Multiplexer #(.select(2), .width(5), .enable("false")) multiplexer_8 (
    .in0(RdW_t), .in1(RtW), .in2({5{1'b1}}), .out(out_5), .sel(RegAddrSel));  // open: in3
  Multiplexer #(.select(2), .width(32), .enable("false")) multiplexer_9 (
    .in0(ALUResW), .in1(RDW), .in2(adder_2_out), .out(out_6), .sel(RegDataSel));  // open: in3
  W w_1 (.Instr(InstW), .pc4(PC4W), .ALUresult(ALUResW), .RD_W(RDW), .Out_W(Out_W), .tnew_W(Tnew_W), .WtoD(WtoD));
  Multiplexer #(.select(2), .width(32), .enable("false")) multiplexer_10 (
    .in0(RD1E), .in1(MtoD), .in2(WtoD), .in3({32{1'b0}}), .out(Fwd_ALU_A_E), .sel(F_Rs_Sel_E));
  Multiplexer #(.select(2), .width(32), .enable("false")) multiplexer_11 (
    .in0(RD2E), .in1(MtoD), .in2(WtoD), .in3({32{1'b0}}), .out(Fwd_ALU_B_E), .sel(F_Rt_Sel_E));

  // Other names for the same wires on the sheet: ALUResult[31:0] = out_8; DMAddrM[31:0] = out_8;
  //   DMDataM[31:0] = out_9; DMWrM = out_7; RegAddrW[4:0] = out_5; RegDataW[31:0] = out_6; RegWriteW = out_4
endmodule

module GRF (
  input  we,
  input  [4:0] A1,
  input  [4:0] A2,
  input  [4:0] A3,
  input  [31:0] WD,
  input  rst,
  output [31:0] RD1,
  output [31:0] RD2
);

  wire clk;
  wire [31:0] i0, i1, i2, i3, i4, i5, i6, i7, i8, i9, i10, i11, i12, i13, i14, i15, i16, i17, i18, i19, i20,
       i21, i22, i23, i24, i25, i26, i27, i28, i29, i30, i31, o0, o1, o2, o3, o4, o5, o6, o7, o8, o9, o10,
       o11, o12, o13, o14, o15, o16, o17, o18, o19, o20, o21, o22, o23, o24, o25, o26, o27, o28, o29, o30,
       o31;

  Clock clock_1 (.out(clk));
  Register #(.width(32)) r0 (.D({32{1'b0}}), .en(we), .Q(o0), .clk(clk), .clr(rst));
  Register #(.width(32)) r1 (.D(i1), .en(we), .Q(o1), .clk(clk), .clr(rst));
  Register #(.width(32)) r2 (.D(i2), .en(we), .Q(o2), .clk(clk), .clr(rst));
  Register #(.width(32)) r3 (.D(i3), .en(we), .Q(o3), .clk(clk), .clr(rst));
  Register #(.width(32)) r4 (.D(i4), .en(we), .Q(o4), .clk(clk), .clr(rst));
  Register #(.width(32)) r5 (.D(i5), .en(we), .Q(o5), .clk(clk), .clr(rst));
  Register #(.width(32)) r6 (.D(i6), .en(we), .Q(o6), .clk(clk), .clr(rst));
  Register #(.width(32)) r7 (.D(i7), .en(we), .Q(o7), .clk(clk), .clr(rst));
  Register #(.width(32)) r8 (.D(i8), .en(we), .Q(o8), .clk(clk), .clr(rst));
  Register #(.width(32)) r9 (.D(i9), .en(we), .Q(o9), .clk(clk), .clr(rst));
  Register #(.width(32)) r10 (.D(i10), .en(we), .Q(o10), .clk(clk), .clr(rst));
  Register #(.width(32)) r11 (.D(i11), .en(we), .Q(o11), .clk(clk), .clr(rst));
  Register #(.width(32)) r12 (.D(i12), .en(we), .Q(o12), .clk(clk), .clr(rst));
  Register #(.width(32)) r13 (.D(i13), .en(we), .Q(o13), .clk(clk), .clr(rst));
  Register #(.width(32)) r14 (.D(i14), .en(we), .Q(o14), .clk(clk), .clr(rst));
  Register #(.width(32)) r15 (.D(i15), .en(we), .Q(o15), .clk(clk), .clr(rst));
  Register #(.width(32)) r16 (.D(i16), .en(we), .Q(o16), .clk(clk), .clr(rst));
  Register #(.width(32)) r17 (.D(i17), .en(we), .Q(o17), .clk(clk), .clr(rst));
  Register #(.width(32)) r18 (.D(i18), .en(we), .Q(o18), .clk(clk), .clr(rst));
  Register #(.width(32)) r19 (.D(i19), .en(we), .Q(o19), .clk(clk), .clr(rst));
  Register #(.width(32)) r20 (.D(i20), .en(we), .Q(o20), .clk(clk), .clr(rst));
  Register #(.width(32)) r21 (.D(i21), .en(we), .Q(o21), .clk(clk), .clr(rst));
  Register #(.width(32)) r22 (.D(i22), .en(we), .Q(o22), .clk(clk), .clr(rst));
  Register #(.width(32)) r23 (.D(i23), .en(we), .Q(o23), .clk(clk), .clr(rst));
  Register #(.width(32)) r24 (.D(i24), .en(we), .Q(o24), .clk(clk), .clr(rst));
  Register #(.width(32)) r25 (.D(i25), .en(we), .Q(o25), .clk(clk), .clr(rst));
  Register #(.width(32)) r26 (.D(i26), .en(we), .Q(o26), .clk(clk), .clr(rst));
  Register #(.width(32)) r27 (.D(i27), .en(we), .Q(o27), .clk(clk), .clr(rst));
  Register #(.width(32)) r28 (.D(i28), .en(we), .Q(o28), .clk(clk), .clr(rst));
  Register #(.width(32)) r29 (.D(i29), .en(we), .Q(o29), .clk(clk), .clr(rst));
  Register #(.width(32)) r30 (.D(i30), .en(we), .Q(o30), .clk(clk), .clr(rst));
  Register #(.width(32)) r31 (.D(i31), .en(we), .Q(o31), .clk(clk), .clr(rst));
  Multiplexer #(.select(5), .width(32), .enable("false")) multiplexer_1 (
    .in0(o0), .in1(o1), .in2(o2), .in3(o3), .in4(o4), .in5(o5), .in6(o6), .in7(o7), .in8(o8), .in9(o9),
    .in10(o10), .in11(o11), .in12(o12), .in13(o13), .in14(o14), .in15(o15), .in16(o16), .in17(o17),
    .in18(o18), .in19(o19), .in20(o20), .in21(o21), .in22(o22), .in23(o23), .in24(o24), .in25(o25),
    .in26(o26), .in27(o27), .in28(o28), .in29(o29), .in30(o30), .in31(o31), .out(RD1), .sel(A1));
  Multiplexer #(.select(5), .width(32), .enable("false")) multiplexer_2 (
    .in0(o0), .in1(o1), .in2(o2), .in3(o3), .in4(o4), .in5(o5), .in6(o6), .in7(o7), .in8(o8), .in9(o9),
    .in10(o10), .in11(o11), .in12(o12), .in13(o13), .in14(o14), .in15(o15), .in16(o16), .in17(o17),
    .in18(o18), .in19(o19), .in20(o20), .in21(o21), .in22(o22), .in23(o23), .in24(o24), .in25(o25),
    .in26(o26), .in27(o27), .in28(o28), .in29(o29), .in30(o30), .in31(o31), .out(RD2), .sel(A2));
  Demultiplexer #(.select(5), .width(32), .tristate("true"), .enable("false")) demultiplexer_1 (
    .out0(i0), .out1(i1), .out2(i2), .out3(i3), .out4(i4), .out5(i5), .out6(i6), .out7(i7), .out8(i8),
    .out9(i9), .out10(i10), .out11(i11), .out12(i12), .out13(i13), .out14(i14), .out15(i15), .out16(i16),
    .out17(i17), .out18(i18), .out19(i19), .out20(i20), .out21(i21), .out22(i22), .out23(i23), .out24(i24),
    .out25(i25), .out26(i26), .out27(i27), .out28(i28), .out29(i29), .out30(i30), .out31(i31), .in(WD),
    .sel(A3));
endmodule

module PC (
  input  clk,
  input  reset,
  input  [31:0] DI,
  input  Stall,
  output [31:0] DO
);

  wire not_1_out;
  wire [31:0] register_1_q, subtractor_1_out;

  Subtractor #(.width(32)) subtractor_1 (.a(DI), .b(32'h3000), .out(subtractor_1_out));  // open: bin, bout
  not not_1 (not_1_out, Stall);
  Register #(.width(32)) register_1 (.D(subtractor_1_out), .en(not_1_out), .Q(register_1_q), .clk(clk), .clr(reset));
  Adder #(.width(32)) adder_1 (.a(register_1_q), .b(32'h3000), .out(DO));  // open: cin, cout
endmodule

module NPC (
  input  [31:0] PC,
  input  [25:0] Imm26,
  input  [2:0] NPCSel,
  input  [31:0] RA,
  output [31:0] NPC,
  output [31:0] PC4
);

  wire [31:0] adder_2_out, bit_extender_1_out, shifter_1_out;

  assign bit_extender_1_out = {{16{Imm26[15]}}, Imm26[15:0]};  // Bit_Extender bit_extender_1
  Adder #(.width(32)) adder_1 (.a(PC), .b(32'h4), .out(PC4));  // open: cin, cout
  Shifter #(.width(32)) shifter_1 (.in(bit_extender_1_out), .\dist (5'b00010), .out(shifter_1_out));
  Adder #(.width(32)) adder_2 (.a(PC4), .b(shifter_1_out), .out(adder_2_out));  // open: cin, cout
  Multiplexer #(.select(3), .width(32), .enable("false")) multiplexer_1 (
    .in0(PC4), .in1(adder_2_out), .in2({PC[31:28], Imm26, 2'b00}), .in3(RA), .out(NPC), .sel(NPCSel));  // open: in4, in5, in6, in7
endmodule

module IM (
  input  [31:0] Address,
  output [31:0] Data
);

  ROM #(.addrWidth(10), .dataWidth(32)) rom_1 (.addr(Address[11:2]), .data(Data));  // open: sel

  // Notes on the sheet:
  //   contents of rom_1 (hex, n*v repeats v):
  //   34010064 ac010000 8c020000 401821
endmodule

module DM (
  input  Wr,
  input  clk,
  input  reset,
  input  [31:0] WD,
  input  [31:0] Address,
  output [31:0] RD
);

  RAM #(.addrWidth(10), .dataWidth(32), .bus("separate")) ram_1 (
    .addr(Address[11:2]), .din(WD), .data(RD), .str(Wr), .clk(clk), .clr(reset));  // open: sel, ld
endmodule

module ALU (
  input  [31:0] SrcA,
  input  [31:0] SrcB,
  input  [3:0] ALUControl,
  input  [4:0] Shamt,
  output [31:0] ALUResult,
  output Zero
);

  wire [31:0] adder_1_out, and_1_out, or_1_out, shifter_1_out, shifter_2_out, shifter_3_out, subtractor_1_out;

  Adder #(.width(32)) adder_1 (.a(SrcA), .b(SrcB), .out(adder_1_out));  // open: cin, cout
  Subtractor #(.width(32)) subtractor_1 (.a(SrcA), .b(SrcB), .out(subtractor_1_out));  // open: bin, bout
  assign or_1_out = SrcA | SrcB;  // OR_Gate or_1, 32 bits wide
  assign and_1_out = SrcA & SrcB;  // AND_Gate and_1, 32 bits wide
  Shifter #(.width(32)) shifter_1 (.in(SrcB), .\dist (5'b10000), .out(shifter_1_out));
  Shifter #(.width(32)) shifter_2 (.in(SrcB), .\dist (Shamt), .out(shifter_2_out));
  Shifter #(.width(32)) shifter_3 (.in(SrcA), .\dist (SrcB[4:0]), .out(shifter_3_out));
  Multiplexer #(.select(4), .width(32), .enable("false")) multiplexer_1 (
    .in0(adder_1_out), .in1(subtractor_1_out), .in2(or_1_out), .in3(and_1_out), .in4(shifter_1_out),
    .in5(shifter_2_out), .in6(shifter_3_out), .out(ALUResult), .sel(ALUControl));  // open: in7, in8, in9, in10, in11, in12, in13, in14, in15
  Pull_Resistor pull_resistor_1 (.node(ALUResult));
  Comparator #(.width(32)) comparator_1 (.a({32{1'b0}}), .b(ALUResult), .eq(Zero));  // open: gt, lt
endmodule

module SPLT (
  input  [31:0] Instruction,
  output [5:0] Op_31_26,
  output [15:0] Addr_Imm_15_0,
  output [4:0] Rs_25_21,
  output [4:0] Rt_20_16,
  output [25:0] Imm_25_0,
  output [4:0] Rd_15_11,
  output [4:0] Shamt_6_10,
  output [5:0] Func_5_0
);


  assign Addr_Imm_15_0 = Instruction[15:0];
  assign Func_5_0 = Instruction[5:0];
  assign Imm_25_0 = Instruction[25:0];
  assign Op_31_26 = Instruction[31:26];
  assign Rd_15_11 = Instruction[15:11];
  assign Rs_25_21 = Instruction[25:21];
  assign Rt_20_16 = Instruction[20:16];
  assign Shamt_6_10 = Instruction[10:6];
endmodule

module CU (
  input  Zero,
  input  [31:0] Inst,
  output [2:0] NPCSel,
  output EXTOp,
  output [3:0] ALUControl,
  output DMWr,
  output [1:0] ALUSrcBSel,
  output RFWr,
  output [1:0] WDSel,
  output [1:0] A3Sel,
  output [2:0] Data_Type,
  output PCSel
);

  wire _Load, _Save, add, addu, \and , and_1_out, beq, comparator_2_eq, comparator_3_eq, comparator_4_eq,
       comparator_5_eq, comparator_6_eq, comparator_7_eq, comparator_8_eq, comparator_9_eq, comparator_10_eq,
       comparator_11_eq, j, jal, jr, lb, lbu, lh, lhu, lui, lw, nop, not_2_out, \or , or_1_out, or_2_out,
       or_3_out, or_4_out, or_5_out, or_6_out, or_9_out, or_10_out, or_11_out, or_12_out, or_13_out,
       or_14_out, or_15_out, or_16_out, or_17_out, or_18_out, ori, R, sb, sh, sll, sllv, sub, subu, sw;

  Pull_Resistor pull_resistor_1 (.node(Zero));
  and and_1 (and_1_out, Zero, beq);
  Comparator #(.width(6)) comparator_1 (.a(Inst[31:26]), .b({6{1'b0}}), .eq(R));  // open: gt, lt
  Comparator #(.width(6)) comparator_2 (.a(Inst[5:0]), .b(6'b100001), .eq(comparator_2_eq));  // open: gt, lt
  Comparator #(.width(6)) comparator_3 (.a(Inst[5:0]), .b(6'b100011), .eq(comparator_3_eq));  // open: gt, lt
  Comparator #(.width(6)) comparator_4 (.a(Inst[5:0]), .b(6'b100100), .eq(comparator_4_eq));  // open: gt, lt
  Comparator #(.width(6)) comparator_5 (.a(Inst[5:0]), .b(6'b100101), .eq(comparator_5_eq));  // open: gt, lt
  Comparator #(.width(6)) comparator_6 (.a(Inst[5:0]), .b(6'b001000), .eq(comparator_6_eq));  // open: gt, lt
  Comparator #(.width(6)) comparator_7 (.a(Inst[5:0]), .b(6'b100000), .eq(comparator_7_eq));  // open: gt, lt
  Comparator #(.width(6)) comparator_8 (.a(Inst[5:0]), .b(6'b100010), .eq(comparator_8_eq));  // open: gt, lt
  buf or_1 (or_1_out, and_1_out);  // OR_Gate
  or or_2 (or_2_out, jal, j);
  buf or_3 (or_3_out, jr);  // OR_Gate
  or or_4 (or_4_out, ori, _Load, lui);
  buf or_5 (or_5_out, jal);  // OR_Gate
  and and_2 (addu, R, comparator_2_eq);
  and and_3 (subu, R, comparator_3_eq);
  and and_4 (\and , R, comparator_4_eq);
  and and_5 (\or , R, comparator_5_eq);
  and and_6 (jr, R, comparator_6_eq);
  and and_7 (add, R, comparator_7_eq);
  and and_8 (sub, R, comparator_8_eq);
  or or_6 (or_6_out, _Load, _Save);
  Priority_Encoder priority_encoder_1 (
    .in1(or_1_out), .in2(or_2_out), .in3(or_3_out), .out(NPCSel));  // open: in0, in4, in5, in6, in7, en_in, gs, en_out
  Pull_Resistor pull_resistor_2 (.node(NPCSel));
  Priority_Encoder #(.select(2)) priority_encoder_2 (
    .in1(or_4_out), .in2(or_5_out), .out(A3Sel));  // open: in0, in3, gs, en_out, en_in
  Pull_Resistor pull_resistor_3 (.node(A3Sel));
  buf or_7 (EXTOp, or_6_out);  // OR_Gate
  buf or_8 (DMWr, _Save);  // OR_Gate
  nor nor_1 (RFWr, beq, _Save, jr, j, nop);
  Comparator #(.width(6)) comparator_9 (.a(Inst[5:0]), .b({6{1'b0}}), .eq(comparator_9_eq));  // open: gt, lt
  Comparator #(.width(6)) comparator_10 (.a(Inst[5:0]), .b(6'b000100), .eq(comparator_10_eq));  // open: gt, lt
  not not_1 (PCSel, comparator_11_eq);
  Comparator #(.width(3), .mode("unsigned")) comparator_11 (
    .a(NPCSel), .b(3'b000), .eq(comparator_11_eq));  // open: gt, lt
  not not_2 (not_2_out, nop);
  and and_9 (sll, R, not_2_out, comparator_9_eq);
  and and_10 (sllv, R, comparator_10_eq);
  or or_9 (or_9_out, subu, beq, sub);
  or or_10 (or_10_out, ori, \or );
  buf or_11 (or_11_out, \and );  // OR_Gate
  buf or_12 (or_12_out, lui);  // OR_Gate
  buf or_13 (or_13_out, _Load);  // OR_Gate
  buf or_14 (or_14_out, jal);  // OR_Gate
  or or_15 (or_15_out, sh, lh);
  or or_16 (or_16_out, lhu, sb);
  buf or_17 (or_17_out, lb);  // OR_Gate
  Priority_Encoder #(.select(2)) priority_encoder_3 (
    .in1(or_13_out), .in2(or_14_out), .out(WDSel));  // open: in0, in3, gs, en_out, en_in
  Priority_Encoder #(.select(4)) priority_encoder_4 (
    .in1(or_9_out), .in2(or_10_out), .in3(or_11_out), .in4(or_12_out), .in5(sll), .in6(sllv), .out(ALUControl));  // open: in0, in7, in8, in9, in10, in11, in12, in13, in14, in15, gs, en_out, en_in
  Priority_Encoder priority_encoder_5 (
    .in1(or_15_out), .in2(or_16_out), .in3(or_17_out), .in4(lbu), .out(Data_Type));  // open: in0, in5, in6, in7, en_in, gs, en_out
  or or_18 (or_18_out, ori, _Save, _Load, lui);
  Pull_Resistor pull_resistor_4 (.node(WDSel));
  Pull_Resistor pull_resistor_5 (.node(ALUControl));
  Pull_Resistor pull_resistor_6 (.node(Data_Type));
  Priority_Encoder #(.select(2)) priority_encoder_6 (
    .in1(or_18_out), .out(ALUSrcBSel));  // open: in0, in2, in3, gs, en_out, en_in
  Comparator #(.width(6)) comparator_12 (.a(Inst[31:26]), .b(6'b000100), .eq(beq));  // open: gt, lt
  Comparator #(.width(6)) comparator_13 (.a(Inst[31:26]), .b(6'b001101), .eq(ori));  // open: gt, lt
  Comparator #(.width(6)) comparator_14 (.a(Inst[31:26]), .b(6'b000011), .eq(jal));  // open: gt, lt
  Comparator #(.width(6)) comparator_15 (.a(Inst[31:26]), .b(6'b101011), .eq(sw));  // open: gt, lt
  Comparator #(.width(6)) comparator_16 (.a(Inst[31:26]), .b(6'b100011), .eq(lw));  // open: gt, lt
  Comparator #(.width(6)) comparator_17 (.a(Inst[31:26]), .b(6'b001111), .eq(lui));  // open: gt, lt
  Comparator #(.width(6)) comparator_18 (.a(Inst[31:26]), .b(6'b100001), .eq(lh));  // open: gt, lt
  Comparator #(.width(32), .mode("unsigned")) comparator_19 (.a(Inst), .b({32{1'b0}}), .eq(nop));  // open: gt, lt
  Pull_Resistor pull_resistor_7 (.node(ALUSrcBSel));
  Comparator #(.width(6)) comparator_20 (.a(Inst[31:26]), .b(6'b100101), .eq(lhu));  // open: gt, lt
  Comparator #(.width(6)) comparator_21 (.a(Inst[31:26]), .b(6'b100000), .eq(lb));  // open: gt, lt
  Comparator #(.width(6)) comparator_22 (.a(Inst[31:26]), .b(6'b100100), .eq(lbu));  // open: gt, lt
  Comparator #(.width(6)) comparator_23 (.a(Inst[31:26]), .b(6'b101001), .eq(sh));  // open: gt, lt
  Comparator #(.width(6)) comparator_24 (.a(Inst[31:26]), .b(6'b101000), .eq(sb));  // open: gt, lt
  Comparator #(.width(6)) comparator_25 (.a(Inst[31:26]), .b(6'b000010), .eq(j));  // open: gt, lt
  or or_19 (_Save, sw, sh, sb);
  or or_20 (_Load, lhu, lb, lbu, lh, lw);

  // Other names for the same wires on the sheet: Func[5:0] = Inst[5:0]; Opcode[5:0] = Inst[31:26]

  // Notes on the sheet:
  //   无溢出检测
  //   不用写入寄存器的指令！！！
endmodule

module EXT (
  input  [15:0] Imm16,
  input  Signed,
  output [31:0] Ext32
);

  wire [31:0] bit_extender_1_out, bit_extender_2_out;

  assign bit_extender_1_out = {{16{1'b0}}, Imm16};  // Bit_Extender bit_extender_1
  assign bit_extender_2_out = {{16{Imm16[15]}}, Imm16};  // Bit_Extender bit_extender_2
  Multiplexer #(.width(32), .enable("false")) multiplexer_1 (
    .in0(bit_extender_1_out), .in1(bit_extender_2_out), .out(Ext32), .sel(Signed));
endmodule

module MR (
  input  [31:0] Data,
  input  [31:0] Addr,
  input  [2:0] Data_Type,
  output [31:0] Out
);

  wire [7:0] multiplexer_2_out;
  wire [15:0] multiplexer_1_out;
  wire [31:0] lb, lbu, lh, lhu;

  Multiplexer #(.width(16), .enable("false")) multiplexer_1 (
    .in0(Data[15:0]), .in1(Data[31:16]), .out(multiplexer_1_out), .sel(Addr[1]));
  Multiplexer #(.select(2), .width(8), .enable("false")) multiplexer_2 (
    .in0(Data[7:0]), .in1(Data[15:8]), .in2(Data[23:16]), .in3(Data[31:24]), .out(multiplexer_2_out),
    .sel(Addr[1:0]));
  assign lh = {{16{multiplexer_1_out[15]}}, multiplexer_1_out};  // Bit_Extender bit_extender_1
  assign lhu = {{16{1'b0}}, multiplexer_1_out};  // Bit_Extender bit_extender_2
  assign lb = {{24{multiplexer_2_out[7]}}, multiplexer_2_out};  // Bit_Extender bit_extender_3
  assign lbu = {{24{1'b0}}, multiplexer_2_out};  // Bit_Extender bit_extender_4
  Multiplexer #(.select(3), .width(32), .enable("false")) multiplexer_3 (
    .in0(Data), .in1(lh), .in2(lhu), .in3(lb), .in4(lbu), .out(Out), .sel(Data_Type));  // open: in5, in6, in7
  Pull_Resistor pull_resistor_1 (.node(Out));

  // Other names for the same wires on the sheet: lw[31:0] = Data
endmodule

module MW (
  input  [31:0] Data,
  input  [31:0] Addr,
  input  [31:0] Old_Data,
  input  [2:0] Data_Type,
  output [31:0] Out
);

  wire [31:0] and_1_out, and_2_out, not_1_out, sb, sh, shifter_1_out, shifter_2_out;

  Multiplexer #(.width(32), .enable("false")) multiplexer_1 (
    .in0({Old_Data[31:16], Data[15:0]}), .in1({Data[15:0], Old_Data[15:0]}), .out(sh), .sel(Addr[1]));
  Shifter #(.width(32), .shift("rl")) shifter_1 (.in(32'hffffff00), .\dist ({Addr[1:0], 3'b000}), .out(shifter_1_out));
  Shifter #(.width(32)) shifter_2 (.in(Data), .\dist ({Addr[1:0], 3'b000}), .out(shifter_2_out));
  assign and_1_out = Old_Data & shifter_1_out;  // AND_Gate and_1, 32 bits wide
  assign not_1_out = ~shifter_1_out;  // NOT_Gate not_1, 32 bits wide
  assign and_2_out = not_1_out & shifter_2_out;  // AND_Gate and_2, 32 bits wide
  Multiplexer #(.select(3), .width(32), .enable("false")) multiplexer_2 (
    .in0(Data), .in1(sh), .in2(sb), .out(Out), .sel(Data_Type));  // open: in3, in4, in5, in6, in7
  assign sb = and_1_out | and_2_out;  // OR_Gate or_1, 32 bits wide
  Pull_Resistor pull_resistor_1 (.node(Out));

  // Other names for the same wires on the sheet: sw[31:0] = Data
endmodule

module F_D_Reg (
  input  CLK,
  input  [31:0] Inst_I,
  input  F_D_Stall,
  input  [31:0] PC4_I,
  input  Clear,
  output [31:0] Inst_O,
  output [31:0] PC4_O
);

  wire not_1_out, not_2_out;

  not not_1 (not_1_out, F_D_Stall);
  not not_2 (not_2_out, F_D_Stall);
  Register #(.width(32)) register_1 (.D(Inst_I), .en(not_1_out), .Q(Inst_O), .clk(CLK), .clr(Clear));
  Register #(.width(32)) register_2 (.D(PC4_I), .en(not_2_out), .Q(PC4_O), .clk(CLK), .clr(Clear));
endmodule

module D_E_Reg (
  input  CLK,
  input  [31:0] Inst_I,
  input  Flush,
  input  [31:0] PC_I,
  input  F_D_Stall,
  input  [31:0] PC4_I,
  input  Clear,
  input  [31:0] RD1_I,
  input  [31:0] RD2_I,
  input  [31:0] Ext32_I,
  input  [4:0] Rs_I,
  input  [4:0] Rt_I,
  input  [4:0] Rd_I,
  input  [4:0] Shamt_I,
  output [31:0] Inst_O,
  output [31:0] PC_O,
  output [31:0] PC4_O,
  output [31:0] RD1_O,
  output [31:0] RD2_O,
  output [31:0] Ext32_O,
  output [4:0] Rs_O,
  output [4:0] Rt_O,
  output [4:0] Rd_O,
  output [4:0] Shamt_O
);

  wire not_1_out, not_2_out, not_3_out, not_4_out, not_5_out, not_6_out, not_7_out, not_8_out, not_9_out,
       not_10_out;
  wire [4:0] multiplexer_6_out, multiplexer_7_out, multiplexer_9_out, multiplexer_10_out;
  wire [31:0] multiplexer_1_out, multiplexer_2_out, multiplexer_3_out, multiplexer_4_out, multiplexer_5_out,
       multiplexer_8_out;

  Multiplexer #(.width(32), .enable("false")) multiplexer_1 (
    .in0(Inst_I), .in1({32{1'b0}}), .out(multiplexer_1_out), .sel(Flush));
  not not_1 (not_1_out, F_D_Stall);
  Multiplexer #(.width(32), .enable("false")) multiplexer_2 (
    .in0(PC4_I), .in1({32{1'b0}}), .out(multiplexer_2_out), .sel(Flush));
  Multiplexer #(.width(32), .enable("false")) multiplexer_3 (
    .in0(RD1_I), .in1({32{1'b0}}), .out(multiplexer_3_out), .sel(Flush));
  Multiplexer #(.width(32), .enable("false")) multiplexer_4 (
    .in0(RD2_I), .in1({32{1'b0}}), .out(multiplexer_4_out), .sel(Flush));
  Multiplexer #(.width(32), .enable("false")) multiplexer_5 (
    .in0(Ext32_I), .in1({32{1'b0}}), .out(multiplexer_5_out), .sel(Flush));
  Register #(.width(32)) register_1 (.D(multiplexer_1_out), .en(not_1_out), .Q(Inst_O), .clk(CLK), .clr(Clear));
  Register #(.width(32)) register_2 (.D(multiplexer_2_out), .en(not_2_out), .Q(PC4_O), .clk(CLK), .clr(Clear));
  not not_2 (not_2_out, F_D_Stall);
  Register #(.width(32)) register_3 (.D(multiplexer_3_out), .en(not_3_out), .Q(RD1_O), .clk(CLK), .clr(Clear));
  not not_3 (not_3_out, F_D_Stall);
  Register #(.width(32)) register_4 (.D(multiplexer_4_out), .en(not_4_out), .Q(RD2_O), .clk(CLK), .clr(Clear));
  not not_4 (not_4_out, F_D_Stall);
  Register #(.width(32)) register_5 (.D(multiplexer_5_out), .en(not_5_out), .Q(Ext32_O), .clk(CLK), .clr(Clear));
  not not_5 (not_5_out, F_D_Stall);
  Multiplexer #(.width(5), .enable("false")) multiplexer_6 (
    .in0(Rd_I), .in1({5{1'b0}}), .out(multiplexer_6_out), .sel(Flush));
  Multiplexer #(.width(5), .enable("false")) multiplexer_7 (
    .in0(Shamt_I), .in1({5{1'b0}}), .out(multiplexer_7_out), .sel(Flush));
  Multiplexer #(.width(32), .enable("false")) multiplexer_8 (
    .in0(PC_I), .in1({32{1'b0}}), .out(multiplexer_8_out), .sel(Flush));
  Multiplexer #(.width(5), .enable("false")) multiplexer_9 (
    .in0(Rt_I), .in1({5{1'b0}}), .out(multiplexer_9_out), .sel(Flush));
  Multiplexer #(.width(5), .enable("false")) multiplexer_10 (
    .in0(Rs_I), .in1({5{1'b0}}), .out(multiplexer_10_out), .sel(Flush));
  not not_6 (not_6_out, F_D_Stall);
  not not_7 (not_7_out, F_D_Stall);
  not not_8 (not_8_out, F_D_Stall);
  not not_9 (not_9_out, F_D_Stall);
  not not_10 (not_10_out, F_D_Stall);
  Register #(.width(5)) register_6 (.D(multiplexer_10_out), .en(not_6_out), .Q(Rs_O), .clk(CLK), .clr(Clear));
  Register #(.width(5)) register_7 (.D(multiplexer_9_out), .en(not_7_out), .Q(Rt_O), .clk(CLK), .clr(Clear));
  Register #(.width(5)) register_8 (.D(multiplexer_6_out), .en(not_8_out), .Q(Rd_O), .clk(CLK), .clr(Clear));
  Register #(.width(5)) register_9 (.D(multiplexer_7_out), .en(not_9_out), .Q(Shamt_O), .clk(CLK), .clr(Clear));
  Register #(.width(32)) register_10 (.D(multiplexer_8_out), .en(not_10_out), .Q(PC_O), .clk(CLK), .clr(Clear));

  // Other names for the same wires on the sheet: Clear_i = Clear
endmodule

module E_M_Reg (
  input  CLK,
  input  [31:0] Inst_I,
  input  Flush,
  input  [31:0] PC_I,
  input  F_D_Stall,
  input  [31:0] PC4_I,
  input  Clear,
  input  [31:0] RD1_I,
  input  [31:0] RD2_I,
  input  [31:0] Ext32_I,
  input  [4:0] Rs_I,
  input  [4:0] Rt_I,
  input  [4:0] Rd_I,
  input  [31:0] ALURes_I,
  input  Zero_I,
  output [31:0] Inst_O,
  output [31:0] PC_O,
  output [31:0] PC4_O,
  output [31:0] RD1_O,
  output [31:0] RD2_O,
  output [31:0] Ext32_O,
  output [4:0] Rs_O,
  output [4:0] Rt_O,
  output [4:0] Rd_O,
  output [31:0] ALURes_O,
  output Zero_O
);

  wire Clear_t, multiplexer_1_out, not_1_out, not_2_out, not_3_out, not_4_out, not_5_out, not_6_out,
       not_7_out, not_8_out, not_9_out, not_10_out, not_11_out, register_1_q;

  Register #(.width(1)) register_1 (.D(multiplexer_1_out), .Q(register_1_q), .clk(CLK));  // open: en, clr
  Multiplexer #(.enable("false")) multiplexer_1 (.in0(1'b0), .in1(1'b1), .out(multiplexer_1_out), .sel(Flush));
  or or_1 (Clear_t, Clear, register_1_q);
  Register #(.width(32)) register_2 (.D(Inst_I), .en(not_1_out), .Q(Inst_O), .clk(CLK), .clr(Clear_t));
  not not_1 (not_1_out, F_D_Stall);
  Register #(.width(32)) register_3 (.D(PC4_I), .en(not_2_out), .Q(PC4_O), .clk(CLK), .clr(Clear_t));
  not not_2 (not_2_out, F_D_Stall);
  Register #(.width(32)) register_4 (.D(RD1_I), .en(not_3_out), .Q(RD1_O), .clk(CLK), .clr(Clear_t));
  not not_3 (not_3_out, F_D_Stall);
  Register #(.width(32)) register_5 (.D(RD2_I), .en(not_4_out), .Q(RD2_O), .clk(CLK), .clr(Clear_t));
  not not_4 (not_4_out, F_D_Stall);
  Register #(.width(32)) register_6 (.D(Ext32_I), .en(not_5_out), .Q(Ext32_O), .clk(CLK), .clr(Clear_t));
  not not_5 (not_5_out, F_D_Stall);
  not not_6 (not_6_out, F_D_Stall);
  not not_7 (not_7_out, F_D_Stall);
  not not_8 (not_8_out, F_D_Stall);
  not not_9 (not_9_out, F_D_Stall);
  not not_10 (not_10_out, F_D_Stall);
  Register #(.width(5)) register_7 (.D(Rs_I), .en(not_6_out), .Q(Rs_O), .clk(CLK), .clr(Clear_t));
  Register #(.width(5)) register_8 (.D(Rt_I), .en(not_7_out), .Q(Rt_O), .clk(CLK), .clr(Clear_t));
  Register #(.width(5)) register_9 (.D(Rd_I), .en(not_8_out), .Q(Rd_O), .clk(CLK), .clr(Clear_t));
  Register #(.width(32)) register_10 (.D(ALURes_I), .en(not_9_out), .Q(ALURes_O), .clk(CLK), .clr(Clear_t));
  Register #(.width(1)) register_11 (.D(Zero_I), .en(not_10_out), .Q(Zero_O), .clk(CLK), .clr(Clear_t));
  not not_11 (not_11_out, F_D_Stall);
  Register #(.width(32)) register_12 (.D(PC_I), .en(not_11_out), .Q(PC_O), .clk(CLK), .clr(Clear_t));

  // Other names for the same wires on the sheet: Clear_i = Clear
endmodule

module M_W_Reg (
  input  CLK,
  input  [31:0] Inst_I,
  input  [31:0] PC_I,
  input  F_D_Stall,
  input  [31:0] PC4_I,
  input  Clear,
  input  [31:0] RD1_I,
  input  [31:0] RD2_I,
  input  [31:0] Ext32_I,
  input  [4:0] Rs_I,
  input  [4:0] Rt_I,
  input  [4:0] Rd_I,
  input  [31:0] ALURes_I,
  input  Zero_I,
  input  [31:0] RD_I_2,
  output [31:0] Inst_O,
  output [31:0] PC_O,
  output [31:0] PC4_O,
  output [31:0] RD1_O,
  output [31:0] RD2_O,
  output [31:0] Ext32_O,
  output [4:0] Rs_O,
  output [4:0] Rt_O,
  output [4:0] Rd_O,
  output [31:0] ALURes_O,
  output Zero_O,
  output [31:0] RD_O_2
);

  wire not_1_out, not_2_out, not_3_out, not_4_out, not_5_out, not_6_out, not_7_out, not_8_out, not_9_out,
       not_10_out, not_11_out, not_12_out;

  Register #(.width(32)) register_1 (.D(Inst_I), .en(not_1_out), .Q(Inst_O), .clk(CLK), .clr(Clear));
  not not_1 (not_1_out, F_D_Stall);
  Register #(.width(32)) register_2 (.D(PC4_I), .en(not_2_out), .Q(PC4_O), .clk(CLK), .clr(Clear));
  not not_2 (not_2_out, F_D_Stall);
  Register #(.width(32)) register_3 (.D(RD1_I), .en(not_3_out), .Q(RD1_O), .clk(CLK), .clr(Clear));
  not not_3 (not_3_out, F_D_Stall);
  Register #(.width(32)) register_4 (.D(RD2_I), .en(not_4_out), .Q(RD2_O), .clk(CLK), .clr(Clear));
  not not_4 (not_4_out, F_D_Stall);
  Register #(.width(32)) register_5 (.D(Ext32_I), .en(not_5_out), .Q(Ext32_O), .clk(CLK), .clr(Clear));
  not not_5 (not_5_out, F_D_Stall);
  not not_6 (not_6_out, F_D_Stall);
  not not_7 (not_7_out, F_D_Stall);
  not not_8 (not_8_out, F_D_Stall);
  not not_9 (not_9_out, F_D_Stall);
  not not_10 (not_10_out, F_D_Stall);
  Register #(.width(5)) register_6 (.D(Rs_I), .en(not_6_out), .Q(Rs_O), .clk(CLK), .clr(Clear));
  Register #(.width(5)) register_7 (.D(Rt_I), .en(not_7_out), .Q(Rt_O), .clk(CLK), .clr(Clear));
  Register #(.width(5)) register_8 (.D(Rd_I), .en(not_8_out), .Q(Rd_O), .clk(CLK), .clr(Clear));
  Register #(.width(32)) register_9 (.D(ALURes_I), .en(not_9_out), .Q(ALURes_O), .clk(CLK), .clr(Clear));
  Register #(.width(1)) register_10 (.D(Zero_I), .en(not_10_out), .Q(Zero_O), .clk(CLK), .clr(Clear));
  not not_11 (not_11_out, F_D_Stall);
  not not_12 (not_12_out, F_D_Stall);
  Register #(.width(32)) register_11 (.D(RD_I_2), .en(not_11_out), .Q(RD_O_2), .clk(CLK), .clr(Clear));
  Register #(.width(32)) register_12 (.D(PC_I), .en(not_12_out), .Q(PC_O), .clk(CLK), .clr(Clear));

  // Other names for the same wires on the sheet: RD_I_t[31:0] = RD_I_2; RD_O_t[31:0] = RD_O_2
endmodule

module TJ (
  input  [31:0] Inst,
  output addu,
  output subu,
  output ori,
  output lui,
  output lw,
  output sw,
  output beq,
  output j,
  output jal,
  output jr,
  output nop
);

  wire _Load, _Save, add, \and , comparator_2_eq, comparator_3_eq, comparator_4_eq, comparator_5_eq,
       comparator_6_eq, comparator_7_eq, comparator_8_eq, comparator_9_eq, comparator_10_eq, lb, lbu, lh,
       lhu, not_1_out, \or , R, sb, sh, sll, sllv, sub;

  Comparator #(.width(6)) comparator_1 (.a(Inst[31:26]), .b({6{1'b0}}), .eq(R));  // open: gt, lt
  Comparator #(.width(6)) comparator_2 (.a(Inst[5:0]), .b(6'b100001), .eq(comparator_2_eq));  // open: gt, lt
  Comparator #(.width(6)) comparator_3 (.a(Inst[5:0]), .b(6'b100011), .eq(comparator_3_eq));  // open: gt, lt
  Comparator #(.width(6)) comparator_4 (.a(Inst[5:0]), .b(6'b100100), .eq(comparator_4_eq));  // open: gt, lt
  Comparator #(.width(6)) comparator_5 (.a(Inst[5:0]), .b(6'b100101), .eq(comparator_5_eq));  // open: gt, lt
  Comparator #(.width(6)) comparator_6 (.a(Inst[5:0]), .b(6'b001000), .eq(comparator_6_eq));  // open: gt, lt
  Comparator #(.width(6)) comparator_7 (.a(Inst[5:0]), .b(6'b100000), .eq(comparator_7_eq));  // open: gt, lt
  Comparator #(.width(6)) comparator_8 (.a(Inst[5:0]), .b(6'b100010), .eq(comparator_8_eq));  // open: gt, lt
  and and_1 (addu, R, comparator_2_eq);
  and and_2 (subu, R, comparator_3_eq);
  and and_3 (\and , R, comparator_4_eq);
  and and_4 (\or , R, comparator_5_eq);
  and and_5 (jr, R, comparator_6_eq);
  and and_6 (add, R, comparator_7_eq);
  and and_7 (sub, R, comparator_8_eq);
  Comparator #(.width(6)) comparator_9 (.a(Inst[5:0]), .b({6{1'b0}}), .eq(comparator_9_eq));  // open: gt, lt
  Comparator #(.width(6)) comparator_10 (.a(Inst[5:0]), .b(6'b000100), .eq(comparator_10_eq));  // open: gt, lt
  not not_1 (not_1_out, nop);
  and and_8 (sll, R, not_1_out, comparator_9_eq);
  and and_9 (sllv, R, comparator_10_eq);
  Comparator #(.width(6)) comparator_11 (.a(Inst[31:26]), .b(6'b000100), .eq(beq));  // open: gt, lt
  Comparator #(.width(6)) comparator_12 (.a(Inst[31:26]), .b(6'b001101), .eq(ori));  // open: gt, lt
  Comparator #(.width(6)) comparator_13 (.a(Inst[31:26]), .b(6'b000011), .eq(jal));  // open: gt, lt
  Comparator #(.width(6)) comparator_14 (.a(Inst[31:26]), .b(6'b101011), .eq(sw));  // open: gt, lt
  Comparator #(.width(6)) comparator_15 (.a(Inst[31:26]), .b(6'b100011), .eq(lw));  // open: gt, lt
  Comparator #(.width(6)) comparator_16 (.a(Inst[31:26]), .b(6'b001111), .eq(lui));  // open: gt, lt
  Comparator #(.width(6)) comparator_17 (.a(Inst[31:26]), .b(6'b100001), .eq(lh));  // open: gt, lt
  Comparator #(.width(32), .mode("unsigned")) comparator_18 (.a(Inst), .b({32{1'b0}}), .eq(nop));  // open: gt, lt
  Comparator #(.width(6)) comparator_19 (.a(Inst[31:26]), .b(6'b100101), .eq(lhu));  // open: gt, lt
  Comparator #(.width(6)) comparator_20 (.a(Inst[31:26]), .b(6'b100000), .eq(lb));  // open: gt, lt
  Comparator #(.width(6)) comparator_21 (.a(Inst[31:26]), .b(6'b100100), .eq(lbu));  // open: gt, lt
  Comparator #(.width(6)) comparator_22 (.a(Inst[31:26]), .b(6'b101001), .eq(sh));  // open: gt, lt
  Comparator #(.width(6)) comparator_23 (.a(Inst[31:26]), .b(6'b101000), .eq(sb));  // open: gt, lt
  Comparator #(.width(6)) comparator_24 (.a(Inst[31:26]), .b(6'b000010), .eq(j));  // open: gt, lt
  or or_1 (_Save, sw, sh, sb);
  or or_2 (_Load, lhu, lb, lbu, lh, lw);

  // Other names for the same wires on the sheet: Func[5:0] = Inst[5:0]; Opcode[5:0] = Inst[31:26]

  // Notes on the sheet:
  //   无溢出检测
endmodule

module D (
  input  [31:0] Inst,
  output [4:0] S1_D,
  output [4:0] S2_D,
  output [1:0] tuse1_D,
  output [1:0] tuse2_D
);

  wire addu, beq, j, jal, jr, lui, lw, nop, or_1_out, or_2_out, or_5_out, ori, subu, sw;
  wire [1:0] or_3_out;
  wire [4:0] Rs, Rt;

  TJ tj_1 (
    .Inst(Inst), .addu(addu), .subu(subu), .ori(ori), .lui(lui), .lw(lw), .sw(sw), .beq(beq), .j(j),
    .jal(jal), .jr(jr), .nop(nop));
  SPLT splt_1 (
    .Instruction(Inst), .Rs_25_21(Rs), .Rt_20_16(Rt));  // open: Op_31_26, Addr_Imm_15_0, Imm_25_0, Rd_15_11, Shamt_6_10, Func_5_0
  or or_1 (or_1_out, lw, sw, ori, beq, addu, subu, jr);
  Multiplexer #(.width(5), .enable("false")) multiplexer_1 (.in0({5{1'b0}}), .in1(Rs), .out(S1_D), .sel(or_1_out));
  or or_2 (or_2_out, sw, beq, addu, subu);
  Multiplexer #(.width(5), .enable("false")) multiplexer_2 (.in0({5{1'b0}}), .in1(Rt), .out(S2_D), .sel(or_2_out));
  or or_3 (or_3_out[0], addu, subu);
  buf or_4 (or_3_out[1], sw);  // OR_Gate
  or or_5 (or_5_out, lw, sw, ori, addu, subu);
  Multiplexer #(.select(2), .width(2), .enable("false")) multiplexer_3 (
    .in0(2'b00), .in1(2'b01), .in2(2'b10), .out(tuse2_D), .sel(or_3_out));  // open: in3
  Priority_Encoder #(.select(2)) priority_encoder_1 (
    .in1(or_5_out), .out(tuse1_D));  // open: in0, in2, in3, gs, en_out, en_in
  Pull_Resistor pull_resistor_1 (.node(tuse1_D));
endmodule

module E (
  input  [31:0] Instr,
  input  [31:0] pc_4,
  input  [31:0] imm32,
  output [4:0] S1_E,
  output [4:0] S2_E,
  output [4:0] Out_E,
  output [1:0] tnew_E,
  output [31:0] EtoD
);

  wire addu, beq, j, jal, jr, lui, lw, nop, or_1_out, or_2_out, ori, subu, sw;
  wire [1:0] or_3_out, or_5_out, or_7_out;
  wire [4:0] Rd, Rs, Rt;
  wire [31:0] adder_1_out;

  SPLT splt_1 (
    .Instruction(Instr), .Rs_25_21(Rs), .Rt_20_16(Rt), .Rd_15_11(Rd));  // open: Op_31_26, Addr_Imm_15_0, Imm_25_0, Shamt_6_10, Func_5_0
  TJ tj_1 (
    .Inst(Instr), .addu(addu), .subu(subu), .ori(ori), .lui(lui), .lw(lw), .sw(sw), .beq(beq), .j(j),
    .jal(jal), .jr(jr), .nop(nop));
  Adder #(.width(32)) adder_1 (.a(32'h4), .b(pc_4), .out(adder_1_out));  // open: cin, cout
  or or_1 (or_1_out, lw, sw, ori, addu, subu);
  Multiplexer #(.width(5), .enable("false")) multiplexer_1 (.in0({5{1'b0}}), .in1(Rs), .out(S1_E), .sel(or_1_out));
  or or_2 (or_2_out, sw, addu, subu);
  or or_3 (or_3_out[0], lui, lw, jal, ori);
  or or_4 (or_3_out[1], jal, addu, subu);
  or or_5 (or_5_out[0], lui, addu, subu, ori);
  buf or_6 (or_5_out[1], lw);  // OR_Gate
  buf or_7 (or_7_out[0], jal);  // OR_Gate
  buf or_8 (or_7_out[1], lui);  // OR_Gate
  Multiplexer #(.width(5), .enable("false")) multiplexer_2 (.in0({5{1'b0}}), .in1(Rt), .out(S2_E), .sel(or_2_out));
  Multiplexer #(.select(2), .width(5), .enable("false")) multiplexer_3 (
    .in0({5{1'b0}}), .in1(Rt), .in2(Rd), .in3({5{1'b1}}), .out(Out_E), .sel(or_3_out));
  Multiplexer #(.select(2), .width(2), .enable("false")) multiplexer_4 (
    .in0(2'b00), .in1(2'b01), .in2(2'b10), .out(tnew_E), .sel(or_5_out));  // open: in3
  Multiplexer #(.select(2), .width(32), .enable("false")) multiplexer_5 (
    .in0({32{1'b0}}), .in1(adder_1_out), .in2(imm32), .out(EtoD), .sel(or_7_out));  // open: in3

  // Other names for the same wires on the sheet: Inst[31:0] = Instr
endmodule

module M (
  input  [31:0] Instr,
  input  [31:0] pc_4,
  input  [31:0] ALUresult,
  output [4:0] S2_M,
  output [4:0] Out_M,
  output [1:0] tnew_M,
  output [31:0] MtoD
);

  wire addu, beq, j, jal, jr, lui, lw, nop, or_5_out, or_6_out, ori, subu, sw;
  wire [1:0] or_1_out, or_3_out;
  wire [4:0] Rd, Rs, Rt;
  wire [31:0] adder_1_out;

  SPLT splt_1 (
    .Instruction(Instr), .Rs_25_21(Rs), .Rt_20_16(Rt), .Rd_15_11(Rd));  // open: Op_31_26, Addr_Imm_15_0, Imm_25_0, Shamt_6_10, Func_5_0
  TJ tj_1 (
    .Inst(Instr), .addu(addu), .subu(subu), .ori(ori), .lui(lui), .lw(lw), .sw(sw), .beq(beq), .j(j),
    .jal(jal), .jr(jr), .nop(nop));
  Adder #(.width(32)) adder_1 (.a(32'h4), .b(pc_4), .out(adder_1_out));  // open: cin, cout
  or or_1 (or_1_out[0], lui, lw, jal, ori);
  or or_2 (or_1_out[1], jal, addu, subu);
  buf or_3 (or_3_out[0], jal);  // OR_Gate
  or or_4 (or_3_out[1], ori, lui, addu, subu);
  Multiplexer #(.width(5), .enable("false")) multiplexer_1 (.in0({5{1'b0}}), .in1(Rt), .out(S2_M), .sel(or_5_out));
  buf or_5 (or_5_out, sw);  // OR_Gate
  Multiplexer #(.select(2), .width(5), .enable("false")) multiplexer_2 (
    .in0({5{1'b0}}), .in1(Rt), .in2(Rd), .in3({5{1'b1}}), .out(Out_M), .sel(or_1_out));
  buf or_6 (or_6_out, lw);  // OR_Gate
  Multiplexer #(.width(2), .enable("false")) multiplexer_3 (.in0(2'b00), .in1(2'b01), .out(tnew_M), .sel(or_6_out));
  Multiplexer #(.select(2), .width(32), .enable("false")) multiplexer_4 (
    .in0({32{1'b0}}), .in1(adder_1_out), .in2(ALUresult), .out(MtoD), .sel(or_3_out));  // open: in3

  // Other names for the same wires on the sheet: Inst[31:0] = Instr
endmodule

module W (
  input  [31:0] Instr,
  input  [31:0] pc4,
  input  [31:0] ALUresult,
  input  [31:0] RD_W,
  output [4:0] Out_W,
  output [1:0] tnew_W,
  output [31:0] WtoD
);

  wire addu, beq, j, jal, jr, lui, lw, nop, ori, subu, sw;
  wire [1:0] or_1_out, or_3_out;
  wire [4:0] Rd, Rs, Rt;
  wire [31:0] adder_1_out;

  SPLT splt_1 (
    .Instruction(Instr), .Rs_25_21(Rs), .Rt_20_16(Rt), .Rd_15_11(Rd));  // open: Op_31_26, Addr_Imm_15_0, Imm_25_0, Shamt_6_10, Func_5_0
  TJ tj_1 (
    .Inst(Instr), .addu(addu), .subu(subu), .ori(ori), .lui(lui), .lw(lw), .sw(sw), .beq(beq), .j(j),
    .jal(jal), .jr(jr), .nop(nop));
  Adder #(.width(32)) adder_1 (.a(32'h4), .b(pc4), .out(adder_1_out));  // open: cin, cout
  or or_1 (or_1_out[0], lw, jal);
  or or_2 (or_1_out[1], ori, lui, lw, addu, subu);
  or or_3 (or_3_out[0], lui, lw, jal, ori);
  or or_4 (or_3_out[1], jal, addu, subu);
  Multiplexer #(.select(2), .width(32), .enable("false")) multiplexer_1 (
    .in0({32{1'b0}}), .in1(adder_1_out), .in2(ALUresult), .in3(RD_W), .out(WtoD), .sel(or_1_out));
  Multiplexer #(.select(2), .width(5), .enable("false")) multiplexer_2 (
    .in0({5{1'b0}}), .in1(Rt), .in2(Rd), .in3({5{1'b1}}), .out(Out_W), .sel(or_3_out));

  assign tnew_W = 2'b00;

  // Other names for the same wires on the sheet: Inst[31:0] = Instr
endmodule

module SU (
  input  [4:0] S1_D,
  input  [4:0] S2_D,
  input  [1:0] Tuse1_D,
  input  [1:0] Tuse2_D,
  input  [4:0] Out_E,
  input  [1:0] Tnew_E,
  input  [4:0] Out_M,
  input  [1:0] Tnew_M,
  output Stall_F,
  output Stall_D,
  output flush_E
);

  wire and_1_out, and_2_out, and_3_out, and_4_out, comparator_1_eq, comparator_2_eq, comparator_3_lt,
       comparator_4_eq, comparator_5_eq, comparator_6_lt, comparator_7_eq, comparator_8_eq, comparator_9_lt,
       comparator_10_eq, comparator_11_eq, comparator_12_lt, not_1_out, not_2_out, not_3_out, not_4_out;

  Comparator #(.width(5), .mode("unsigned")) comparator_1 (
    .a(S1_D), .b({5{1'b0}}), .eq(comparator_1_eq));  // open: gt, lt
  Comparator #(.width(5), .mode("unsigned")) comparator_2 (.a(S1_D), .b(Out_E), .eq(comparator_2_eq));  // open: gt, lt
  Comparator #(.width(2), .mode("unsigned")) comparator_3 (
    .a(Tuse1_D), .b(Tnew_E), .lt(comparator_3_lt));  // open: gt, eq
  Comparator #(.width(5), .mode("unsigned")) comparator_4 (
    .a(S2_D), .b({5{1'b0}}), .eq(comparator_4_eq));  // open: gt, lt
  Comparator #(.width(5), .mode("unsigned")) comparator_5 (.a(S2_D), .b(Out_E), .eq(comparator_5_eq));  // open: gt, lt
  Comparator #(.width(2), .mode("unsigned")) comparator_6 (
    .a(Tuse2_D), .b(Tnew_E), .lt(comparator_6_lt));  // open: gt, eq
  Comparator #(.width(5), .mode("unsigned")) comparator_7 (
    .a(S1_D), .b({5{1'b0}}), .eq(comparator_7_eq));  // open: gt, lt
  Comparator #(.width(5), .mode("unsigned")) comparator_8 (.a(S1_D), .b(Out_M), .eq(comparator_8_eq));  // open: gt, lt
  Comparator #(.width(2), .mode("unsigned")) comparator_9 (
    .a(Tuse1_D), .b(Tnew_M), .lt(comparator_9_lt));  // open: gt, eq
  Comparator #(.width(5), .mode("unsigned")) comparator_10 (
    .a(S2_D), .b({5{1'b0}}), .eq(comparator_10_eq));  // open: gt, lt
  Comparator #(.width(5), .mode("unsigned")) comparator_11 (
    .a(S2_D), .b(Out_M), .eq(comparator_11_eq));  // open: gt, lt
  Comparator #(.width(2), .mode("unsigned")) comparator_12 (
    .a(Tuse2_D), .b(Tnew_M), .lt(comparator_12_lt));  // open: gt, eq
  not not_1 (not_1_out, comparator_1_eq);
  not not_2 (not_2_out, comparator_4_eq);
  not not_3 (not_3_out, comparator_7_eq);
  not not_4 (not_4_out, comparator_10_eq);
  and and_1 (and_1_out, not_1_out, comparator_2_eq, comparator_3_lt);
  and and_2 (and_2_out, not_2_out, comparator_5_eq, comparator_6_lt);
  and and_3 (and_3_out, not_3_out, comparator_8_eq, comparator_9_lt);
  and and_4 (and_4_out, not_4_out, comparator_11_eq, comparator_12_lt);
  or or_1 (flush_E, and_1_out, and_2_out, and_3_out, and_4_out);

  assign Stall_D = flush_E;
  assign Stall_F = flush_E;

  // Other names for the same wires on the sheet: Stall = flush_E
endmodule

module FU (
  input  [4:0] s1_D,
  input  [4:0] s2_D,
  input  [4:0] s1_E,
  input  [4:0] s2_E,
  input  [4:0] des_E,
  input  [1:0] tNew_E,
  input  [4:0] s2_M,
  input  [1:0] tNew_M,
  input  [4:0] des_M,
  input  [1:0] tNew_W,
  input  [4:0] des_W,
  output [1:0] fRsDsel,
  output [1:0] fRtDsel,
  output [1:0] fRsEsel,
  output [1:0] fRtEsel,
  output fRtMsel
);

  wire and_1_out, and_2_out, and_3_out, and_4_out, and_5_out, and_6_out, and_7_out, and_8_out, and_9_out,
       comparator_1_eq, comparator_2_eq, comparator_3_eq, comparator_4_eq, comparator_5_eq, comparator_6_eq,
       comparator_7_eq, comparator_8_eq, comparator_9_eq, comparator_10_eq, comparator_11_eq,
       comparator_12_eq, comparator_13_eq, comparator_14_eq, comparator_15_eq, comparator_16_eq,
       comparator_17_eq, comparator_18_eq, comparator_19_eq, comparator_20_eq, comparator_21_eq,
       comparator_22_eq, comparator_23_eq, comparator_24_eq, comparator_25_eq, comparator_26_eq,
       comparator_27_eq, not_1_out, not_2_out, not_3_out, not_4_out, not_5_out, not_6_out, not_7_out,
       not_8_out, not_9_out;
  wire [1:0] multiplexer_1_out, multiplexer_2_out, multiplexer_5_out, multiplexer_6_out;

  Comparator #(.width(5), .mode("unsigned")) comparator_1 (
    .a(s1_D), .b({5{1'b0}}), .eq(comparator_1_eq));  // open: gt, lt
  not not_1 (not_1_out, comparator_1_eq);
  Comparator #(.width(5), .mode("unsigned")) comparator_2 (.a(s1_D), .b(des_M), .eq(comparator_2_eq));  // open: gt, lt
  Comparator #(.width(2), .mode("unsigned")) comparator_3 (
    .a(tNew_M), .b(2'b00), .eq(comparator_3_eq));  // open: gt, lt
  Comparator #(.width(5), .mode("unsigned")) comparator_4 (
    .a(s1_D), .b({5{1'b0}}), .eq(comparator_4_eq));  // open: gt, lt
  Comparator #(.width(5), .mode("unsigned")) comparator_5 (.a(s1_D), .b(des_E), .eq(comparator_5_eq));  // open: gt, lt
  Comparator #(.width(2), .mode("unsigned")) comparator_6 (
    .a(tNew_E), .b(2'b00), .eq(comparator_6_eq));  // open: gt, lt
  Comparator #(.width(5), .mode("unsigned")) comparator_7 (
    .a(s2_D), .b({5{1'b0}}), .eq(comparator_7_eq));  // open: gt, lt
  Comparator #(.width(5), .mode("unsigned")) comparator_8 (.a(s2_D), .b(des_M), .eq(comparator_8_eq));  // open: gt, lt
  Comparator #(.width(2), .mode("unsigned")) comparator_9 (
    .a(tNew_M), .b(2'b00), .eq(comparator_9_eq));  // open: gt, lt
  Comparator #(.width(5), .mode("unsigned")) comparator_10 (
    .a(s2_D), .b({5{1'b0}}), .eq(comparator_10_eq));  // open: gt, lt
  Comparator #(.width(5), .mode("unsigned")) comparator_11 (
    .a(s2_D), .b(des_E), .eq(comparator_11_eq));  // open: gt, lt
  Comparator #(.width(2), .mode("unsigned")) comparator_12 (
    .a(tNew_E), .b(2'b00), .eq(comparator_12_eq));  // open: gt, lt
  and and_1 (and_1_out, not_1_out, comparator_2_eq, comparator_3_eq);
  not not_2 (not_2_out, comparator_4_eq);
  not not_3 (not_3_out, comparator_7_eq);
  not not_4 (not_4_out, comparator_10_eq);
  Multiplexer #(.width(2)) multiplexer_1 (
    .in0(2'b00), .in1(2'b10), .out(multiplexer_1_out), .sel(and_1_out));  // open: en
  and and_2 (and_2_out, not_2_out, comparator_5_eq, comparator_6_eq);
  and and_3 (and_3_out, not_3_out, comparator_8_eq, comparator_9_eq);
  and and_4 (and_4_out, not_4_out, comparator_11_eq, comparator_12_eq);
  Multiplexer #(.width(2)) multiplexer_2 (
    .in0(2'b00), .in1(2'b10), .out(multiplexer_2_out), .sel(and_3_out));  // open: en
  Multiplexer #(.width(2)) multiplexer_3 (
    .in0(multiplexer_1_out), .in1(2'b01), .out(fRsDsel), .sel(and_2_out));  // open: en
  Multiplexer #(.width(2)) multiplexer_4 (
    .in0(multiplexer_2_out), .in1(2'b01), .out(fRtDsel), .sel(and_4_out));  // open: en
  Comparator #(.width(5), .mode("unsigned")) comparator_13 (
    .a(s1_E), .b({5{1'b0}}), .eq(comparator_13_eq));  // open: gt, lt
  Comparator #(.width(5), .mode("unsigned")) comparator_14 (
    .a(s1_E), .b(des_W), .eq(comparator_14_eq));  // open: gt, lt
  Comparator #(.width(2), .mode("unsigned")) comparator_15 (
    .a(tNew_W), .b(2'b00), .eq(comparator_15_eq));  // open: gt, lt
  Comparator #(.width(5), .mode("unsigned")) comparator_16 (
    .a(s1_E), .b({5{1'b0}}), .eq(comparator_16_eq));  // open: gt, lt
  Comparator #(.width(5), .mode("unsigned")) comparator_17 (
    .a(s1_E), .b(des_M), .eq(comparator_17_eq));  // open: gt, lt
  Comparator #(.width(2), .mode("unsigned")) comparator_18 (
    .a(tNew_M), .b(2'b00), .eq(comparator_18_eq));  // open: gt, lt
  Comparator #(.width(5), .mode("unsigned")) comparator_19 (
    .a(s2_E), .b({5{1'b0}}), .eq(comparator_19_eq));  // open: gt, lt
  Comparator #(.width(5), .mode("unsigned")) comparator_20 (
    .a(s2_E), .b(des_W), .eq(comparator_20_eq));  // open: gt, lt
  Comparator #(.width(2), .mode("unsigned")) comparator_21 (
    .a(tNew_W), .b(2'b00), .eq(comparator_21_eq));  // open: gt, lt
  Comparator #(.width(5), .mode("unsigned")) comparator_22 (
    .a(s2_E), .b({5{1'b0}}), .eq(comparator_22_eq));  // open: gt, lt
  Comparator #(.width(5), .mode("unsigned")) comparator_23 (
    .a(s2_E), .b(des_M), .eq(comparator_23_eq));  // open: gt, lt
  Comparator #(.width(2), .mode("unsigned")) comparator_24 (
    .a(tNew_M), .b(2'b00), .eq(comparator_24_eq));  // open: gt, lt
  not not_5 (not_5_out, comparator_13_eq);
  not not_6 (not_6_out, comparator_16_eq);
  not not_7 (not_7_out, comparator_19_eq);
  not not_8 (not_8_out, comparator_22_eq);
  and and_5 (and_5_out, not_5_out, comparator_14_eq, comparator_15_eq);
  and and_6 (and_6_out, not_6_out, comparator_17_eq, comparator_18_eq);
  and and_7 (and_7_out, not_7_out, comparator_20_eq, comparator_21_eq);
  and and_8 (and_8_out, not_8_out, comparator_23_eq, comparator_24_eq);
  Multiplexer #(.width(2)) multiplexer_5 (
    .in0(2'b00), .in1(2'b10), .out(multiplexer_5_out), .sel(and_5_out));  // open: en
  Multiplexer #(.width(2)) multiplexer_6 (
    .in0(2'b00), .in1(2'b10), .out(multiplexer_6_out), .sel(and_7_out));  // open: en
  Multiplexer #(.width(2)) multiplexer_7 (
    .in0(multiplexer_6_out), .in1(2'b01), .out(fRtEsel), .sel(and_8_out));  // open: en
  Multiplexer #(.width(2)) multiplexer_8 (
    .in0(multiplexer_5_out), .in1(2'b01), .out(fRsEsel), .sel(and_6_out));  // open: en
  Comparator #(.width(5), .mode("unsigned")) comparator_25 (
    .a(s2_M), .b({5{1'b0}}), .eq(comparator_25_eq));  // open: gt, lt
  not not_9 (not_9_out, comparator_25_eq);
  Comparator #(.width(5), .mode("unsigned")) comparator_26 (
    .a(s2_M), .b(des_W), .eq(comparator_26_eq));  // open: gt, lt
  Comparator #(.width(2), .mode("unsigned")) comparator_27 (
    .a(tNew_W), .b(2'b00), .eq(comparator_27_eq));  // open: gt, lt
  and and_9 (and_9_out, not_9_out, comparator_26_eq, comparator_27_eq);
  Multiplexer multiplexer_9 (.in0(1'b0), .in1(1'b1), .out(fRtMsel), .sel(and_9_out));  // open: en
endmodule
