// Logisim project cpu_pipeline.circ as structural Verilog: 16 circuits, main circuit main
module main (
  input  RESET,
  output [31:0] _pc_w,
  output [31:0] _pc_m,
  output out_4,
  output [4:0] out_5,
  output [31:0] out_6,
  output out_7,
  output [31:0] out_8,
  output [31:0] out_9
);

  wire alu_1_zero, and_1_out, and_2_out, CLK, e_m_reg_1_zero_o, EqualD, ExtOpD, not_1_out, not_2_out, PCSelD;
  wire [1:0] ALUSrcBSel, counter_2_q, RegAddrSel, RegDataSel;
  wire [2:0] counter_1_q, Data_typeM, NPCSelD;
  wire [3:0] ALUControlE;
  wire [4:0] d_e_reg_1_rd_o, d_e_reg_1_rs_o, d_e_reg_1_rt_o, e_m_reg_1_rd_o, e_m_reg_1_rs_o, e_m_reg_1_rt_o,
       RdD, RdW_t, RsD, RtD, RtW, ShamtD, ShamtE;
  wire [15:0] splt_1_addr_imm_15_0;
  wire [25:0] Imm26;
  wire [31:0] adder_2_out, alu_1_aluresult, ALUResW, d_e_reg_1_ext32_o, d_e_reg_1_inst_o, d_e_reg_1_pc4_o,
       d_e_reg_1_pc_o, d_e_reg_1_rd1_o, d_e_reg_1_rd2_o, e_m_reg_1_ext32_o, e_m_reg_1_inst_o,
       e_m_reg_1_pc4_o, e_m_reg_1_rd1_o, e_m_reg_1_rd2_o, Ext32D, f_d_reg_1_inst_o, f_d_reg_1_pc4_o,
       im_1_data, m_w_reg_1_inst_o, mr_1_out, multiplexer_1_out, multiplexer_4_out, mw_1_out_addr, NPCD,
       Old_Data, PC4D, PC4F, PC4W, pc_1_do, PCM, PCW, RD1D, RD2D, RDW;

  Clock clock_1 (.out(CLK));
  Multiplexer #(.width(32), .enable("false")) multiplexer_1 (
    .in0(PC4F), .in1(NPCD), .out(multiplexer_1_out), .sel(PCSelD));
  PC pc_1 (.clk(CLK), .reset(RESET), .DI(multiplexer_1_out), .DO(pc_1_do));
  // Probe on pc_1_do
  Counter #(.width(3), .max('h4), .ongoal("stay")) counter_1 (
    .D(3'b100), .Q(counter_1_q), .clk(CLK), .clr(RESET));  // open: load, count, carry
  Adder #(.width(32)) adder_1 (.a(pc_1_do), .b(32'h4), .out(PC4F));  // open: cin, cout
  not not_1 (not_1_out, counter_1_q[0]);
  not not_2 (not_2_out, counter_1_q[1]);
  IM im_1 (.Address(pc_1_do), .Data(im_1_data));
  and and_1 (and_1_out, not_1_out, not_2_out, counter_1_q[2]);
  Counter #(.width(2), .max('h3), .ongoal("stay")) counter_2 (
    .D(2'b11), .Q(counter_2_q), .clk(CLK), .clr(RESET));  // open: load, count, carry
  and and_2 (and_2_out, counter_2_q[0], counter_2_q[1]);
  F_D_Reg f_d_reg_1 (
    .CLK(CLK), .Inst_I(im_1_data), .F_D_Stall(1'b0), .PC4_I(pc_1_do), .Reset(RESET),
    .Inst_O(f_d_reg_1_inst_o), .PC4_O(f_d_reg_1_pc4_o));
  Multiplexer #(.width(32), .enable("false")) multiplexer_2 (.in0(32'h3000), .in1(PCW), .out(_pc_w), .sel(and_1_out));
  Multiplexer #(.width(32), .enable("false")) multiplexer_3 (.in0(32'h3000), .in1(PCM), .out(_pc_m), .sel(and_2_out));
  SPLT splt_1 (
    .Instruction(f_d_reg_1_inst_o), .Addr_Imm_15_0(splt_1_addr_imm_15_0), .Rs_25_21(RsD), .Rt_20_16(RtD),
    .Imm_25_0(Imm26), .Rd_15_11(RdD), .Shamt_6_10(ShamtD));  // open: Op_31_26, Func_5_0
  NPC npc_1 (.PC(f_d_reg_1_pc4_o), .Imm26(Imm26), .NPC(NPCD), .NPCSel(NPCSelD), .PC4(PC4D), .RA(RD1D));
  CU cu_1 (
    .Equal(EqualD), .Inst(f_d_reg_1_inst_o), .NPCSel(NPCSelD), .EXTOp(ExtOpD), .PCSel(PCSelD), .RD1(RD1D));  // open: ALUControl, DMWr, ALUSrcBSel, RFWr, WDSel, A3Sel, Data_Type
  GRF grf_1 (.A1(RsD), .A2(RtD), .A3(out_5), .WD(out_6), .RD1(RD1D), .RD2(RD2D), .we(out_4), .rst(RESET));
  Comparator #(.width(32)) comparator_1 (.a(RD1D), .b(RD2D), .eq(EqualD));  // open: gt, lt
  EXT ext_1 (.Imm16(splt_1_addr_imm_15_0), .Signed(ExtOpD), .Ext32(Ext32D));
  D_E_Reg d_e_reg_1 (
    .Inst_O(d_e_reg_1_inst_o), .CLK(CLK), .Inst_I(f_d_reg_1_inst_o), .F_D_Stall(1'b0),
    .PC4_O(d_e_reg_1_pc4_o), .PC4_I(PC4D), .Clear(RESET), .RD1_I(RD1D), .RD2_I(RD2D), .Ext32_I(Ext32D),
    .Rs_I(RsD), .Rt_I(RtD), .Rd_I(RdD), .RD1_O(d_e_reg_1_rd1_o), .RD2_O(d_e_reg_1_rd2_o),
    .Rs_O(d_e_reg_1_rs_o), .Rt_O(d_e_reg_1_rt_o), .Rd_O(d_e_reg_1_rd_o), .Ext32_O(d_e_reg_1_ext32_o),
    .Shamt_I(ShamtD), .Shamt_O(ShamtE), .PC_I(f_d_reg_1_pc4_o), .PC_O(d_e_reg_1_pc_o));
  Multiplexer #(.select(2), .width(32), .enable("false")) multiplexer_4 (
    .in0(d_e_reg_1_rd2_o), .in1(d_e_reg_1_ext32_o), .out(multiplexer_4_out), .sel(ALUSrcBSel));  // open: in2, in3
  ALU alu_1 (
    .SrcA(d_e_reg_1_rd1_o), .SrcB(multiplexer_4_out), .ALUControl(ALUControlE), .ALUResult(alu_1_aluresult),
    .Zero(alu_1_zero), .Shamt(ShamtE));
  CU cu_2 (
    .Inst(d_e_reg_1_inst_o), .ALUControl(ALUControlE), .ALUSrcBSel(ALUSrcBSel));  // open: Equal, NPCSel, EXTOp, DMWr, RFWr, WDSel, A3Sel, Data_Type, PCSel, RD1
  E_M_Reg e_m_reg_1 (
    .CLK(CLK), .Inst_I(d_e_reg_1_inst_o), .F_D_Stall(1'b0), .PC4_I(d_e_reg_1_pc4_o), .Clear(RESET),
    .RD1_I(d_e_reg_1_rd1_o), .RD2_I(d_e_reg_1_rd2_o), .Ext32_I(d_e_reg_1_ext32_o), .Rs_I(d_e_reg_1_rs_o),
    .Rt_I(d_e_reg_1_rt_o), .Rd_I(d_e_reg_1_rd_o), .Inst_O(e_m_reg_1_inst_o), .PC4_O(e_m_reg_1_pc4_o),
    .RD1_O(e_m_reg_1_rd1_o), .RD2_O(e_m_reg_1_rd2_o), .Ext32_O(e_m_reg_1_ext32_o), .Rs_O(e_m_reg_1_rs_o),
    .Rt_O(e_m_reg_1_rt_o), .Rd_O(e_m_reg_1_rd_o), .ALURes_I(alu_1_aluresult), .ALURes_O(out_8),
    .Zero_I(alu_1_zero), .Zero_O(e_m_reg_1_zero_o), .PC_I(d_e_reg_1_pc_o), .PC_O(PCM));
  MW mw_1 (
    .Data(e_m_reg_1_rd2_o), .Addr(out_8), .Old_Data(Old_Data), .Data_Type(Data_typeM), .Out(out_9),
    .Out_Addr(mw_1_out_addr));
  CU cu_3 (
    .Inst(e_m_reg_1_inst_o), .DMWr(out_7), .Data_Type(Data_typeM));  // open: Equal, NPCSel, EXTOp, ALUControl, ALUSrcBSel, RFWr, WDSel, A3Sel, PCSel, RD1
  DM dm_1 (.WD(out_9), .Address(mw_1_out_addr), .RD(Old_Data), .Wr(out_7), .clk(CLK), .reset(RESET));
  MR mr_1 (.Data(Old_Data), .Addr(out_8), .Data_Type(Data_typeM), .Out(mr_1_out));
  M_W_Reg m_w_reg_1 (
    .CLK(CLK), .Inst_I(e_m_reg_1_inst_o), .F_D_Stall(1'b0), .PC4_I(e_m_reg_1_pc4_o), .Clear(RESET),
    .RD1_I(e_m_reg_1_rd1_o), .RD2_I(e_m_reg_1_rd2_o), .Ext32_I(e_m_reg_1_ext32_o), .Rs_I(e_m_reg_1_rs_o),
    .Rt_I(e_m_reg_1_rt_o), .Rd_I(e_m_reg_1_rd_o), .ALURes_I(out_8), .Zero_I(e_m_reg_1_zero_o),
    .Inst_O(m_w_reg_1_inst_o), .PC4_O(PC4W), .Rt_O(RtW), .Rd_O(RdW_t), .ALURes_O(ALUResW), .RD_I_2(mr_1_out),
    .RD_O_2(RDW), .PC_I(PCM), .PC_O(PCW));  // open: RD1_O, RD2_O, Ext32_O, Rs_O, Zero_O
  CU cu_4 (
    .Inst(m_w_reg_1_inst_o), .RFWr(out_4), .WDSel(RegDataSel), .A3Sel(RegAddrSel));  // open: Equal, NPCSel, EXTOp, ALUControl, DMWr, ALUSrcBSel, Data_Type, PCSel, RD1
  Adder #(.width(32)) adder_2 (.a(PC4W), .b(32'h4), .out(adder_2_out));  // open: cin, cout
  Multiplexer #(.select(2), .width(5), .enable("false")) multiplexer_5 (
    .in0(RdW_t), .in1(RtW), .in2({5{1'b1}}), .out(out_5), .sel(RegAddrSel));  // open: in3
  Multiplexer #(.select(2), .width(32), .enable("false")) multiplexer_6 (
    .in0(ALUResW), .in1(RDW), .in2(adder_2_out), .out(out_6), .sel(RegDataSel));  // open: in3

  // Other names for the same wires on the sheet: DMAddrM[31:0] = out_8; DMDataM[31:0] = out_9; DMWrM = out_7;
  //   RegAddrW[4:0] = out_5; RegDataW[31:0] = out_6; RegWriteW = out_4

  // Notes on the sheet:
  //   记得修改为输出！！
endmodule

module GRF (
  input  we,
  input  [4:0] A1,
  input  [4:0] A2,
  input  [4:0] A3,
  input  [31:0] WD,
  input  rst,
  output [31:0] RD1,
  output [31:0] RD2
);

  wire clk;
  wire [31:0] i0, i1, i2, i3, i4, i5, i6, i7, i8, i9, i10, i11, i12, i13, i14, i15, i16, i17, i18, i19, i20,
       i21, i22, i23, i24, i25, i26, i27, i28, i29, i30, i31, o0, o1, o2, o3, o4, o5, o6, o7, o8, o9, o10,
       o11, o12, o13, o14, o15, o16, o17, o18, o19, o20, o21, o22, o23, o24, o25, o26, o27, o28, o29, o30,
       o31;

  Clock clock_1 (.out(clk));
  Register #(.width(32)) r0 (.D({32{1'b0}}), .en(we), .Q(o0), .clk(clk), .clr(rst));
  Register #(.width(32)) r1 (.D(i1), .en(we), .Q(o1), .clk(clk), .clr(rst));
  Register #(.width(32)) r2 (.D(i2), .en(we), .Q(o2), .clk(clk), .clr(rst));
  Register #(.width(32)) r3 (.D(i3), .en(we), .Q(o3), .clk(clk), .clr(rst));
  Register #(.width(32)) r4 (.D(i4), .en(we), .Q(o4), .clk(clk), .clr(rst));
  Register #(.width(32)) r5 (.D(i5), .en(we), .Q(o5), .clk(clk), .clr(rst));
  Register #(.width(32)) r6 (.D(i6), .en(we), .Q(o6), .clk(clk), .clr(rst));
  Register #(.width(32)) r7 (.D(i7), .en(we), .Q(o7), .clk(clk), .clr(rst));
  Register #(.width(32)) r8 (.D(i8), .en(we), .Q(o8), .clk(clk), .clr(rst));
  Register #(.width(32)) r9 (.D(i9), .en(we), .Q(o9), .clk(clk), .clr(rst));
  Register #(.width(32)) r10 (.D(i10), .en(we), .Q(o10), .clk(clk), .clr(rst));
  Register #(.width(32)) r11 (.D(i11), .en(we), .Q(o11), .clk(clk), .clr(rst));
  Register #(.width(32)) r12 (.D(i12), .en(we), .Q(o12), .clk(clk), .clr(rst));
  Register #(.width(32)) r13 (.D(i13), .en(we), .Q(o13), .clk(clk), .clr(rst));
  Register #(.width(32)) r14 (.D(i14), .en(we), .Q(o14), .clk(clk), .clr(rst));
  Register #(.width(32)) r15 (.D(i15), .en(we), .Q(o15), .clk(clk), .clr(rst));
  Register #(.width(32)) r16 (.D(i16), .en(we), .Q(o16), .clk(clk), .clr(rst));
  Register #(.width(32)) r17 (.D(i17), .en(we), .Q(o17), .clk(clk), .clr(rst));
  Register #(.width(32)) r18 (.D(i18), .en(we), .Q(o18), .clk(clk), .clr(rst));
  Register #(.width(32)) r19 (.D(i19), .en(we), .Q(o19), .clk(clk), .clr(rst));
  Register #(.width(32)) r20 (.D(i20), .en(we), .Q(o20), .clk(clk), .clr(rst));
  Register #(.width(32)) r21 (.D(i21), .en(we), .Q(o21), .clk(clk), .clr(rst));
  Register #(.width(32)) r22 (.D(i22), .en(we), .Q(o22), .clk(clk), .clr(rst));
  Register #(.width(32)) r23 (.D(i23), .en(we), .Q(o23), .clk(clk), .clr(rst));
  Register #(.width(32)) r24 (.D(i24), .en(we), .Q(o24), .clk(clk), .clr(rst));
  Register #(.width(32)) r25 (.D(i25), .en(we), .Q(o25), .clk(clk), .clr(rst));
  Register #(.width(32)) r26 (.D(i26), .en(we), .Q(o26), .clk(clk), .clr(rst));
  Register #(.width(32)) r27 (.D(i27), .en(we), .Q(o27), .clk(clk), .clr(rst));
  Register #(.width(32)) r28 (.D(i28), .en(we), .Q(o28), .clk(clk), .clr(rst));
  Register #(.width(32)) r29 (.D(i29), .en(we), .Q(o29), .clk(clk), .clr(rst));
  Register #(.width(32)) r30 (.D(i30), .en(we), .Q(o30), .clk(clk), .clr(rst));
  Register #(.width(32)) r31 (.D(i31), .en(we), .Q(o31), .clk(clk), .clr(rst));
  Multiplexer #(.select(5), .width(32), .enable("false")) multiplexer_1 (
    .in0(o0), .in1(o1), .in2(o2), .in3(o3), .in4(o4), .in5(o5), .in6(o6), .in7(o7), .in8(o8), .in9(o9),
    .in10(o10), .in11(o11), .in12(o12), .in13(o13), .in14(o14), .in15(o15), .in16(o16), .in17(o17),
    .in18(o18), .in19(o19), .in20(o20), .in21(o21), .in22(o22), .in23(o23), .in24(o24), .in25(o25),
    .in26(o26), .in27(o27), .in28(o28), .in29(o29), .in30(o30), .in31(o31), .out(RD1), .sel(A1));
  Multiplexer #(.select(5), .width(32), .enable("false")) multiplexer_2 (
    .in0(o0), .in1(o1), .in2(o2), .in3(o3), .in4(o4), .in5(o5), .in6(o6), .in7(o7), .in8(o8), .in9(o9),
    .in10(o10), .in11(o11), .in12(o12), .in13(o13), .in14(o14), .in15(o15), .in16(o16), .in17(o17),
    .in18(o18), .in19(o19), .in20(o20), .in21(o21), .in22(o22), .in23(o23), .in24(o24), .in25(o25),
    .in26(o26), .in27(o27), .in28(o28), .in29(o29), .in30(o30), .in31(o31), .out(RD2), .sel(A2));
  Demultiplexer #(.select(5), .width(32), .tristate("true"), .enable("false")) demultiplexer_1 (
    .out0(i0), .out1(i1), .out2(i2), .out3(i3), .out4(i4), .out5(i5), .out6(i6), .out7(i7), .out8(i8),
    .out9(i9), .out10(i10), .out11(i11), .out12(i12), .out13(i13), .out14(i14), .out15(i15), .out16(i16),
    .out17(i17), .out18(i18), .out19(i19), .out20(i20), .out21(i21), .out22(i22), .out23(i23), .out24(i24),
    .out25(i25), .out26(i26), .out27(i27), .out28(i28), .out29(i29), .out30(i30), .out31(i31), .in(WD),
    .sel(A3));
endmodule

module PC (
  input  clk,
  input  reset,
  input  [31:0] DI,
  output [31:0] DO
);

  wire [31:0] register_1_q, subtractor_1_out;

  Subtractor #(.width(32)) subtractor_1 (.a(DI), .b(32'h3000), .out(subtractor_1_out));  // open: bin, bout
  Register #(.width(32)) register_1 (.D(subtractor_1_out), .Q(register_1_q), .clk(clk), .clr(reset));  // open: en
  Adder #(.width(32)) adder_1 (.a(register_1_q), .b(32'h3000), .out(DO));  // open: cin, cout
endmodule

module NPC (
  input  [31:0] PC,
  input  [25:0] Imm26,
  input  [2:0] NPCSel,
  input  [31:0] RA,
  output [31:0] NPC,
  output [31:0] PC4
);

  wire [31:0] adder_2_out, bit_extender_1_out, shifter_1_out;

  assign bit_extender_1_out = {{16{Imm26[15]}}, Imm26[15:0]};  // Bit_Extender bit_extender_1
  Adder #(.width(32)) adder_1 (.a(PC), .b(32'h4), .out(PC4));  // open: cin, cout
  Shifter #(.width(32)) shifter_1 (.in(bit_extender_1_out), .\dist (5'b00010), .out(shifter_1_out));
  Adder #(.width(32)) adder_2 (.a(PC4), .b(shifter_1_out), .out(adder_2_out));  // open: cin, cout
  Multiplexer #(.select(3), .width(32), .enable("false")) multiplexer_1 (
    .in0(PC4), .in1(adder_2_out), .in2({PC[31:28], Imm26, 2'b00}), .in3(RA), .out(NPC), .sel(NPCSel));  // open: in4, in5, in6, in7
endmodule

module IM (
  input  [31:0] Address,
  output [31:0] Data
);

  ROM #(.addrWidth(10), .dataWidth(32)) rom_1 (.addr(Address[11:2]), .data(Data));  // open: sel

  // Notes on the sheet:
  //   contents of rom_1 (hex, n*v repeats v):
  //   34010008 4*0 34020009 4*0 3c030bc6 4*0 222021 4*0 412823 4*0 34060008 4*0 1026000e 4*0 34070001 4*0
  //   8000c3c 4*0 34080001 4*0 8000c3c 4*0 34090001 4*0 340a0001 4*0 c000c4b 4*0 340b0001 4*0 340c0001 4*0
  //   1000ffff
endmodule

module DM (
  input  Wr,
  input  clk,
  input  reset,
  input  [31:0] WD,
  input  [31:0] Address,
  output [31:0] RD
);

  RAM #(.addrWidth(10), .dataWidth(32), .bus("separate")) ram_1 (
    .addr(Address[11:2]), .din(WD), .data(RD), .str(Wr), .clk(clk), .clr(reset));  // open: sel, ld
endmodule

module ALU (
  input  [31:0] SrcA,
  input  [31:0] SrcB,
  input  [3:0] ALUControl,
  input  [4:0] Shamt,
  output [31:0] ALUResult,
  output Zero
);

  wire comparator_1_lt;
  wire [31:0] adder_1_out, and_1_out, bit_extender_1_out, or_1_out, shifter_1_out, shifter_2_out,
       shifter_3_out, subtractor_1_out;

  Adder #(.width(32)) adder_1 (.a(SrcA), .b(SrcB), .out(adder_1_out));  // open: cin, cout
  Subtractor #(.width(32)) subtractor_1 (.a(SrcA), .b(SrcB), .out(subtractor_1_out));  // open: bin, bout
  assign or_1_out = SrcA | SrcB;  // OR_Gate or_1, 32 bits wide
  assign and_1_out = SrcA & SrcB;  // AND_Gate and_1, 32 bits wide
  Shifter #(.width(32)) shifter_1 (.in(SrcB), .\dist (5'b10000), .out(shifter_1_out));
  Shifter #(.width(32)) shifter_2 (.in(SrcB), .\dist (Shamt), .out(shifter_2_out));
  Shifter #(.width(32)) shifter_3 (.in(SrcA), .\dist (SrcB[4:0]), .out(shifter_3_out));
  Comparator #(.width(32)) comparator_1 (.a(SrcA), .b(SrcB), .lt(comparator_1_lt));  // open: gt, eq
  assign bit_extender_1_out = {{31{1'b0}}, comparator_1_lt};  // Bit_Extender bit_extender_1
  Multiplexer #(.select(4), .width(32), .enable("false")) multiplexer_1 (
    .in0(adder_1_out), .in1(subtractor_1_out), .in2(or_1_out), .in3(and_1_out), .in4(shifter_1_out),
    .in5(shifter_2_out), .in6(shifter_3_out), .in7(bit_extender_1_out), .out(ALUResult), .sel(ALUControl));  // open: in8, in9, in10, in11, in12, in13, in14, in15
  Pull_Resistor pull_resistor_1 (.node(ALUResult));
  Comparator #(.width(32)) comparator_2 (.a({32{1'b0}}), .b(ALUResult), .eq(Zero));  // open: gt, lt
endmodule

module SPLT (
  input  [31:0] Instruction,
  output [5:0] Op_31_26,
  output [15:0] Addr_Imm_15_0,
  output [4:0] Rs_25_21,
  output [4:0] Rt_20_16,
  output [25:0] Imm_25_0,
  output [4:0] Rd_15_11,
  output [4:0] Shamt_6_10,
  output [5:0] Func_5_0
);


  assign Addr_Imm_15_0 = Instruction[15:0];
  assign Func_5_0 = Instruction[5:0];
  assign Imm_25_0 = Instruction[25:0];
  assign Op_31_26 = Instruction[31:26];
  assign Rd_15_11 = Instruction[15:11];
  assign Rs_25_21 = Instruction[25:21];
  assign Rt_20_16 = Instruction[20:16];
  assign Shamt_6_10 = Instruction[10:6];
endmodule

module CU (
  input  Equal,
  input  [31:0] Inst,
  input  [31:0] RD1,
  output [2:0] NPCSel,
  output EXTOp,
  output [3:0] ALUControl,
  output DMWr,
  output [1:0] ALUSrcBSel,
  output RFWr,
  output [1:0] WDSel,
  output [1:0] A3Sel,
  output [2:0] Data_Type,
  output PCSel
);

  wire _0, _0_t, _0_t_t, _Branch, _Load, _Save, add, addu, \and , and_8_out, and_9_out, and_10_out, beq,
       bgez, bne, comparator_2_eq, comparator_3_eq, comparator_4_eq, comparator_5_eq, comparator_6_eq,
       comparator_7_eq, comparator_8_eq, comparator_9_eq, comparator_10_eq, comparator_11_eq,
       comparator_13_eq, j, jal, jalr, jr, lb, lbu, lh, lhu, lui, lw, nop, not_1_out, not_2_out, \or ,
       or_1_out, or_2_out, or_3_out, or_4_out, or_5_out, or_6_out, or_7_out, or_10_out, or_11_out, or_12_out,
       or_13_out, or_14_out, or_15_out, or_16_out, or_17_out, or_18_out, or_19_out, or_20_out, ori, R, sb,
       sh, sll, sllv, slt, slti, sub, subu, sw;

  Pull_Resistor pull_resistor_1 (.node(Equal));
  Comparator #(.width(6)) comparator_1 (.a(Inst[31:26]), .b({6{1'b0}}), .eq(R));  // open: gt, lt
  Comparator #(.width(6)) comparator_2 (.a(Inst[5:0]), .b(6'b100001), .eq(comparator_2_eq));  // open: gt, lt
  Comparator #(.width(6)) comparator_3 (.a(Inst[5:0]), .b(6'b100011), .eq(comparator_3_eq));  // open: gt, lt
  Comparator #(.width(6)) comparator_4 (.a(Inst[5:0]), .b(6'b100100), .eq(comparator_4_eq));  // open: gt, lt
  Comparator #(.width(6)) comparator_5 (.a(Inst[5:0]), .b(6'b100101), .eq(comparator_5_eq));  // open: gt, lt
  Comparator #(.width(6)) comparator_6 (.a(Inst[5:0]), .b(6'b001000), .eq(comparator_6_eq));  // open: gt, lt
  Comparator #(.width(6)) comparator_7 (.a(Inst[5:0]), .b(6'b100000), .eq(comparator_7_eq));  // open: gt, lt
  Comparator #(.width(6)) comparator_8 (.a(Inst[5:0]), .b(6'b100010), .eq(comparator_8_eq));  // open: gt, lt
  and and_1 (addu, R, comparator_2_eq);
  and and_2 (subu, R, comparator_3_eq);
  and and_3 (\and , R, comparator_4_eq);
  and and_4 (\or , R, comparator_5_eq);
  and and_5 (jr, R, comparator_6_eq);
  and and_6 (add, R, comparator_7_eq);
  and and_7 (sub, R, comparator_8_eq);
  not not_1 (not_1_out, Equal);
  or or_1 (or_1_out, _0_t_t, _0_t);
  and and_8 (and_8_out, Equal, beq);
  and and_9 (and_9_out, bne, not_1_out);
  and and_10 (and_10_out, bgez, or_1_out);
  or or_2 (or_2_out, and_8_out, and_9_out, and_10_out);
  or or_3 (or_3_out, jal, j);
  or or_4 (or_4_out, jr, jalr);
  or or_5 (or_5_out, ori, slti, _Load, lui);
  buf or_6 (or_6_out, jal);  // OR_Gate
  Comparator #(.width(6)) comparator_9 (.a(Inst[5:0]), .b({6{1'b0}}), .eq(comparator_9_eq));  // open: gt, lt
  Comparator #(.width(6)) comparator_10 (.a(Inst[5:0]), .b(6'b000100), .eq(comparator_10_eq));  // open: gt, lt
  Comparator #(.width(6)) comparator_11 (.a(Inst[5:0]), .b(6'b101010), .eq(comparator_11_eq));  // open: gt, lt
  or or_7 (or_7_out, _Load, _Save);
  not not_2 (not_2_out, nop);
  and and_11 (sll, R, not_2_out, comparator_9_eq);
  and and_12 (sllv, R, comparator_10_eq);
  and and_13 (slt, R, comparator_11_eq);
  Priority_Encoder priority_encoder_1 (
    .in1(or_2_out), .in2(or_3_out), .in3(or_4_out), .out(NPCSel));  // open: in0, in4, in5, in6, in7, en_in, gs, en_out
  Pull_Resistor pull_resistor_2 (.node(NPCSel));
  Pull_Resistor pull_resistor_3 (.node(A3Sel));
  Priority_Encoder #(.select(2)) priority_encoder_2 (
    .in1(or_5_out), .in2(or_6_out), .out(A3Sel));  // open: in0, in3, gs, en_out, en_in
  or or_8 (EXTOp, or_7_out, slti);
  buf or_9 (DMWr, _Save);  // OR_Gate
  nor nor_1 (RFWr, _Branch, _Save, jr, j, nop);
  Comparator #(.width(32)) comparator_12 (.a(RD1), .b({32{1'b0}}), .gt(_0_t_t), .eq(_0_t), .lt(_0));
  Comparator #(.width(3), .mode("unsigned")) comparator_13 (
    .a(NPCSel), .b(3'b000), .eq(comparator_13_eq));  // open: gt, lt
  not not_3 (PCSel, comparator_13_eq);
  or or_10 (or_10_out, bne, subu, beq, sub);
  or or_11 (or_11_out, ori, \or );
  buf or_12 (or_12_out, \and );  // OR_Gate
  buf or_13 (or_13_out, lui);  // OR_Gate
  or or_14 (or_14_out, slt, slti);
  Comparator #(.width(6)) comparator_14 (.a(Inst[31:26]), .b(6'b000100), .eq(beq));  // open: gt, lt
  Comparator #(.width(6)) comparator_15 (.a(Inst[31:26]), .b(6'b001101), .eq(ori));  // open: gt, lt
  Comparator #(.width(6)) comparator_16 (.a(Inst[31:26]), .b(6'b000011), .eq(jal));  // open: gt, lt
  Comparator #(.width(6)) comparator_17 (.a(Inst[31:26]), .b(6'b101011), .eq(sw));  // open: gt, lt
  Comparator #(.width(6)) comparator_18 (.a(Inst[31:26]), .b(6'b100011), .eq(lw));  // open: gt, lt
  Comparator #(.width(6)) comparator_19 (.a(Inst[31:26]), .b(6'b001111), .eq(lui));  // open: gt, lt
  Comparator #(.width(6)) comparator_20 (.a(Inst[31:26]), .b(6'b100001), .eq(lh));  // open: gt, lt
  buf or_15 (or_15_out, _Load);  // OR_Gate
  or or_16 (or_16_out, jal, jalr);
  or or_17 (or_17_out, sh, lh);
  or or_18 (or_18_out, lhu, sb);
  buf or_19 (or_19_out, lb);  // OR_Gate
  Priority_Encoder #(.select(2)) priority_encoder_3 (
    .in1(or_15_out), .in2(or_16_out), .out(WDSel));  // open: in0, in3, gs, en_out, en_in
  Priority_Encoder #(.select(4)) priority_encoder_4 (
    .in1(or_10_out), .in2(or_11_out), .in3(or_12_out), .in4(or_13_out), .in5(sll), .in6(sllv),
    .in7(or_14_out), .out(ALUControl));  // open: in0, in8, in9, in10, in11, in12, in13, in14, in15, gs, en_out, en_in
  Priority_Encoder priority_encoder_5 (
    .in1(or_17_out), .in2(or_18_out), .in3(or_19_out), .in4(lbu), .out(Data_Type));  // open: in0, in5, in6, in7, en_in, gs, en_out
  or or_20 (or_20_out, ori, _Save, _Load, lui, slti);
  Pull_Resistor pull_resistor_4 (.node(WDSel));
  Pull_Resistor pull_resistor_5 (.node(ALUControl));
  Pull_Resistor pull_resistor_6 (.node(Data_Type));
  Priority_Encoder #(.select(2)) priority_encoder_6 (
    .in1(or_20_out), .out(ALUSrcBSel));  // open: in0, in2, in3, gs, en_out, en_in
  Comparator #(.width(6)) comparator_21 (.a(Inst[31:26]), .b(6'b100101), .eq(lhu));  // open: gt, lt
  Comparator #(.width(6)) comparator_22 (.a(Inst[31:26]), .b(6'b100000), .eq(lb));  // open: gt, lt
  Comparator #(.width(6)) comparator_23 (.a(Inst[31:26]), .b(6'b100100), .eq(lbu));  // open: gt, lt
  Comparator #(.width(6)) comparator_24 (.a(Inst[31:26]), .b(6'b101001), .eq(sh));  // open: gt, lt
  Comparator #(.width(6)) comparator_25 (.a(Inst[31:26]), .b(6'b101000), .eq(sb));  // open: gt, lt
  Comparator #(.width(6)) comparator_26 (.a(Inst[31:26]), .b(6'b000010), .eq(j));  // open: gt, lt
  Comparator #(.width(32)) comparator_27 (.a(Inst), .b({32{1'b0}}), .eq(nop));  // open: gt, lt
  Pull_Resistor pull_resistor_7 (.node(ALUSrcBSel));
  Comparator #(.width(6)) comparator_28 (.a(Inst[31:26]), .b(6'b001001), .eq(jalr));  // open: gt, lt
  Comparator #(.width(6)) comparator_29 (.a(Inst[31:26]), .b(6'b000101), .eq(bne));  // open: gt, lt
  Comparator #(.width(6)) comparator_30 (.a(Inst[31:26]), .b(6'b000001), .eq(bgez));  // open: gt, lt
  Comparator #(.width(6)) comparator_31 (.a(Inst[31:26]), .b(6'b001010), .eq(slti));  // open: gt, lt
  or or_21 (_Branch, bne, beq, bgez);
  or or_22 (_Save, sw, sh, sb);
  or or_23 (_Load, lhu, lb, lbu, lh, lw);

  // Other names for the same wires on the sheet: Func[5:0] = Inst[5:0]; Opcode[5:0] = Inst[31:26]

  // Notes on the sheet:
  //   无溢出检测
  //   不用写入寄存器的指令！！！
endmodule

module EXT (
  input  [15:0] Imm16,
  input  Signed,
  output [31:0] Ext32
);

  wire [31:0] bit_extender_1_out, bit_extender_2_out;

  assign bit_extender_1_out = {{16{1'b0}}, Imm16};  // Bit_Extender bit_extender_1
  assign bit_extender_2_out = {{16{Imm16[15]}}, Imm16};  // Bit_Extender bit_extender_2
  Multiplexer #(.width(32), .enable("false")) multiplexer_1 (
    .in0(bit_extender_1_out), .in1(bit_extender_2_out), .out(Ext32), .sel(Signed));
endmodule

module MR (
  input  [31:0] Data,
  input  [31:0] Addr,
  input  [2:0] Data_Type,
  output [31:0] Out
);

  wire [7:0] multiplexer_2_out;
  wire [15:0] multiplexer_1_out;
  wire [31:0] lb, lbu, lh, lhu;

  Multiplexer #(.width(16), .enable("false")) multiplexer_1 (
    .in0(Data[15:0]), .in1(Data[31:16]), .out(multiplexer_1_out), .sel(Addr[1]));
  Multiplexer #(.select(2), .width(8), .enable("false")) multiplexer_2 (
    .in0(Data[7:0]), .in1(Data[15:8]), .in2(Data[23:16]), .in3(Data[31:24]), .out(multiplexer_2_out),
    .sel(Addr[1:0]));
  assign lh = {{16{multiplexer_1_out[15]}}, multiplexer_1_out};  // Bit_Extender bit_extender_1
  assign lhu = {{16{1'b0}}, multiplexer_1_out};  // Bit_Extender bit_extender_2
  assign lb = {{24{multiplexer_2_out[7]}}, multiplexer_2_out};  // Bit_Extender bit_extender_3
  assign lbu = {{24{1'b0}}, multiplexer_2_out};  // Bit_Extender bit_extender_4
  Multiplexer #(.select(3), .width(32), .enable("false")) multiplexer_3 (
    .in0(Data), .in1(lh), .in2(lhu), .in3(lb), .in4(lbu), .out(Out), .sel(Data_Type));  // open: in5, in6, in7
  Pull_Resistor pull_resistor_1 (.node(Out));

  // Other names for the same wires on the sheet: lw[31:0] = Data
endmodule

module MW (
  input  [31:0] Data,
  input  [31:0] Addr,
  input  [31:0] Old_Data,
  input  [2:0] Data_Type,
  output [31:0] Out,
  output [31:0] Out_Addr
);

  wire [31:0] and_1_out, and_2_out, not_1_out, sb, sh, shifter_1_out, shifter_2_out;

  Multiplexer #(.width(32), .enable("false")) multiplexer_1 (
    .in0({Old_Data[31:16], Data[15:0]}), .in1({Data[15:0], Old_Data[15:0]}), .out(sh), .sel(Addr[1]));
  Shifter #(.width(32), .shift("rl")) shifter_1 (.in(32'hffffff00), .\dist ({Addr[1:0], 3'b000}), .out(shifter_1_out));
  Shifter #(.width(32)) shifter_2 (.in(Data), .\dist ({Addr[1:0], 3'b000}), .out(shifter_2_out));
  assign and_1_out = Old_Data & shifter_1_out;  // AND_Gate and_1, 32 bits wide
  assign not_1_out = ~shifter_1_out;  // NOT_Gate not_1, 32 bits wide
  assign and_2_out = not_1_out & shifter_2_out;  // AND_Gate and_2, 32 bits wide
  Multiplexer #(.select(3), .width(32), .enable("false")) multiplexer_2 (
    .in0(Data), .in1(sh), .in2(sb), .out(Out), .sel(Data_Type));  // open: in3, in4, in5, in6, in7
  assign sb = and_1_out | and_2_out;  // OR_Gate or_1, 32 bits wide
  Pull_Resistor pull_resistor_1 (.node(Out));

  assign Out_Addr = Addr;

  // Other names for the same wires on the sheet: sw[31:0] = Data
endmodule

module F_D_Reg (
  input  CLK,
  input  [31:0] Inst_I,
  input  F_D_Stall,
  input  [31:0] PC4_I,
  input  Reset,
  output [31:0] Inst_O,
  output [31:0] PC4_O
);

  wire not_1_out, not_2_out;

  Register #(.width(32)) register_1 (.D(Inst_I), .en(not_1_out), .Q(Inst_O), .clk(CLK), .clr(Reset));
  not not_1 (not_1_out, F_D_Stall);
  Register #(.width(32)) register_2 (.D(PC4_I), .en(not_2_out), .Q(PC4_O), .clk(CLK), .clr(Reset));
  not not_2 (not_2_out, F_D_Stall);
endmodule

module D_E_Reg (
  input  CLK,
  input  [31:0] Inst_I,
  input  F_D_Stall,
  input  [31:0] PC_I,
  input  Clear,
  input  [31:0] PC4_I,
  input  [31:0] RD1_I,
  input  [31:0] RD2_I,
  input  [31:0] Ext32_I,
  input  [4:0] Rs_I,
  input  [4:0] Rt_I,
  input  [4:0] Rd_I,
  input  [4:0] Shamt_I,
  output [31:0] Inst_O,
  output [31:0] PC_O,
  output [31:0] PC4_O,
  output [31:0] RD1_O,
  output [31:0] RD2_O,
  output [31:0] Ext32_O,
  output [4:0] Rs_O,
  output [4:0] Rt_O,
  output [4:0] Rd_O,
  output [4:0] Shamt_O
);

  wire not_1_out, not_2_out, not_3_out, not_4_out, not_5_out, not_6_out, not_7_out, not_8_out, not_9_out,
       not_10_out;

  not not_1 (not_1_out, F_D_Stall);
  Register #(.width(32)) register_1 (.D(Inst_I), .en(not_1_out), .Q(Inst_O), .clk(CLK), .clr(Clear));
  Register #(.width(32)) register_2 (.D(PC4_I), .en(not_2_out), .Q(PC4_O), .clk(CLK), .clr(Clear));
  not not_2 (not_2_out, F_D_Stall);
  Register #(.width(32)) register_3 (.D(RD1_I), .en(not_3_out), .Q(RD1_O), .clk(CLK), .clr(Clear));
  not not_3 (not_3_out, F_D_Stall);
  Register #(.width(32)) register_4 (.D(RD2_I), .en(not_4_out), .Q(RD2_O), .clk(CLK), .clr(Clear));
  not not_4 (not_4_out, F_D_Stall);
  Register #(.width(32)) register_5 (.D(Ext32_I), .en(not_5_out), .Q(Ext32_O), .clk(CLK), .clr(Clear));
  not not_5 (not_5_out, F_D_Stall);
  not not_6 (not_6_out, F_D_Stall);
  not not_7 (not_7_out, F_D_Stall);
  not not_8 (not_8_out, F_D_Stall);
  not not_9 (not_9_out, F_D_Stall);
  not not_10 (not_10_out, F_D_Stall);
  Register #(.width(5)) register_6 (.D(Rs_I), .en(not_6_out), .Q(Rs_O), .clk(CLK), .clr(Clear));
  Register #(.width(5)) register_7 (.D(Rt_I), .en(not_7_out), .Q(Rt_O), .clk(CLK), .clr(Clear));
  Register #(.width(5)) register_8 (.D(Rd_I), .en(not_8_out), .Q(Rd_O), .clk(CLK), .clr(Clear));
  Register #(.width(5)) register_9 (.D(Shamt_I), .en(not_9_out), .Q(Shamt_O), .clk(CLK), .clr(Clear));
  Register #(.width(32)) register_10 (.D(PC_I), .en(not_10_out), .Q(PC_O), .clk(CLK), .clr(Clear));
endmodule

module E_M_Reg (
  input  CLK,
  input  [31:0] Inst_I,
  input  F_D_Stall,
  input  [31:0] PC_I,
  input  Clear,
  input  [31:0] PC4_I,
  input  [31:0] RD1_I,
  input  [31:0] RD2_I,
  input  [31:0] Ext32_I,
  input  [4:0] Rs_I,
  input  [4:0] Rt_I,
  input  [4:0] Rd_I,
  input  [31:0] ALURes_I,
  input  Zero_I,
  output [31:0] Inst_O,
  output [31:0] PC_O,
  output [31:0] PC4_O,
  output [31:0] RD1_O,
  output [31:0] RD2_O,
  output [31:0] Ext32_O,
  output [4:0] Rs_O,
  output [4:0] Rt_O,
  output [4:0] Rd_O,
  output [31:0] ALURes_O,
  output Zero_O
);

  wire not_1_out, not_2_out, not_3_out, not_4_out, not_5_out, not_6_out, not_7_out, not_8_out, not_9_out,
       not_10_out, not_11_out;

  not not_1 (not_1_out, F_D_Stall);
  not not_2 (not_2_out, F_D_Stall);
  not not_3 (not_3_out, F_D_Stall);
  not not_4 (not_4_out, F_D_Stall);
  not not_5 (not_5_out, F_D_Stall);
  Register #(.width(32)) register_1 (.D(Inst_I), .en(not_1_out), .Q(Inst_O), .clk(CLK), .clr(Clear));
  Register #(.width(32)) register_2 (.D(PC4_I), .en(not_2_out), .Q(PC4_O), .clk(CLK), .clr(Clear));
  Register #(.width(32)) register_3 (.D(RD1_I), .en(not_3_out), .Q(RD1_O), .clk(CLK), .clr(Clear));
  Register #(.width(32)) register_4 (.D(RD2_I), .en(not_4_out), .Q(RD2_O), .clk(CLK), .clr(Clear));
  Register #(.width(32)) register_5 (.D(Ext32_I), .en(not_5_out), .Q(Ext32_O), .clk(CLK), .clr(Clear));
  Register #(.width(5)) register_6 (.D(Rs_I), .en(not_6_out), .Q(Rs_O), .clk(CLK), .clr(Clear));
  not not_6 (not_6_out, F_D_Stall);
  Register #(.width(5)) register_7 (.D(Rt_I), .en(not_7_out), .Q(Rt_O), .clk(CLK), .clr(Clear));
  not not_7 (not_7_out, F_D_Stall);
  Register #(.width(5)) register_8 (.D(Rd_I), .en(not_8_out), .Q(Rd_O), .clk(CLK), .clr(Clear));
  not not_8 (not_8_out, F_D_Stall);
  Register #(.width(32)) register_9 (.D(ALURes_I), .en(not_9_out), .Q(ALURes_O), .clk(CLK), .clr(Clear));
  not not_9 (not_9_out, F_D_Stall);
  Register #(.width(1)) register_10 (.D(Zero_I), .en(not_10_out), .Q(Zero_O), .clk(CLK), .clr(Clear));
  not not_10 (not_10_out, F_D_Stall);
  not not_11 (not_11_out, F_D_Stall);
  Register #(.width(32)) register_11 (.D(PC_I), .en(not_11_out), .Q(PC_O), .clk(CLK), .clr(Clear));
endmodule

module M_W_Reg (
  input  CLK,
  input  [31:0] Inst_I,
  input  F_D_Stall,
  input  [31:0] PC_I,
  input  Clear,
  input  [31:0] PC4_I,
  input  [31:0] RD1_I,
  input  [31:0] RD2_I,
  input  [31:0] Ext32_I,
  input  [4:0] Rs_I,
  input  [4:0] Rt_I,
  input  [4:0] Rd_I,
  input  [31:0] ALURes_I,
  input  Zero_I,
  input  [31:0] RD_I_2,
  output [31:0] Inst_O,
  output [31:0] PC_O,
  output [31:0] PC4_O,
  output [31:0] RD1_O,
  output [31:0] RD2_O,
  output [31:0] Ext32_O,
  output [4:0] Rs_O,
  output [4:0] Rt_O,
  output [4:0] Rd_O,
  output [31:0] ALURes_O,
  output Zero_O,
  output [31:0] RD_O_2
);

  wire not_1_out, not_2_out, not_3_out, not_4_out, not_5_out, not_6_out, not_7_out, not_8_out, not_9_out,
       not_10_out, not_11_out, not_12_out;

  not not_1 (not_1_out, F_D_Stall);
  not not_2 (not_2_out, F_D_Stall);
  not not_3 (not_3_out, F_D_Stall);
  not not_4 (not_4_out, F_D_Stall);
  not not_5 (not_5_out, F_D_Stall);
  Register #(.width(32)) register_1 (.D(Inst_I), .en(not_1_out), .Q(Inst_O), .clk(CLK), .clr(Clear));
  Register #(.width(32)) register_2 (.D(PC4_I), .en(not_2_out), .Q(PC4_O), .clk(CLK), .clr(Clear));
  Register #(.width(32)) register_3 (.D(RD1_I), .en(not_3_out), .Q(RD1_O), .clk(CLK), .clr(Clear));
  Register #(.width(32)) register_4 (.D(RD2_I), .en(not_4_out), .Q(RD2_O), .clk(CLK), .clr(Clear));
  Register #(.width(32)) register_5 (.D(Ext32_I), .en(not_5_out), .Q(Ext32_O), .clk(CLK), .clr(Clear));
  Register #(.width(5)) register_6 (.D(Rs_I), .en(not_6_out), .Q(Rs_O), .clk(CLK), .clr(Clear));
  not not_6 (not_6_out, F_D_Stall);
  Register #(.width(5)) register_7 (.D(Rt_I), .en(not_7_out), .Q(Rt_O), .clk(CLK), .clr(Clear));
  not not_7 (not_7_out, F_D_Stall);
  Register #(.width(5)) register_8 (.D(Rd_I), .en(not_8_out), .Q(Rd_O), .clk(CLK), .clr(Clear));
  not not_8 (not_8_out, F_D_Stall);
  Register #(.width(32)) register_9 (.D(ALURes_I), .en(not_9_out), .Q(ALURes_O), .clk(CLK), .clr(Clear));
  not not_9 (not_9_out, F_D_Stall);
  Register #(.width(1)) register_10 (.D(Zero_I), .en(not_10_out), .Q(Zero_O), .clk(CLK), .clr(Clear));
  not not_10 (not_10_out, F_D_Stall);
  not not_11 (not_11_out, F_D_Stall);
  not not_12 (not_12_out, F_D_Stall);
  Register #(.width(32)) register_11 (.D(RD_I_2), .en(not_11_out), .Q(RD_O_2), .clk(CLK), .clr(Clear));
  Register #(.width(32)) register_12 (.D(PC_I), .en(not_12_out), .Q(PC_O), .clk(CLK), .clr(Clear));

  // Other names for the same wires on the sheet: RD_I_t[31:0] = RD_I_2; RD_O_t[31:0] = RD_O_2
endmodule
