// Logisim project Logisim_swap.circ as structural Verilog: 1 circuit, main circuit main
module main (
  input  in_1,
  input  in_2,
  input  S,
  output out_4,
  output out_5
);

  wire and_1_out, and_2_out, and_3_out, and_4_out, xor_1_out, xor_2_out, xor_3_out;

  xor xor_1 (xor_1_out, in_1, in_2);
  xor xor_2 (xor_2_out, xor_1_out, in_2);
  xor xor_3 (xor_3_out, xor_1_out, xor_2_out);
  and and_1 (and_1_out, in_1, ~S);  // AND_Gate
  and and_2 (and_2_out, xor_3_out, S);
  and and_3 (and_3_out, in_2, ~S);  // AND_Gate
  and and_4 (and_4_out, xor_2_out, S);
  or or_1 (out_4, and_1_out, and_2_out);
  or or_2 (out_5, and_3_out, and_4_out);
endmodule
