// Logisim project mod5.circ as structural Verilog: 2 circuits, main circuit mod5
module mod5 (
  input  in_1,
  output out_2,
  output out_3,
  output out_4,
  output out_5,
  output out_6
);

  wire clock_1_out;
  wire [1:0] register_1_q, \状态转移_1_out_3 ;

  \状态转移  \u_状态转移_1  (.in_1(register_1_q), .in(in_1), .out_3(\状态转移_1_out_3 ));
  Register #(.width(2)) register_1 (.D(\状态转移_1_out_3 ), .Q(register_1_q), .clk(clock_1_out));  // open: en, clr
  Clock clock_1 (.out(clock_1_out));
  Decoder #(.select(2)) decoder_1 (
    .out0(out_3), .out1(out_4), .out2(out_5), .out3(out_6), .sel(\状态转移_1_out_3 ));  // open: en

  assign out_2 = 1'b0;
endmodule

module \状态转移  (
  input  [1:0] in_1,
  input  in,
  output [1:0] out_3
);

  wire and_1_out, and_2_out, and_3_out, and_4_out, and_5_out, and_6_out, not_1_out, not_2_out, not_3_out,
       not_4_out, not_5_out, not_6_out, not_7_out, not_8_out;

  not not_1 (not_1_out, in_1[1]);
  and and_1 (and_1_out, not_1_out, in_1[0]);
  and and_2 (and_2_out, in_1[1], not_2_out);
  not not_2 (not_2_out, in_1[0]);
  not not_3 (not_3_out, in_1[1]);
  and and_3 (and_3_out, not_3_out, not_4_out, in);
  not not_4 (not_4_out, in_1[0]);
  not not_5 (not_5_out, in_1[1]);
  and and_4 (and_4_out, not_5_out, in_1[0], not_6_out);
  not not_6 (not_6_out, in);
  and and_5 (and_5_out, in_1[1], not_7_out, not_8_out);
  not not_7 (not_7_out, in_1[0]);
  not not_8 (not_8_out, in);
  and and_6 (and_6_out, in_1[1], in_1[0], in);
  or or_1 (out_3[1], and_1_out, and_2_out);
  or or_2 (out_3[0], and_3_out, and_4_out, and_5_out, and_6_out);
endmodule
