// Logisim project swap.circ as structural Verilog: 4 circuits, main circuit 1bit_swap
module _1bit_swap (
  input  in_1,
  input  in_2,
  input  S,
  output out_4,
  output out_5
);

  wire and_1_out, and_2_out, and_3_out, and_4_out, xor_1_out, xor_2_out, xor_3_out;

  xor xor_1 (xor_1_out, in_1, in_2);
  xor xor_2 (xor_2_out, xor_1_out, in_2);
  xor xor_3 (xor_3_out, xor_1_out, xor_2_out);
  and and_1 (and_1_out, in_1, ~S);  // AND_Gate
  and and_2 (and_2_out, xor_3_out, S);
  and and_3 (and_3_out, in_2, ~S);  // AND_Gate
  and and_4 (and_4_out, xor_2_out, S);
  or or_1 (out_4, and_1_out, and_2_out);
  or or_2 (out_5, and_3_out, and_4_out);
endmodule

module _4bit_swap (
  input  [3:0] in_1,
  input  [3:0] in_2,
  input  S,
  output [3:0] out_1,
  output [3:0] out_2
);

  _1bit_swap u_1bit_swap_1 (.in_1(in_1[0]), .in_2(in_2[0]), .S(S), .out_4(out_1[0]), .out_5(out_2[0]));
  _1bit_swap u_1bit_swap_2 (.in_1(in_1[1]), .in_2(in_2[1]), .S(S), .out_4(out_1[1]), .out_5(out_2[1]));
  _1bit_swap u_1bit_swap_3 (.in_1(in_1[2]), .in_2(in_2[2]), .S(S), .out_4(out_1[2]), .out_5(out_2[2]));
  _1bit_swap u_1bit_swap_4 (.in_1(in_1[3]), .in_2(in_2[3]), .S(S), .out_4(out_1[3]), .out_5(out_2[3]));
endmodule

module _2_sort (
  input  [3:0] in_1,
  input  [3:0] in_2,
  output [3:0] out_1,
  output [3:0] out_2
);

  wire comparator_1_gt;

  Comparator #(.width(4), .mode("unsigned")) comparator_1 (.a(in_1), .b(in_2), .gt(comparator_1_gt));  // open: eq, lt
  _4bit_swap u_4bit_swap_1 (.in_1(in_1), .in_2(in_2), .S(comparator_1_gt), .out_1(out_1), .out_2(out_2));
endmodule

module _4bit_sort (
  input  [3:0] in_1,
  input  [3:0] in_2,
  input  [3:0] in_3,
  input  [3:0] in_4,
  output [3:0] out_1,
  output [3:0] out_2,
  output [3:0] out_3,
  output [3:0] out_4
);

  wire [3:0] n2_sort_1_out_1, n2_sort_1_out_2, n2_sort_2_out_1, n2_sort_2_out_2, n2_sort_3_out_1,
       n2_sort_3_out_2, n2_sort_4_out_2, n2_sort_5_out_2;

  _2_sort u_2_sort_1 (.in_1(in_1), .in_2(in_2), .out_1(n2_sort_1_out_1), .out_2(n2_sort_1_out_2));
  _2_sort u_2_sort_2 (.in_1(n2_sort_1_out_1), .in_2(in_3), .out_1(n2_sort_2_out_1), .out_2(n2_sort_2_out_2));
  _2_sort u_2_sort_3 (.in_1(n2_sort_1_out_2), .in_2(n2_sort_2_out_2), .out_1(n2_sort_3_out_1), .out_2(n2_sort_3_out_2));
  _2_sort u_2_sort_4 (.in_1(n2_sort_3_out_1), .in_2(n2_sort_5_out_2), .out_1(out_2), .out_2(n2_sort_4_out_2));
  _2_sort u_2_sort_5 (.in_1(n2_sort_2_out_1), .in_2(in_4), .out_1(out_1), .out_2(n2_sort_5_out_2));
  _2_sort u_2_sort_6 (.in_1(n2_sort_3_out_2), .in_2(n2_sort_4_out_2), .out_1(out_3), .out_2(out_4));
endmodule
