// Logisim project 斐波那契.circ as structural Verilog: 3 circuits, main circuit main
module main (
  input  [2:0] in_1,
  output [3:0] out_2
);

  wire \计数逻辑_1_out_2 ;
  wire [3:0] \计算逻辑_1_out_2 ;

  \计数逻辑  \u_计数逻辑_1  (.in_1(in_1), .out_2(\计数逻辑_1_out_2 ));
  \计算逻辑  \u_计算逻辑_1  (.in_1(\计数逻辑_1_out_2 ), .out_2(\计算逻辑_1_out_2 ));
  Multiplexer #(.width(4)) multiplexer_1 (
    .in0(4'b0000), .in1(\计算逻辑_1_out_2 ), .out(out_2), .sel(\计数逻辑_1_out_2 ));  // open: en

  // Other names for the same wires on the sheet: in[2:0] = in_1; res[3:0] = out_2
endmodule

module \计算逻辑  (
  input  in_1,
  output [3:0] out_2
);

  wire clk, counter_1_q, not_1_out;
  wire [3:0] adder_1_out, multiplexer_1_out, register_1_q;

  Counter #(.width(1), .max('h1), .ongoal("stay")) counter_1 (
    .Q(counter_1_q), .clk(clk));  // open: load, D, count, carry, clr
  not not_1 (not_1_out, in_1);
  Multiplexer #(.width(4), .enable("false")) multiplexer_1 (
    .in0(4'b0001), .in1(adder_1_out), .out(multiplexer_1_out), .sel(counter_1_q));
  Register #(.width(4)) register_1 (.D(multiplexer_1_out), .en(not_1_out), .Q(register_1_q), .clk(clk));  // open: clr
  Register #(.width(4)) register_2 (.D(register_1_q), .en(not_1_out), .Q(out_2), .clk(clk));  // open: clr
  Adder #(.width(4)) adder_1 (.a(register_1_q), .b(out_2), .out(adder_1_out));  // open: cin, cout
  Clock clock_1 (.out(clk));

  // Other names for the same wires on the sheet: if_end = in_1
endmodule

module \计数逻辑  (
  input  [2:0] in_1,
  output out_2
);

  wire clk;
  wire [7:0] bit_extender_1_out, counter_1_q;

  assign bit_extender_1_out = {{5{1'b0}}, in_1};  // Bit_Extender bit_extender_1
  Counter #(.ongoal("stay")) counter_1 (.Q(counter_1_q), .clk(clk));  // open: load, D, count, carry, clr
  Comparator #(.mode("unsigned")) comparator_1 (.a(bit_extender_1_out), .b(counter_1_q), .lt(out_2));  // open: gt, eq
  // Probe on bit_extender_1_out
  Clock clock_1 (.out(clk));
endmodule
