// Logisim project 矩阵快速幂斐波那契.circ as structural Verilog: 8 circuits, main circuit main
module main (
  input  [31:0] in_1,
  output [31:0] out_2
);

  wire \计数逻辑_1_out_2 , \计数逻辑_1_out_3 ;

  \计数逻辑  \u_计数逻辑_1  (.in_1(in_1), .out_2(\计数逻辑_1_out_2 ), .out_3(\计数逻辑_1_out_3 ));
  \计算逻辑  \u_计算逻辑_1  (.in_1(\计数逻辑_1_out_2 ), .in_2(\计数逻辑_1_out_3 ), .out_3(out_2));

  // Other names for the same wires on the sheet: in[31:0] = in_1
endmodule

module \矩阵寄存器  (
  input  [31:0] in_11,
  input  [31:0] in_12,
  input  [31:0] in_21,
  input  [31:0] in_22,
  input  clk,
  input  en,
  output [31:0] in_11_2,
  output [31:0] in_12_2,
  output [31:0] in_21_2,
  output [31:0] in_22_2
);

  Register #(.width(32)) register_1 (.D(in_11), .en(en), .Q(in_11_2), .clk(clk));  // open: clr
  Register #(.width(32)) register_2 (.D(in_21), .en(en), .Q(in_21_2), .clk(clk));  // open: clr
  Register #(.width(32)) register_3 (.D(in_12), .en(en), .Q(in_12_2), .clk(clk));  // open: clr
  Register #(.width(32)) register_4 (.D(in_22), .en(en), .Q(in_22_2), .clk(clk));  // open: clr

  // Other names for the same wires on the sheet: out_11[31:0] = in_11_2; out_12[31:0] = in_12_2;
  //   out_21[31:0] = in_21_2; out_22[31:0] = in_22_2
endmodule

module \矩阵乘法  (
  input  [31:0] in_1,
  input  [31:0] in_2,
  input  [31:0] in_3,
  input  [31:0] in_4,
  input  [31:0] in_5,
  input  [31:0] in_6,
  input  [31:0] in_7,
  input  [31:0] in_8,
  output [31:0] out_9,
  output [31:0] out_10,
  output [31:0] out_11,
  output [31:0] out_12
);

  wire [31:0] multiplier_1_out, multiplier_2_out, multiplier_3_out, multiplier_4_out, multiplier_5_out,
       multiplier_6_out, multiplier_7_out, multiplier_8_out;

  Multiplier #(.width(32)) multiplier_1 (.a(in_1), .b(in_5), .out(multiplier_1_out));  // open: cin, cout
  Multiplier #(.width(32)) multiplier_2 (.a(in_2), .b(in_7), .out(multiplier_2_out));  // open: cin, cout
  Multiplier #(.width(32)) multiplier_3 (.a(in_1), .b(in_6), .out(multiplier_3_out));  // open: cin, cout
  Multiplier #(.width(32)) multiplier_4 (.a(in_2), .b(in_8), .out(multiplier_4_out));  // open: cin, cout
  Multiplier #(.width(32)) multiplier_5 (.a(in_3), .b(in_5), .out(multiplier_5_out));  // open: cin, cout
  Multiplier #(.width(32)) multiplier_6 (.a(in_4), .b(in_7), .out(multiplier_6_out));  // open: cin, cout
  Multiplier #(.width(32)) multiplier_7 (.a(in_3), .b(in_6), .out(multiplier_7_out));  // open: cin, cout
  Multiplier #(.width(32)) multiplier_8 (.a(in_4), .b(in_8), .out(multiplier_8_out));  // open: cin, cout
  Adder #(.width(32)) adder_1 (.a(multiplier_1_out), .b(multiplier_2_out), .out(out_9));  // open: cin, cout
  Adder #(.width(32)) adder_2 (.a(multiplier_3_out), .b(multiplier_4_out), .out(out_10));  // open: cin, cout
  Adder #(.width(32)) adder_3 (.a(multiplier_5_out), .b(multiplier_6_out), .out(out_11));  // open: cin, cout
  Adder #(.width(32)) adder_4 (.a(multiplier_7_out), .b(multiplier_8_out), .out(out_12));  // open: cin, cout

  // Other names for the same wires on the sheet: a11[31:0] = in_1; a12[31:0] = in_2; a21[31:0] = in_3;
  //   a22[31:0] = in_4; b11[31:0] = in_5; b12[31:0] = in_6; b21[31:0] = in_7; b22[31:0] = in_8
endmodule

module \矩阵选择器  (
  input  in_1,
  input  [31:0] in_2,
  input  [31:0] in_3,
  input  [31:0] in_4,
  input  [31:0] in_5,
  input  [31:0] in_6,
  input  [31:0] in_7,
  input  [31:0] in_8,
  input  [31:0] in_9,
  output [31:0] out_10,
  output [31:0] out_11,
  output [31:0] out_12,
  output [31:0] out_13
);

  Multiplexer #(.width(32)) multiplexer_1 (.in0(in_2), .in1(in_6), .out(out_10), .sel(in_1));  // open: en
  Multiplexer #(.width(32)) multiplexer_2 (.in0(in_3), .in1(in_7), .out(out_11), .sel(in_1));  // open: en
  Multiplexer #(.width(32)) multiplexer_3 (.in0(in_4), .in1(in_8), .out(out_12), .sel(in_1));  // open: en
  Multiplexer #(.width(32)) multiplexer_4 (.in0(in_5), .in1(in_9), .out(out_13), .sel(in_1));  // open: en

  // Other names for the same wires on the sheet: a11[31:0] = in_2; a12[31:0] = in_3; a21[31:0] = in_4;
  //   a22[31:0] = in_5; b11[31:0] = in_6; b12[31:0] = in_7; b21[31:0] = in_8; b22[31:0] = in_9; sel = in_1
endmodule

module \矩阵初始化  (
  output [31:0] out_1,
  output [31:0] out_2,
  output [31:0] out_3,
  output [31:0] out_4
);


  assign out_1 = 32'h1;
  assign out_2 = 32'h1;
  assign out_3 = 32'h1;
  assign out_4 = {32{1'b0}};
endmodule

module \矩阵单位化  (
  output [31:0] out_1,
  output [31:0] out_2,
  output [31:0] out_3,
  output [31:0] out_4
);


  assign out_1 = 32'h1;
  assign out_2 = {32{1'b0}};
  assign out_3 = {32{1'b0}};
  assign out_4 = 32'h1;
endmodule

module \计算逻辑  (
  input  in_1,
  input  in_2,
  output [31:0] out_3
);

  wire clk, en, is_begin;
  wire [31:0] a11, a12, a21, a22, s11, s12, s21, s22, \矩阵乘法_1_out_9 , \矩阵乘法_1_out_10 , \矩阵乘法_1_out_11 ,
       \矩阵乘法_1_out_12 , \矩阵乘法_2_out_9 , \矩阵乘法_2_out_10 , \矩阵乘法_2_out_11 , \矩阵乘法_2_out_12 , \矩阵初始化_1_out_1 ,
       \矩阵初始化_1_out_2 , \矩阵初始化_1_out_3 , \矩阵初始化_1_out_4 , \矩阵单位化_1_out_1 , \矩阵单位化_1_out_2 , \矩阵单位化_1_out_3 ,
       \矩阵单位化_1_out_4 , \矩阵选择器_1_out_10 , \矩阵选择器_1_out_11 , \矩阵选择器_1_out_12 , \矩阵选择器_1_out_13 ,
       \矩阵选择器_2_out_10 , \矩阵选择器_2_out_11 , \矩阵选择器_2_out_12 , \矩阵选择器_2_out_13 , \矩阵选择器_3_out_10 ,
       \矩阵选择器_3_out_11 , \矩阵选择器_3_out_12 , \矩阵选择器_3_out_13 ;

  Clock clock_1 (.out(clk));
  Counter #(.width(1), .max('h1), .ongoal("stay")) counter_1 (
    .Q(is_begin), .clk(clk));  // open: load, D, count, carry, clr
  not not_1 (en, in_2);
  \矩阵乘法  \u_矩阵乘法_1  (
    .in_1(s11), .in_2(s12), .in_3(s21), .in_4(s22), .in_5(a11), .in_6(a12), .in_7(a21), .in_8(a22),
    .out_9(\矩阵乘法_1_out_9 ), .out_10(\矩阵乘法_1_out_10 ), .out_11(\矩阵乘法_1_out_11 ), .out_12(\矩阵乘法_1_out_12 ));
  \矩阵乘法  \u_矩阵乘法_2  (
    .in_1(a11), .in_2(a12), .in_3(a21), .in_4(a22), .in_5(a11), .in_6(a12), .in_7(a21), .in_8(a22),
    .out_9(\矩阵乘法_2_out_9 ), .out_10(\矩阵乘法_2_out_10 ), .out_11(\矩阵乘法_2_out_11 ), .out_12(\矩阵乘法_2_out_12 ));
  \矩阵选择器  \u_矩阵选择器_1  (
    .in_1(in_1), .in_2(s11), .in_3(s12), .in_4(s21), .in_5(s22), .in_6(\矩阵乘法_1_out_9 ),
    .in_7(\矩阵乘法_1_out_10 ), .in_8(\矩阵乘法_1_out_11 ), .in_9(\矩阵乘法_1_out_12 ), .out_10(\矩阵选择器_1_out_10 ),
    .out_11(\矩阵选择器_1_out_11 ), .out_12(\矩阵选择器_1_out_12 ), .out_13(\矩阵选择器_1_out_13 ));
  \矩阵初始化  \u_矩阵初始化_1  (
    .out_1(\矩阵初始化_1_out_1 ), .out_2(\矩阵初始化_1_out_2 ), .out_3(\矩阵初始化_1_out_3 ), .out_4(\矩阵初始化_1_out_4 ));
  \矩阵选择器  \u_矩阵选择器_2  (
    .in_1(is_begin), .in_2(\矩阵初始化_1_out_1 ), .in_3(\矩阵初始化_1_out_2 ), .in_4(\矩阵初始化_1_out_3 ),
    .in_5(\矩阵初始化_1_out_4 ), .in_6(\矩阵乘法_2_out_9 ), .in_7(\矩阵乘法_2_out_10 ), .in_8(\矩阵乘法_2_out_11 ),
    .in_9(\矩阵乘法_2_out_12 ), .out_10(\矩阵选择器_2_out_10 ), .out_11(\矩阵选择器_2_out_11 ), .out_12(\矩阵选择器_2_out_12 ),
    .out_13(\矩阵选择器_2_out_13 ));
  \矩阵寄存器  \u_矩阵寄存器_1  (
    .in_11(\矩阵选择器_2_out_10 ), .in_12(\矩阵选择器_2_out_11 ), .in_21(\矩阵选择器_2_out_12 ), .in_22(\矩阵选择器_2_out_13 ),
    .clk(clk), .en(en), .in_11_2(a11), .in_12_2(a12), .in_21_2(a21), .in_22_2(a22));
  \矩阵单位化  \u_矩阵单位化_1  (
    .out_1(\矩阵单位化_1_out_1 ), .out_2(\矩阵单位化_1_out_2 ), .out_3(\矩阵单位化_1_out_3 ), .out_4(\矩阵单位化_1_out_4 ));
  \矩阵选择器  \u_矩阵选择器_3  (
    .in_1(is_begin), .in_2(\矩阵单位化_1_out_1 ), .in_3(\矩阵单位化_1_out_2 ), .in_4(\矩阵单位化_1_out_3 ),
    .in_5(\矩阵单位化_1_out_4 ), .in_6(\矩阵选择器_1_out_10 ), .in_7(\矩阵选择器_1_out_11 ), .in_8(\矩阵选择器_1_out_12 ),
    .in_9(\矩阵选择器_1_out_13 ), .out_10(\矩阵选择器_3_out_10 ), .out_11(\矩阵选择器_3_out_11 ), .out_12(\矩阵选择器_3_out_12 ),
    .out_13(\矩阵选择器_3_out_13 ));
  \矩阵寄存器  \u_矩阵寄存器_2  (
    .in_11(\矩阵选择器_3_out_10 ), .in_12(\矩阵选择器_3_out_11 ), .in_21(\矩阵选择器_3_out_12 ), .in_22(\矩阵选择器_3_out_13 ),
    .clk(clk), .en(en), .in_11_2(s11), .in_12_2(s12), .in_21_2(s21), .in_22_2(s22));
  Multiplexer #(.width(32)) multiplexer_1 (.in0({32{1'b0}}), .in1(s12), .out(out_3), .sel(in_2));  // open: en

  // Other names for the same wires on the sheet: is_end = in_2; is_one = in_1
endmodule

module \计数逻辑  (
  input  [31:0] in_1,
  output out_2,
  output out_3
);

  wire clk, comparator_1_eq, is_begin;
  wire [31:0] multiplexer_1_out, p_in, shifter_1_out;

  Clock clock_1 (.out(clk));
  Counter #(.width(1), .max('h1), .ongoal("stay")) counter_1 (
    .Q(is_begin), .clk(clk));  // open: load, D, count, carry, clr
  Shifter #(.width(32), .shift("lr")) shifter_1 (.in(p_in), .\dist (5'b00001), .out(shifter_1_out));
  Register #(.width(32)) register_1 (.D(multiplexer_1_out), .Q(p_in), .clk(clk));  // open: en, clr
  Multiplexer #(.width(32)) multiplexer_1 (
    .in0(in_1), .in1(shifter_1_out), .out(multiplexer_1_out), .sel(is_begin));  // open: en
  Bit_Extender #(.in_width(32), .out_width(1)) bit_extender_1 (.in(p_in), .out(out_2));
  Comparator #(.width(32)) comparator_1 (.a(p_in), .b({32{1'b0}}), .eq(comparator_1_eq));  // open: gt, lt
  Multiplexer multiplexer_2 (.in0(1'b0), .in1(comparator_1_eq), .out(out_3), .sel(is_begin));  // open: en
  // Probe on p_in

  // Other names for the same wires on the sheet: in[31:0] = in_1
endmodule
